// Logisim project 32Bit_CPU.circ as structural Verilog
module main (
  output [31:0] out_1,
  output [31:0] out_2,
  output [31:0] out_3,
  output [31:0] out_4,
  output [31:0] out_5,
  output [31:0] out_6,
  output [31:0] out_7,
  output [31:0] out_8,
  output [31:0] out_9
);

  wire Clk_out, controlunit_1_branch, controlunit_1_float, controlunit_1_floatwrite, controlunit_1_intwrite,
       controlunit_1_isel, controlunit_1_jump, controlunit_1_load, controlunit_1_store,
       cpu_ram_interface_1_output_enable, cpu_ram_interface_1_ram_clk, cpu_ram_interface_1_write_enable,
       doubledabble3digit_1_ah, doubledabble3digit_1_ao, doubledabble3digit_1_at, doubledabble3digit_1_bh,
       doubledabble3digit_1_bo, doubledabble3digit_1_bt, doubledabble3digit_1_ch, doubledabble3digit_1_co,
       doubledabble3digit_1_ct, doubledabble3digit_1_dh, doubledabble3digit_1_do, doubledabble3digit_1_doth,
       doubledabble3digit_1_doto, doubledabble3digit_1_dott, doubledabble3digit_1_dt,
       doubledabble3digit_1_eh, doubledabble3digit_1_eo, doubledabble3digit_1_et, doubledabble3digit_1_fh,
       doubledabble3digit_1_fo, doubledabble3digit_1_ft, doubledabble3digit_1_gh, doubledabble3digit_1_go,
       doubledabble3digit_1_gt, doubledabble3digit_2_ah, doubledabble3digit_2_ao, doubledabble3digit_2_at,
       doubledabble3digit_2_bh, doubledabble3digit_2_bo, doubledabble3digit_2_bt, doubledabble3digit_2_ch,
       doubledabble3digit_2_co, doubledabble3digit_2_ct, doubledabble3digit_2_dh, doubledabble3digit_2_do,
       doubledabble3digit_2_doth, doubledabble3digit_2_doto, doubledabble3digit_2_dott,
       doubledabble3digit_2_dt, doubledabble3digit_2_eh, doubledabble3digit_2_eo, doubledabble3digit_2_et,
       doubledabble3digit_2_fh, doubledabble3digit_2_fo, doubledabble3digit_2_ft, doubledabble3digit_2_gh,
       doubledabble3digit_2_go, doubledabble3digit_2_gt, doubledabble3digit_3_ah, doubledabble3digit_3_ao,
       doubledabble3digit_3_at, doubledabble3digit_3_bh, doubledabble3digit_3_bo, doubledabble3digit_3_bt,
       doubledabble3digit_3_ch, doubledabble3digit_3_co, doubledabble3digit_3_ct, doubledabble3digit_3_dh,
       doubledabble3digit_3_do, doubledabble3digit_3_doth, doubledabble3digit_3_doto,
       doubledabble3digit_3_dott, doubledabble3digit_3_dt, doubledabble3digit_3_eh, doubledabble3digit_3_eo,
       doubledabble3digit_3_et, doubledabble3digit_3_fh, doubledabble3digit_3_fo, doubledabble3digit_3_ft,
       doubledabble3digit_3_gh, doubledabble3digit_3_go, doubledabble3digit_3_gt, doubledabble3digit_4_ah,
       doubledabble3digit_4_ao, doubledabble3digit_4_at, doubledabble3digit_4_bh, doubledabble3digit_4_bo,
       doubledabble3digit_4_bt, doubledabble3digit_4_ch, doubledabble3digit_4_co, doubledabble3digit_4_ct,
       doubledabble3digit_4_dh, doubledabble3digit_4_do, doubledabble3digit_4_doth,
       doubledabble3digit_4_doto, doubledabble3digit_4_dott, doubledabble3digit_4_dt,
       doubledabble3digit_4_eh, doubledabble3digit_4_eo, doubledabble3digit_4_et, doubledabble3digit_4_fh,
       doubledabble3digit_4_fo, doubledabble3digit_4_ft, doubledabble3digit_4_gh, doubledabble3digit_4_go,
       doubledabble3digit_4_gt, doubledabble3digit_5_ah, doubledabble3digit_5_ao, doubledabble3digit_5_at,
       doubledabble3digit_5_bh, doubledabble3digit_5_bo, doubledabble3digit_5_bt, doubledabble3digit_5_ch,
       doubledabble3digit_5_co, doubledabble3digit_5_ct, doubledabble3digit_5_dh, doubledabble3digit_5_do,
       doubledabble3digit_5_doth, doubledabble3digit_5_doto, doubledabble3digit_5_dott,
       doubledabble3digit_5_dt, doubledabble3digit_5_eh, doubledabble3digit_5_eo, doubledabble3digit_5_et,
       doubledabble3digit_5_fh, doubledabble3digit_5_fo, doubledabble3digit_5_ft, doubledabble3digit_5_gh,
       doubledabble3digit_5_go, doubledabble3digit_5_gt, doubledabble3digit_6_ah, doubledabble3digit_6_ao,
       doubledabble3digit_6_at, doubledabble3digit_6_bh, doubledabble3digit_6_bo, doubledabble3digit_6_bt,
       doubledabble3digit_6_ch, doubledabble3digit_6_co, doubledabble3digit_6_ct, doubledabble3digit_6_dh,
       doubledabble3digit_6_do, doubledabble3digit_6_doth, doubledabble3digit_6_doto,
       doubledabble3digit_6_dott, doubledabble3digit_6_dt, doubledabble3digit_6_eh, doubledabble3digit_6_eo,
       doubledabble3digit_6_et, doubledabble3digit_6_fh, doubledabble3digit_6_fo, doubledabble3digit_6_ft,
       doubledabble3digit_6_gh, doubledabble3digit_6_go, doubledabble3digit_6_gt, doubledabble3digit_7_ah,
       doubledabble3digit_7_ao, doubledabble3digit_7_at, doubledabble3digit_7_bh, doubledabble3digit_7_bo,
       doubledabble3digit_7_bt, doubledabble3digit_7_ch, doubledabble3digit_7_co, doubledabble3digit_7_ct,
       doubledabble3digit_7_dh, doubledabble3digit_7_do, doubledabble3digit_7_doth,
       doubledabble3digit_7_doto, doubledabble3digit_7_dott, doubledabble3digit_7_dt,
       doubledabble3digit_7_eh, doubledabble3digit_7_eo, doubledabble3digit_7_et, doubledabble3digit_7_fh,
       doubledabble3digit_7_fo, doubledabble3digit_7_ft, doubledabble3digit_7_gh, doubledabble3digit_7_go,
       doubledabble3digit_7_gt, doubledabble3digit_8_ah, doubledabble3digit_8_ao, doubledabble3digit_8_at,
       doubledabble3digit_8_bh, doubledabble3digit_8_bo, doubledabble3digit_8_bt, doubledabble3digit_8_ch,
       doubledabble3digit_8_co, doubledabble3digit_8_ct, doubledabble3digit_8_dh, doubledabble3digit_8_do,
       doubledabble3digit_8_doth, doubledabble3digit_8_doto, doubledabble3digit_8_dott,
       doubledabble3digit_8_dt, doubledabble3digit_8_eh, doubledabble3digit_8_eo, doubledabble3digit_8_et,
       doubledabble3digit_8_fh, doubledabble3digit_8_fo, doubledabble3digit_8_ft, doubledabble3digit_8_gh,
       doubledabble3digit_8_go, doubledabble3digit_8_gt, doubledabble3digit_9_ah, doubledabble3digit_9_ao,
       doubledabble3digit_9_at, doubledabble3digit_9_bh, doubledabble3digit_9_bo, doubledabble3digit_9_bt,
       doubledabble3digit_9_ch, doubledabble3digit_9_co, doubledabble3digit_9_ct, doubledabble3digit_9_dh,
       doubledabble3digit_9_do, doubledabble3digit_9_doth, doubledabble3digit_9_doto,
       doubledabble3digit_9_dott, doubledabble3digit_9_dt, doubledabble3digit_9_eh, doubledabble3digit_9_eo,
       doubledabble3digit_9_et, doubledabble3digit_9_fh, doubledabble3digit_9_fo, doubledabble3digit_9_ft,
       doubledabble3digit_9_gh, doubledabble3digit_9_go, doubledabble3digit_9_gt, doubledabble3digit_10_ah,
       doubledabble3digit_10_ao, doubledabble3digit_10_at, doubledabble3digit_10_bh,
       doubledabble3digit_10_bo, doubledabble3digit_10_bt, doubledabble3digit_10_ch,
       doubledabble3digit_10_co, doubledabble3digit_10_ct, doubledabble3digit_10_dh,
       doubledabble3digit_10_do, doubledabble3digit_10_doth, doubledabble3digit_10_doto,
       doubledabble3digit_10_dott, doubledabble3digit_10_dt, doubledabble3digit_10_eh,
       doubledabble3digit_10_eo, doubledabble3digit_10_et, doubledabble3digit_10_fh,
       doubledabble3digit_10_fo, doubledabble3digit_10_ft, doubledabble3digit_10_gh,
       doubledabble3digit_10_go, doubledabble3digit_10_gt, integerunit_1_cmpdataout, regfilesdatainsel_1_mff,
       regfilesdatainsel_1_mtf;
  wire [4:0] controlunit_1_rd, controlunit_1_rs, controlunit_1_rt, controlunit_1_sa;
  wire [5:0] controlunit_1_fct;
  wire [9:0] cpu_ram_interface_1_ram_adress, programcounter_1_instructionadress;
  wire [15:0] controlunit_1_branchto, controlunit_1_i;
  wire [25:0] controlunit_1_jumpto;
  wire [31:0] cpu_ram_interface_1_ram_input, cpu_ram_interface_1_regfile_input, fpregfile_1_xbus,
       fpregfile_1_ybus, multiplexer_1_out, multiplexer_2_out, ram_1_dout, ram_10adress_output_1_adress0,
       ram_10adress_output_1_adress1, ram_10adress_output_1_adress2, ram_10adress_output_1_adress3,
       ram_10adress_output_1_adress4, ram_10adress_output_1_adress5, ram_10adress_output_1_adress6,
       ram_10adress_output_1_adress7, ram_10adress_output_1_adress8, ram_10adress_output_1_adress9,
       regfile32bit_1_xbus, regfile32bit_1_ybus, rom_1_data;

  Clock Clk (.out(Clk_out));
  ROM #(.addrWidth(10), .dataWidth(32)) rom_1 (.addr(programcounter_1_instructionadress), .data(rom_1_data));
  ProgramCounter programcounter_1 (
    .jump(controlunit_1_jump), .branch(controlunit_1_branch), .CmpDataOut(integerunit_1_cmpdataout),
    .branchto(controlunit_1_branchto), .jumpto(controlunit_1_jumpto), .Clk(Clk_out),
    .instructionadress(programcounter_1_instructionadress));
  ControlUnit controlunit_1 (
    .Instruction(rom_1_data), .rs(controlunit_1_rs), .FloatWrite(controlunit_1_floatwrite),
    .branch(controlunit_1_branch), .store(controlunit_1_store), .load(controlunit_1_load),
    .ISel(controlunit_1_isel), .jump(controlunit_1_jump), .Float(controlunit_1_float),
    .IntWrite(controlunit_1_intwrite), .rt(controlunit_1_rt), .rd(controlunit_1_rd), .sa(controlunit_1_sa),
    .branchto(controlunit_1_branchto), .i(controlunit_1_i), .jumpto(controlunit_1_jumpto),
    .fct(controlunit_1_fct));
  FPRegFile fpregfile_1 (
    .WSel(controlunit_1_rd), .WR(controlunit_1_floatwrite), .Data(multiplexer_1_out), .Clk(Clk_out),
    .YSel(controlunit_1_rt), .XSel(controlunit_1_rs), .XBus(fpregfile_1_xbus), .YBus(fpregfile_1_ybus),
    .out_8(out_7), .out_9(out_6), .out_10(out_5), .out_11(out_4));
  Multiplexer #(.width(32)) multiplexer_1 (
    .in0(cpu_ram_interface_1_regfile_input), .in1(regfile32bit_1_xbus), .out(multiplexer_1_out),
    .sel(regfilesdatainsel_1_mtf));
  RegFilesDataInSel regfilesdatainsel_1 (
    .in_1(controlunit_1_fct), .MTF(regfilesdatainsel_1_mtf), .MFF(regfilesdatainsel_1_mff));
  RegFile32Bit regfile32bit_1 (
    .WSel(controlunit_1_rd), .WR(controlunit_1_intwrite), .Data(multiplexer_2_out), .Clk(Clk_out),
    .YSel(controlunit_1_rt), .XSel(controlunit_1_rs), .XBus(regfile32bit_1_xbus), .YBus(regfile32bit_1_ybus),
    .out_8(out_3), .out_9(out_2), .out_10(out_1));
  Multiplexer #(.width(32)) multiplexer_2 (
    .in0(cpu_ram_interface_1_regfile_input), .in1(fpregfile_1_xbus), .out(multiplexer_2_out),
    .sel(regfilesdatainsel_1_mff));
  CPU_RAM_Interface cpu_ram_interface_1 (
    .OpCode(controlunit_1_fct), .IU_Output(out_9), .FPU_Output(out_8), .RAM_Output(ram_1_dout),
    .int_X_Bus(regfile32bit_1_xbus), .Load(controlunit_1_load), .Store(controlunit_1_store),
    .float(controlunit_1_float), .Clk(Clk_out), .int_Y_Bus(regfile32bit_1_ybus),
    .float_Y_Bus(fpregfile_1_ybus), .RegFile_Input(cpu_ram_interface_1_regfile_input),
    .RAM_Adress(cpu_ram_interface_1_ram_adress), .Output_Enable(cpu_ram_interface_1_output_enable),
    .Write_Enable(cpu_ram_interface_1_write_enable), .RAM_Input(cpu_ram_interface_1_ram_input),
    .RAM_Clk(cpu_ram_interface_1_ram_clk));
  RAM #(.addrWidth(10), .asyncread("true"), .dataWidth(32)) ram_1 (
    .addr(cpu_ram_interface_1_ram_adress), .we(cpu_ram_interface_1_write_enable),
    .oe(cpu_ram_interface_1_output_enable), .clk(cpu_ram_interface_1_ram_clk),
    .din(cpu_ram_interface_1_ram_input), .dout(ram_1_dout));
  FloatingPointUnit floatingpointunit_1 ();
  IntegerUnit integerunit_1 (
    .Clk(Clk_out), .ISel(controlunit_1_isel), .I(controlunit_1_i), .SA(controlunit_1_sa),
    .A(regfile32bit_1_xbus), .B(regfile32bit_1_ybus), .Sel(controlunit_1_fct), .IntegerResult(out_9),
    .CmpDataOut(integerunit_1_cmpdataout));
  RAM_10Adress_Output ram_10adress_output_1 (
    .Write_enable(cpu_ram_interface_1_write_enable), .Clk(Clk_out), .Adress(cpu_ram_interface_1_ram_adress),
    .RAM_Input(cpu_ram_interface_1_ram_input), .Adress0(ram_10adress_output_1_adress0),
    .Adress1(ram_10adress_output_1_adress1), .Adress2(ram_10adress_output_1_adress2),
    .Adress3(ram_10adress_output_1_adress3), .Adress4(ram_10adress_output_1_adress4),
    .Adress5(ram_10adress_output_1_adress5), .Adress6(ram_10adress_output_1_adress6),
    .Adress7(ram_10adress_output_1_adress7), .Adress8(ram_10adress_output_1_adress8),
    .Adress9(ram_10adress_output_1_adress9));
  DoubleDabble3digit doubledabble3digit_1 (
    .DataIn(ram_10adress_output_1_adress0), .aH(doubledabble3digit_1_ah), .bH(doubledabble3digit_1_bh),
    .cH(doubledabble3digit_1_ch), .dH(doubledabble3digit_1_dh), .eH(doubledabble3digit_1_eh),
    .fH(doubledabble3digit_1_fh), .gH(doubledabble3digit_1_gh), .dotH(doubledabble3digit_1_doth),
    .aT(doubledabble3digit_1_at), .bT(doubledabble3digit_1_bt), .cT(doubledabble3digit_1_ct),
    .dT(doubledabble3digit_1_dt), .eT(doubledabble3digit_1_et), .fT(doubledabble3digit_1_ft),
    .gT(doubledabble3digit_1_gt), .dotT(doubledabble3digit_1_dott), .aO(doubledabble3digit_1_ao),
    .bO(doubledabble3digit_1_bo), .cO(doubledabble3digit_1_co), .dO(doubledabble3digit_1_do),
    .eO(doubledabble3digit_1_eo), .fO(doubledabble3digit_1_fo), .gO(doubledabble3digit_1_go),
    .dotO(doubledabble3digit_1_doto));
  DoubleDabble3digit doubledabble3digit_2 (
    .DataIn(ram_10adress_output_1_adress1), .aH(doubledabble3digit_2_ah), .bH(doubledabble3digit_2_bh),
    .cH(doubledabble3digit_2_ch), .dH(doubledabble3digit_2_dh), .eH(doubledabble3digit_2_eh),
    .fH(doubledabble3digit_2_fh), .gH(doubledabble3digit_2_gh), .dotH(doubledabble3digit_2_doth),
    .aT(doubledabble3digit_2_at), .bT(doubledabble3digit_2_bt), .cT(doubledabble3digit_2_ct),
    .dT(doubledabble3digit_2_dt), .eT(doubledabble3digit_2_et), .fT(doubledabble3digit_2_ft),
    .gT(doubledabble3digit_2_gt), .dotT(doubledabble3digit_2_dott), .aO(doubledabble3digit_2_ao),
    .bO(doubledabble3digit_2_bo), .cO(doubledabble3digit_2_co), .dO(doubledabble3digit_2_do),
    .eO(doubledabble3digit_2_eo), .fO(doubledabble3digit_2_fo), .gO(doubledabble3digit_2_go),
    .dotO(doubledabble3digit_2_doto));
  DoubleDabble3digit doubledabble3digit_3 (
    .DataIn(ram_10adress_output_1_adress2), .aH(doubledabble3digit_3_ah), .bH(doubledabble3digit_3_bh),
    .cH(doubledabble3digit_3_ch), .dH(doubledabble3digit_3_dh), .eH(doubledabble3digit_3_eh),
    .fH(doubledabble3digit_3_fh), .gH(doubledabble3digit_3_gh), .dotH(doubledabble3digit_3_doth),
    .aT(doubledabble3digit_3_at), .bT(doubledabble3digit_3_bt), .cT(doubledabble3digit_3_ct),
    .dT(doubledabble3digit_3_dt), .eT(doubledabble3digit_3_et), .fT(doubledabble3digit_3_ft),
    .gT(doubledabble3digit_3_gt), .dotT(doubledabble3digit_3_dott), .aO(doubledabble3digit_3_ao),
    .bO(doubledabble3digit_3_bo), .cO(doubledabble3digit_3_co), .dO(doubledabble3digit_3_do),
    .eO(doubledabble3digit_3_eo), .fO(doubledabble3digit_3_fo), .gO(doubledabble3digit_3_go),
    .dotO(doubledabble3digit_3_doto));
  DoubleDabble3digit doubledabble3digit_4 (
    .DataIn(ram_10adress_output_1_adress3), .aH(doubledabble3digit_4_ah), .bH(doubledabble3digit_4_bh),
    .cH(doubledabble3digit_4_ch), .dH(doubledabble3digit_4_dh), .eH(doubledabble3digit_4_eh),
    .fH(doubledabble3digit_4_fh), .gH(doubledabble3digit_4_gh), .dotH(doubledabble3digit_4_doth),
    .aT(doubledabble3digit_4_at), .bT(doubledabble3digit_4_bt), .cT(doubledabble3digit_4_ct),
    .dT(doubledabble3digit_4_dt), .eT(doubledabble3digit_4_et), .fT(doubledabble3digit_4_ft),
    .gT(doubledabble3digit_4_gt), .dotT(doubledabble3digit_4_dott), .aO(doubledabble3digit_4_ao),
    .bO(doubledabble3digit_4_bo), .cO(doubledabble3digit_4_co), .dO(doubledabble3digit_4_do),
    .eO(doubledabble3digit_4_eo), .fO(doubledabble3digit_4_fo), .gO(doubledabble3digit_4_go),
    .dotO(doubledabble3digit_4_doto));
  DoubleDabble3digit doubledabble3digit_5 (
    .DataIn(ram_10adress_output_1_adress4), .aH(doubledabble3digit_5_ah), .bH(doubledabble3digit_5_bh),
    .cH(doubledabble3digit_5_ch), .dH(doubledabble3digit_5_dh), .eH(doubledabble3digit_5_eh),
    .fH(doubledabble3digit_5_fh), .gH(doubledabble3digit_5_gh), .dotH(doubledabble3digit_5_doth),
    .aT(doubledabble3digit_5_at), .bT(doubledabble3digit_5_bt), .cT(doubledabble3digit_5_ct),
    .dT(doubledabble3digit_5_dt), .eT(doubledabble3digit_5_et), .fT(doubledabble3digit_5_ft),
    .gT(doubledabble3digit_5_gt), .dotT(doubledabble3digit_5_dott), .aO(doubledabble3digit_5_ao),
    .bO(doubledabble3digit_5_bo), .cO(doubledabble3digit_5_co), .dO(doubledabble3digit_5_do),
    .eO(doubledabble3digit_5_eo), .fO(doubledabble3digit_5_fo), .gO(doubledabble3digit_5_go),
    .dotO(doubledabble3digit_5_doto));
  DoubleDabble3digit doubledabble3digit_6 (
    .DataIn(ram_10adress_output_1_adress5), .aH(doubledabble3digit_6_ah), .bH(doubledabble3digit_6_bh),
    .cH(doubledabble3digit_6_ch), .dH(doubledabble3digit_6_dh), .eH(doubledabble3digit_6_eh),
    .fH(doubledabble3digit_6_fh), .gH(doubledabble3digit_6_gh), .dotH(doubledabble3digit_6_doth),
    .aT(doubledabble3digit_6_at), .bT(doubledabble3digit_6_bt), .cT(doubledabble3digit_6_ct),
    .dT(doubledabble3digit_6_dt), .eT(doubledabble3digit_6_et), .fT(doubledabble3digit_6_ft),
    .gT(doubledabble3digit_6_gt), .dotT(doubledabble3digit_6_dott), .aO(doubledabble3digit_6_ao),
    .bO(doubledabble3digit_6_bo), .cO(doubledabble3digit_6_co), .dO(doubledabble3digit_6_do),
    .eO(doubledabble3digit_6_eo), .fO(doubledabble3digit_6_fo), .gO(doubledabble3digit_6_go),
    .dotO(doubledabble3digit_6_doto));
  DoubleDabble3digit doubledabble3digit_7 (
    .DataIn(ram_10adress_output_1_adress6), .aH(doubledabble3digit_7_ah), .bH(doubledabble3digit_7_bh),
    .cH(doubledabble3digit_7_ch), .dH(doubledabble3digit_7_dh), .eH(doubledabble3digit_7_eh),
    .fH(doubledabble3digit_7_fh), .gH(doubledabble3digit_7_gh), .dotH(doubledabble3digit_7_doth),
    .aT(doubledabble3digit_7_at), .bT(doubledabble3digit_7_bt), .cT(doubledabble3digit_7_ct),
    .dT(doubledabble3digit_7_dt), .eT(doubledabble3digit_7_et), .fT(doubledabble3digit_7_ft),
    .gT(doubledabble3digit_7_gt), .dotT(doubledabble3digit_7_dott), .aO(doubledabble3digit_7_ao),
    .bO(doubledabble3digit_7_bo), .cO(doubledabble3digit_7_co), .dO(doubledabble3digit_7_do),
    .eO(doubledabble3digit_7_eo), .fO(doubledabble3digit_7_fo), .gO(doubledabble3digit_7_go),
    .dotO(doubledabble3digit_7_doto));
  DoubleDabble3digit doubledabble3digit_8 (
    .DataIn(ram_10adress_output_1_adress7), .aH(doubledabble3digit_8_ah), .bH(doubledabble3digit_8_bh),
    .cH(doubledabble3digit_8_ch), .dH(doubledabble3digit_8_dh), .eH(doubledabble3digit_8_eh),
    .fH(doubledabble3digit_8_fh), .gH(doubledabble3digit_8_gh), .dotH(doubledabble3digit_8_doth),
    .aT(doubledabble3digit_8_at), .bT(doubledabble3digit_8_bt), .cT(doubledabble3digit_8_ct),
    .dT(doubledabble3digit_8_dt), .eT(doubledabble3digit_8_et), .fT(doubledabble3digit_8_ft),
    .gT(doubledabble3digit_8_gt), .dotT(doubledabble3digit_8_dott), .aO(doubledabble3digit_8_ao),
    .bO(doubledabble3digit_8_bo), .cO(doubledabble3digit_8_co), .dO(doubledabble3digit_8_do),
    .eO(doubledabble3digit_8_eo), .fO(doubledabble3digit_8_fo), .gO(doubledabble3digit_8_go),
    .dotO(doubledabble3digit_8_doto));
  DoubleDabble3digit doubledabble3digit_9 (
    .DataIn(ram_10adress_output_1_adress8), .aH(doubledabble3digit_9_ah), .bH(doubledabble3digit_9_bh),
    .cH(doubledabble3digit_9_ch), .dH(doubledabble3digit_9_dh), .eH(doubledabble3digit_9_eh),
    .fH(doubledabble3digit_9_fh), .gH(doubledabble3digit_9_gh), .dotH(doubledabble3digit_9_doth),
    .aT(doubledabble3digit_9_at), .bT(doubledabble3digit_9_bt), .cT(doubledabble3digit_9_ct),
    .dT(doubledabble3digit_9_dt), .eT(doubledabble3digit_9_et), .fT(doubledabble3digit_9_ft),
    .gT(doubledabble3digit_9_gt), .dotT(doubledabble3digit_9_dott), .aO(doubledabble3digit_9_ao),
    .bO(doubledabble3digit_9_bo), .cO(doubledabble3digit_9_co), .dO(doubledabble3digit_9_do),
    .eO(doubledabble3digit_9_eo), .fO(doubledabble3digit_9_fo), .gO(doubledabble3digit_9_go),
    .dotO(doubledabble3digit_9_doto));
  DoubleDabble3digit doubledabble3digit_10 (
    .DataIn(ram_10adress_output_1_adress9), .aH(doubledabble3digit_10_ah), .bH(doubledabble3digit_10_bh),
    .cH(doubledabble3digit_10_ch), .dH(doubledabble3digit_10_dh), .eH(doubledabble3digit_10_eh),
    .fH(doubledabble3digit_10_fh), .gH(doubledabble3digit_10_gh), .dotH(doubledabble3digit_10_doth),
    .aT(doubledabble3digit_10_at), .bT(doubledabble3digit_10_bt), .cT(doubledabble3digit_10_ct),
    .dT(doubledabble3digit_10_dt), .eT(doubledabble3digit_10_et), .fT(doubledabble3digit_10_ft),
    .gT(doubledabble3digit_10_gt), .dotT(doubledabble3digit_10_dott), .aO(doubledabble3digit_10_ao),
    .bO(doubledabble3digit_10_bo), .cO(doubledabble3digit_10_co), .dO(doubledabble3digit_10_do),
    .eO(doubledabble3digit_10_eo), .fO(doubledabble3digit_10_fo), .gO(doubledabble3digit_10_go),
    .dotO(doubledabble3digit_10_doto));
  _7_Segment_Display u_7_segment_display_1 (
    .g(doubledabble3digit_1_gh), .f(doubledabble3digit_1_fh), .a(doubledabble3digit_1_ah),
    .b(doubledabble3digit_1_bh), .e(doubledabble3digit_1_eh), .d(doubledabble3digit_1_dh),
    .c(doubledabble3digit_1_ch), .dp(doubledabble3digit_1_doth));
  _7_Segment_Display u_7_segment_display_2 (
    .g(doubledabble3digit_1_gt), .f(doubledabble3digit_1_ft), .a(doubledabble3digit_1_at),
    .b(doubledabble3digit_1_bt), .e(doubledabble3digit_1_et), .d(doubledabble3digit_1_dt),
    .c(doubledabble3digit_1_ct), .dp(doubledabble3digit_1_dott));
  _7_Segment_Display u_7_segment_display_3 (
    .g(doubledabble3digit_2_gh), .f(doubledabble3digit_2_fh), .a(doubledabble3digit_2_ah),
    .b(doubledabble3digit_2_bh), .e(doubledabble3digit_2_eh), .d(doubledabble3digit_2_dh),
    .c(doubledabble3digit_2_ch), .dp(doubledabble3digit_2_doth));
  _7_Segment_Display u_7_segment_display_4 (
    .g(doubledabble3digit_2_gt), .f(doubledabble3digit_2_ft), .a(doubledabble3digit_2_at),
    .b(doubledabble3digit_2_bt), .e(doubledabble3digit_2_et), .d(doubledabble3digit_2_dt),
    .c(doubledabble3digit_2_ct), .dp(doubledabble3digit_2_dott));
  _7_Segment_Display u_7_segment_display_5 (
    .g(doubledabble3digit_3_gh), .f(doubledabble3digit_3_fh), .a(doubledabble3digit_3_ah),
    .b(doubledabble3digit_3_bh), .e(doubledabble3digit_3_eh), .d(doubledabble3digit_3_dh),
    .c(doubledabble3digit_3_ch), .dp(doubledabble3digit_3_doth));
  _7_Segment_Display u_7_segment_display_6 (
    .g(doubledabble3digit_3_gt), .f(doubledabble3digit_3_ft), .a(doubledabble3digit_3_at),
    .b(doubledabble3digit_3_bt), .e(doubledabble3digit_3_et), .d(doubledabble3digit_3_dt),
    .c(doubledabble3digit_3_ct), .dp(doubledabble3digit_3_dott));
  _7_Segment_Display u_7_segment_display_7 (
    .g(doubledabble3digit_4_gh), .f(doubledabble3digit_4_fh), .a(doubledabble3digit_4_ah),
    .b(doubledabble3digit_4_bh), .e(doubledabble3digit_4_eh), .d(doubledabble3digit_4_dh),
    .c(doubledabble3digit_4_ch), .dp(doubledabble3digit_4_doth));
  _7_Segment_Display u_7_segment_display_8 (
    .g(doubledabble3digit_4_gt), .f(doubledabble3digit_4_ft), .a(doubledabble3digit_4_at),
    .b(doubledabble3digit_4_bt), .e(doubledabble3digit_4_et), .d(doubledabble3digit_4_dt),
    .c(doubledabble3digit_4_ct), .dp(doubledabble3digit_4_dott));
  _7_Segment_Display u_7_segment_display_9 (
    .g(doubledabble3digit_5_gh), .f(doubledabble3digit_5_fh), .a(doubledabble3digit_5_ah),
    .b(doubledabble3digit_5_bh), .e(doubledabble3digit_5_eh), .d(doubledabble3digit_5_dh),
    .c(doubledabble3digit_5_ch), .dp(doubledabble3digit_5_doth));
  _7_Segment_Display u_7_segment_display_10 (
    .g(doubledabble3digit_5_gt), .f(doubledabble3digit_5_ft), .a(doubledabble3digit_5_at),
    .b(doubledabble3digit_5_bt), .e(doubledabble3digit_5_et), .d(doubledabble3digit_5_dt),
    .c(doubledabble3digit_5_ct), .dp(doubledabble3digit_5_dott));
  _7_Segment_Display u_7_segment_display_11 (
    .g(doubledabble3digit_6_gh), .f(doubledabble3digit_6_fh), .a(doubledabble3digit_6_ah),
    .b(doubledabble3digit_6_bh), .e(doubledabble3digit_6_eh), .d(doubledabble3digit_6_dh),
    .c(doubledabble3digit_6_ch), .dp(doubledabble3digit_6_doth));
  _7_Segment_Display u_7_segment_display_12 (
    .g(doubledabble3digit_6_gt), .f(doubledabble3digit_6_ft), .a(doubledabble3digit_6_at),
    .b(doubledabble3digit_6_bt), .e(doubledabble3digit_6_et), .d(doubledabble3digit_6_dt),
    .c(doubledabble3digit_6_ct), .dp(doubledabble3digit_6_dott));
  _7_Segment_Display u_7_segment_display_13 (
    .g(doubledabble3digit_7_gh), .f(doubledabble3digit_7_fh), .a(doubledabble3digit_7_ah),
    .b(doubledabble3digit_7_bh), .e(doubledabble3digit_7_eh), .d(doubledabble3digit_7_dh),
    .c(doubledabble3digit_7_ch), .dp(doubledabble3digit_7_doth));
  _7_Segment_Display u_7_segment_display_14 (
    .g(doubledabble3digit_7_gt), .f(doubledabble3digit_7_ft), .a(doubledabble3digit_7_at),
    .b(doubledabble3digit_7_bt), .e(doubledabble3digit_7_et), .d(doubledabble3digit_7_dt),
    .c(doubledabble3digit_7_ct), .dp(doubledabble3digit_7_dott));
  _7_Segment_Display u_7_segment_display_15 (
    .g(doubledabble3digit_8_gh), .f(doubledabble3digit_8_fh), .a(doubledabble3digit_8_ah),
    .b(doubledabble3digit_8_bh), .e(doubledabble3digit_8_eh), .d(doubledabble3digit_8_dh),
    .c(doubledabble3digit_8_ch), .dp(doubledabble3digit_8_doth));
  _7_Segment_Display u_7_segment_display_16 (
    .g(doubledabble3digit_8_gt), .f(doubledabble3digit_8_ft), .a(doubledabble3digit_8_at),
    .b(doubledabble3digit_8_bt), .e(doubledabble3digit_8_et), .d(doubledabble3digit_8_dt),
    .c(doubledabble3digit_8_ct), .dp(doubledabble3digit_8_dott));
  _7_Segment_Display u_7_segment_display_17 (
    .g(doubledabble3digit_9_gh), .f(doubledabble3digit_9_fh), .a(doubledabble3digit_9_ah),
    .b(doubledabble3digit_9_bh), .e(doubledabble3digit_9_eh), .d(doubledabble3digit_9_dh),
    .c(doubledabble3digit_9_ch), .dp(doubledabble3digit_9_doth));
  _7_Segment_Display u_7_segment_display_18 (
    .g(doubledabble3digit_9_gt), .f(doubledabble3digit_9_ft), .a(doubledabble3digit_9_at),
    .b(doubledabble3digit_9_bt), .e(doubledabble3digit_9_et), .d(doubledabble3digit_9_dt),
    .c(doubledabble3digit_9_ct), .dp(doubledabble3digit_9_dott));
  _7_Segment_Display u_7_segment_display_19 (
    .g(doubledabble3digit_10_gh), .f(doubledabble3digit_10_fh), .a(doubledabble3digit_10_ah),
    .b(doubledabble3digit_10_bh), .e(doubledabble3digit_10_eh), .d(doubledabble3digit_10_dh),
    .c(doubledabble3digit_10_ch), .dp(doubledabble3digit_10_doth));
  _7_Segment_Display u_7_segment_display_20 (
    .g(doubledabble3digit_10_gt), .f(doubledabble3digit_10_ft), .a(doubledabble3digit_10_at),
    .b(doubledabble3digit_10_bt), .e(doubledabble3digit_10_et), .d(doubledabble3digit_10_dt),
    .c(doubledabble3digit_10_ct), .dp(doubledabble3digit_10_dott));
  _7_Segment_Display u_7_segment_display_21 (
    .g(doubledabble3digit_1_go), .f(doubledabble3digit_1_fo), .a(doubledabble3digit_1_ao),
    .b(doubledabble3digit_1_bo), .e(doubledabble3digit_1_eo), .d(doubledabble3digit_1_do),
    .c(doubledabble3digit_1_co), .dp(doubledabble3digit_1_doto));
  _7_Segment_Display u_7_segment_display_22 (
    .g(doubledabble3digit_2_go), .f(doubledabble3digit_2_fo), .a(doubledabble3digit_2_ao),
    .b(doubledabble3digit_2_bo), .e(doubledabble3digit_2_eo), .d(doubledabble3digit_2_do),
    .c(doubledabble3digit_2_co), .dp(doubledabble3digit_2_doto));
  _7_Segment_Display u_7_segment_display_23 (
    .g(doubledabble3digit_3_go), .f(doubledabble3digit_3_fo), .a(doubledabble3digit_3_ao),
    .b(doubledabble3digit_3_bo), .e(doubledabble3digit_3_eo), .d(doubledabble3digit_3_do),
    .c(doubledabble3digit_3_co), .dp(doubledabble3digit_3_doto));
  _7_Segment_Display u_7_segment_display_24 (
    .g(doubledabble3digit_4_go), .f(doubledabble3digit_4_fo), .a(doubledabble3digit_4_ao),
    .b(doubledabble3digit_4_bo), .e(doubledabble3digit_4_eo), .d(doubledabble3digit_4_do),
    .c(doubledabble3digit_4_co), .dp(doubledabble3digit_4_doto));
  _7_Segment_Display u_7_segment_display_25 (
    .g(doubledabble3digit_5_go), .f(doubledabble3digit_5_fo), .a(doubledabble3digit_5_ao),
    .b(doubledabble3digit_5_bo), .e(doubledabble3digit_5_eo), .d(doubledabble3digit_5_do),
    .c(doubledabble3digit_5_co), .dp(doubledabble3digit_5_doto));
  _7_Segment_Display u_7_segment_display_26 (
    .g(doubledabble3digit_6_go), .f(doubledabble3digit_6_fo), .a(doubledabble3digit_6_ao),
    .b(doubledabble3digit_6_bo), .e(doubledabble3digit_6_eo), .d(doubledabble3digit_6_do),
    .c(doubledabble3digit_6_co), .dp(doubledabble3digit_6_doto));
  _7_Segment_Display u_7_segment_display_27 (
    .g(doubledabble3digit_7_go), .f(doubledabble3digit_7_fo), .a(doubledabble3digit_7_ao),
    .b(doubledabble3digit_7_bo), .e(doubledabble3digit_7_eo), .d(doubledabble3digit_7_do),
    .c(doubledabble3digit_7_co), .dp(doubledabble3digit_7_doto));
  _7_Segment_Display u_7_segment_display_28 (
    .g(doubledabble3digit_8_go), .f(doubledabble3digit_8_fo), .a(doubledabble3digit_8_ao),
    .b(doubledabble3digit_8_bo), .e(doubledabble3digit_8_eo), .d(doubledabble3digit_8_do),
    .c(doubledabble3digit_8_co), .dp(doubledabble3digit_8_doto));
  _7_Segment_Display u_7_segment_display_29 (
    .g(doubledabble3digit_9_go), .f(doubledabble3digit_9_fo), .a(doubledabble3digit_9_ao),
    .b(doubledabble3digit_9_bo), .e(doubledabble3digit_9_eo), .d(doubledabble3digit_9_do),
    .c(doubledabble3digit_9_co), .dp(doubledabble3digit_9_doto));
  _7_Segment_Display u_7_segment_display_30 (
    .g(doubledabble3digit_10_go), .f(doubledabble3digit_10_fo), .a(doubledabble3digit_10_ao),
    .b(doubledabble3digit_10_bo), .e(doubledabble3digit_10_eo), .d(doubledabble3digit_10_do),
    .c(doubledabble3digit_10_co), .dp(doubledabble3digit_10_doto));

  // Notes on the sheet:
  //   contents of rom_1 (hex, n*v repeats v):
  //   5c014020 c210000 20003a 2008000a f9000000 fd010000
  //   CPU
  //   MEMORY
  //   OUTPUT
endmodule

module Reg8Bit (
  input  [7:0] in_1,
  input  in_2,
  input  in_3,
  output [7:0] out_4
);

  Register #(.width(1)) register_1 (.D(in_1[0]), .en(in_3), .clk(in_2), .Q(out_4[0]));  // open: clr
  Register #(.width(1)) register_2 (.D(in_1[1]), .en(in_3), .clk(in_2), .Q(out_4[1]));  // open: clr
  Register #(.width(1)) register_3 (.D(in_1[2]), .en(in_3), .clk(in_2), .Q(out_4[2]));  // open: clr
  Register #(.width(1)) register_4 (.D(in_1[3]), .en(in_3), .clk(in_2), .Q(out_4[3]));  // open: clr
  Register #(.width(1)) register_5 (.D(in_1[4]), .en(in_3), .clk(in_2), .Q(out_4[4]));  // open: clr
  Register #(.width(1)) register_6 (.D(in_1[5]), .en(in_3), .clk(in_2), .Q(out_4[5]));  // open: clr
  Register #(.width(1)) register_7 (.D(in_1[6]), .en(in_3), .clk(in_2), .Q(out_4[6]));  // open: clr
  Register #(.width(1)) register_8 (.D(in_1[7]), .en(in_3), .clk(in_2), .Q(out_4[7]));  // open: clr
endmodule

module Reg32Bit (
  input  [31:0] Eingabe,
  input  Clk,
  input  Enable,
  output [31:0] Ausgabe
);

  Reg8Bit reg8bit_1 (.in_1(Eingabe[7:0]), .in_2(Clk), .in_3(Enable), .out_4(Ausgabe[7:0]));
  Reg8Bit reg8bit_2 (.in_1(Eingabe[15:8]), .in_2(Clk), .in_3(Enable), .out_4(Ausgabe[15:8]));
  Reg8Bit reg8bit_3 (.in_1(Eingabe[23:16]), .in_2(Clk), .in_3(Enable), .out_4(Ausgabe[23:16]));
  Reg8Bit reg8bit_4 (.in_1(Eingabe[31:24]), .in_2(Clk), .in_3(Enable), .out_4(Ausgabe[31:24]));
endmodule

module FPReg32Bit (
  input  [31:0] Eingabe,
  input  Clk,
  input  Enable,
  output [31:0] Ausgabe
);

  Reg8Bit reg8bit_1 (.in_1(Eingabe[7:0]), .in_2(Clk), .in_3(Enable), .out_4(Ausgabe[7:0]));
  Reg8Bit reg8bit_2 (.in_1(Eingabe[15:8]), .in_2(Clk), .in_3(Enable), .out_4(Ausgabe[15:8]));
  Reg8Bit reg8bit_3 (.in_1(Eingabe[23:16]), .in_2(Clk), .in_3(Enable), .out_4(Ausgabe[23:16]));
  Reg8Bit reg8bit_4 (.in_1(Eingabe[31:24]), .in_2(Clk), .in_3(Enable), .out_4(Ausgabe[31:24]));
endmodule

module RegZERO (
  input  Enable,
  output [31:0] Ausgabe,
  output [31:0] Display
);

  Reg32Bit reg32bit_1 (.Eingabe({32{1'b0}}), .Enable(Enable), .Ausgabe(Ausgabe));  // open: Clk

  assign Display = Ausgabe;
endmodule

module RegAT (
  input  [31:0] Eingabe,
  input  Clk,
  input  Enable,
  output [31:0] Ausgabe
);

  Reg32Bit reg32bit_1 (.Eingabe(Eingabe), .Clk(Clk), .Enable(Enable), .Ausgabe(Ausgabe));
endmodule

module RegV (
  input  EnableV0,
  input  [31:0] Eingabe,
  input  Clk,
  input  EnableV1,
  output [31:0] AusgabeV0,
  output [31:0] AusgabeV1
);

  Reg32Bit reg32bit_1 (.Eingabe(Eingabe), .Clk(Clk), .Enable(EnableV0), .Ausgabe(AusgabeV0));
  Reg32Bit reg32bit_2 (.Eingabe(Eingabe), .Clk(Clk), .Enable(EnableV1), .Ausgabe(AusgabeV1));
endmodule

module RegA (
  input  Clk,
  input  [31:0] Eingabe,
  input  EnableA0,
  input  EnableA1,
  input  EnableA2,
  input  EnableA3,
  output [31:0] AusgabeA0,
  output [31:0] AusgabeA1,
  output [31:0] AusgabeA2,
  output [31:0] AusgabeA3
);

  Reg32Bit reg32bit_1 (.Eingabe(Eingabe), .Clk(Clk), .Enable(EnableA0), .Ausgabe(AusgabeA0));
  Reg32Bit reg32bit_2 (.Eingabe(Eingabe), .Clk(Clk), .Enable(EnableA1), .Ausgabe(AusgabeA1));
  Reg32Bit reg32bit_3 (.Eingabe(Eingabe), .Clk(Clk), .Enable(EnableA2), .Ausgabe(AusgabeA2));
  Reg32Bit reg32bit_4 (.Eingabe(Eingabe), .Clk(Clk), .Enable(EnableA3), .Ausgabe(AusgabeA3));
endmodule

module RegT (
  input  Clk,
  input  [31:0] Eingabe,
  input  EnableT0,
  input  EnableT1,
  input  EnableT2,
  input  EnableT3,
  input  EnableT4,
  input  EnableT5,
  input  EnableT6,
  input  EnableT7,
  input  EnableT8,
  input  EnableT9,
  output [31:0] AusgabeT0,
  output [31:0] AusgabeT1,
  output [31:0] AusgabeT2,
  output [31:0] AusgabeT3,
  output [31:0] AusgabeT4,
  output [31:0] AusgabeT5,
  output [31:0] AusgabeT6,
  output [31:0] AusgabeT7,
  output [31:0] AusgabeT8,
  output [31:0] AusgabeT9
);

  Reg32Bit reg32bit_1 (.Eingabe(Eingabe), .Clk(Clk), .Enable(EnableT0), .Ausgabe(AusgabeT0));
  Reg32Bit reg32bit_2 (.Eingabe(Eingabe), .Clk(Clk), .Enable(EnableT1), .Ausgabe(AusgabeT1));
  Reg32Bit reg32bit_3 (.Eingabe(Eingabe), .Clk(Clk), .Enable(EnableT2), .Ausgabe(AusgabeT2));
  Reg32Bit reg32bit_4 (.Eingabe(Eingabe), .Clk(Clk), .Enable(EnableT3), .Ausgabe(AusgabeT3));
  Reg32Bit reg32bit_5 (.Eingabe(Eingabe), .Clk(Clk), .Enable(EnableT4), .Ausgabe(AusgabeT4));
  Reg32Bit reg32bit_6 (.Eingabe(Eingabe), .Clk(Clk), .Enable(EnableT5), .Ausgabe(AusgabeT5));
  Reg32Bit reg32bit_7 (.Eingabe(Eingabe), .Clk(Clk), .Enable(EnableT6), .Ausgabe(AusgabeT6));
  Reg32Bit reg32bit_8 (.Eingabe(Eingabe), .Clk(Clk), .Enable(EnableT7), .Ausgabe(AusgabeT7));
  Reg32Bit reg32bit_9 (.Eingabe(Eingabe), .Clk(Clk), .Enable(EnableT8), .Ausgabe(AusgabeT8));
  Reg32Bit reg32bit_10 (.Eingabe(Eingabe), .Clk(Clk), .Enable(EnableT9), .Ausgabe(AusgabeT9));
endmodule

module RegS (
  input  Clk,
  input  [31:0] Eingabe,
  input  EnableS0,
  input  EnableS1,
  input  EnableS2,
  input  EnableS3,
  input  EnableS4,
  input  EnableS5,
  input  EnableS6,
  input  EnableS7,
  output [31:0] AusgabeS0,
  output [31:0] AusgabeS1,
  output [31:0] AusgabeS2,
  output [31:0] AusgabeS3,
  output [31:0] AusgabeS4,
  output [31:0] AusgabeS5,
  output [31:0] AusgabeS6,
  output [31:0] AusgabeS7
);

  Reg32Bit reg32bit_1 (.Eingabe(Eingabe), .Clk(Clk), .Enable(EnableS0), .Ausgabe(AusgabeS0));
  Reg32Bit reg32bit_2 (.Eingabe(Eingabe), .Clk(Clk), .Enable(EnableS1), .Ausgabe(AusgabeS1));
  Reg32Bit reg32bit_3 (.Eingabe(Eingabe), .Clk(Clk), .Enable(EnableS2), .Ausgabe(AusgabeS2));
  Reg32Bit reg32bit_4 (.Eingabe(Eingabe), .Clk(Clk), .Enable(EnableS3), .Ausgabe(AusgabeS3));
  Reg32Bit reg32bit_5 (.Eingabe(Eingabe), .Clk(Clk), .Enable(EnableS4), .Ausgabe(AusgabeS4));
  Reg32Bit reg32bit_6 (.Eingabe(Eingabe), .Clk(Clk), .Enable(EnableS5), .Ausgabe(AusgabeS5));
  Reg32Bit reg32bit_7 (.Eingabe(Eingabe), .Clk(Clk), .Enable(EnableS6), .Ausgabe(AusgabeS6));
  Reg32Bit reg32bit_8 (.Eingabe(Eingabe), .Clk(Clk), .Enable(EnableS7), .Ausgabe(AusgabeS7));
endmodule

module RegK (
  input  EnableK0,
  input  [31:0] Eingabe,
  input  Clk,
  input  EnableK1,
  output [31:0] AusgabeK0,
  output [31:0] AusgabeK1
);

  Reg32Bit reg32bit_1 (.Eingabe(Eingabe), .Clk(Clk), .Enable(EnableK0), .Ausgabe(AusgabeK0));
  Reg32Bit reg32bit_2 (.Eingabe(Eingabe), .Clk(Clk), .Enable(EnableK1), .Ausgabe(AusgabeK1));
endmodule

module RegGP (
  input  [31:0] Eingabe,
  input  Clk,
  input  Enable,
  output [31:0] Ausgabe
);

  Reg32Bit reg32bit_1 (.Eingabe(Eingabe), .Clk(Clk), .Enable(Enable), .Ausgabe(Ausgabe));
endmodule

module RegSP (
  input  [31:0] Eingabe,
  input  Clk,
  input  Enable,
  output [31:0] Ausgabe
);

  Reg32Bit reg32bit_1 (.Eingabe(Eingabe), .Clk(Clk), .Enable(Enable), .Ausgabe(Ausgabe));
endmodule

module RegFP (
  input  [31:0] Eingabe,
  input  Clk,
  input  Enable,
  output [31:0] Ausgabe
);

  Reg32Bit reg32bit_1 (.Eingabe(Eingabe), .Clk(Clk), .Enable(Enable), .Ausgabe(Ausgabe));
endmodule

module RegRA (
  input  [31:0] Eingabe,
  input  Clk,
  input  Enable,
  output [31:0] Ausgabe
);

  Reg32Bit reg32bit_1 (.Eingabe(Eingabe), .Clk(Clk), .Enable(Enable), .Ausgabe(Ausgabe));
endmodule

module RegHI (
  input  [31:0] Eingabe,
  input  Clk,
  output [31:0] Ausgabe
);

  Reg32Bit reg32bit_1 (.Eingabe(Eingabe), .Clk(Clk), .Enable(1'b1), .Ausgabe(Ausgabe));
endmodule

module RegLO (
  input  [31:0] Eingabe,
  input  Clk,
  output [31:0] Ausgabe
);

  Reg32Bit reg32bit_1 (.Eingabe(Eingabe), .Clk(Clk), .Enable(1'b1), .Ausgabe(Ausgabe));
endmodule

module RegFile32Bit (
  input  [4:0] XSel,
  input  [31:0] Data,
  input  Clk,
  input  [4:0] WSel,
  input  WR,
  input  [4:0] YSel,
  output [31:0] XBus,
  output [31:0] out_8,
  output [31:0] out_9,
  output [31:0] out_10,
  output [31:0] YBus
);

  wire demultiplexer_1_out0, demultiplexer_1_out1, demultiplexer_1_out2, demultiplexer_1_out3,
       demultiplexer_1_out4, demultiplexer_1_out5, demultiplexer_1_out6, demultiplexer_1_out7,
       demultiplexer_1_out8, demultiplexer_1_out9, demultiplexer_1_out10, demultiplexer_1_out11,
       demultiplexer_1_out12, demultiplexer_1_out13, demultiplexer_1_out14, demultiplexer_1_out15,
       demultiplexer_1_out16, demultiplexer_1_out17, demultiplexer_1_out18, demultiplexer_1_out19,
       demultiplexer_1_out20, demultiplexer_1_out21, demultiplexer_1_out22, demultiplexer_1_out23,
       demultiplexer_1_out24, demultiplexer_1_out25, demultiplexer_1_out26, demultiplexer_1_out27,
       demultiplexer_1_out28, demultiplexer_1_out29, demultiplexer_1_out30, demultiplexer_1_out31;
  wire [31:0] rega_1_ausgabea0, rega_1_ausgabea1, rega_1_ausgabea2, rega_1_ausgabea3, regfp_1_ausgabe,
       reggp_1_ausgabe, regk_1_ausgabek0, regk_1_ausgabek1, regra_1_ausgabe, regs_1_ausgabes0,
       regs_1_ausgabes1, regs_1_ausgabes2, regs_1_ausgabes3, regs_1_ausgabes4, regs_1_ausgabes5,
       regs_1_ausgabes6, regs_1_ausgabes7, regsp_1_ausgabe, regt_1_ausgabet2, regt_1_ausgabet3,
       regt_1_ausgabet4, regt_1_ausgabet5, regt_1_ausgabet6, regt_1_ausgabet7, regt_1_ausgabet8,
       regt_1_ausgabet9, regv_1_ausgabev0, regv_1_ausgabev1, regzero_1_ausgabe;

  Demultiplexer #(.select(5)) demultiplexer_1 (
    .out0(demultiplexer_1_out0), .out1(demultiplexer_1_out1), .out2(demultiplexer_1_out2),
    .out3(demultiplexer_1_out3), .out4(demultiplexer_1_out4), .out5(demultiplexer_1_out5),
    .out6(demultiplexer_1_out6), .out7(demultiplexer_1_out7), .out8(demultiplexer_1_out8),
    .out9(demultiplexer_1_out9), .out10(demultiplexer_1_out10), .out11(demultiplexer_1_out11),
    .out12(demultiplexer_1_out12), .out13(demultiplexer_1_out13), .out14(demultiplexer_1_out14),
    .out15(demultiplexer_1_out15), .out16(demultiplexer_1_out16), .out17(demultiplexer_1_out17),
    .out18(demultiplexer_1_out18), .out19(demultiplexer_1_out19), .out20(demultiplexer_1_out20),
    .out21(demultiplexer_1_out21), .out22(demultiplexer_1_out22), .out23(demultiplexer_1_out23),
    .out24(demultiplexer_1_out24), .out25(demultiplexer_1_out25), .out26(demultiplexer_1_out26),
    .out27(demultiplexer_1_out27), .out28(demultiplexer_1_out28), .out29(demultiplexer_1_out29),
    .out30(demultiplexer_1_out30), .out31(demultiplexer_1_out31), .in(WR), .sel(WSel));
  RegZERO regzero_1 (.Enable(demultiplexer_1_out0), .Ausgabe(regzero_1_ausgabe));  // open: Display
  RegAT regat_1 (.Clk(Clk), .Eingabe(Data), .Enable(demultiplexer_1_out1), .Ausgabe(out_8));
  RegV regv_1 (
    .Clk(Clk), .Eingabe(Data), .EnableV0(demultiplexer_1_out2), .EnableV1(demultiplexer_1_out3),
    .AusgabeV0(regv_1_ausgabev0), .AusgabeV1(regv_1_ausgabev1));
  RegA rega_1 (
    .Clk(Clk), .Eingabe(Data), .EnableA0(demultiplexer_1_out4), .EnableA1(demultiplexer_1_out5),
    .EnableA2(demultiplexer_1_out6), .EnableA3(demultiplexer_1_out7), .AusgabeA0(rega_1_ausgabea0),
    .AusgabeA1(rega_1_ausgabea1), .AusgabeA2(rega_1_ausgabea2), .AusgabeA3(rega_1_ausgabea3));
  RegT regt_1 (
    .Clk(Clk), .Eingabe(Data), .EnableT0(demultiplexer_1_out8), .EnableT1(demultiplexer_1_out9),
    .EnableT2(demultiplexer_1_out10), .EnableT3(demultiplexer_1_out11), .EnableT4(demultiplexer_1_out12),
    .EnableT5(demultiplexer_1_out13), .EnableT6(demultiplexer_1_out14), .EnableT7(demultiplexer_1_out15),
    .EnableT8(demultiplexer_1_out24), .EnableT9(demultiplexer_1_out25), .AusgabeT0(out_9),
    .AusgabeT1(out_10), .AusgabeT2(regt_1_ausgabet2), .AusgabeT3(regt_1_ausgabet3),
    .AusgabeT4(regt_1_ausgabet4), .AusgabeT5(regt_1_ausgabet5), .AusgabeT6(regt_1_ausgabet6),
    .AusgabeT7(regt_1_ausgabet7), .AusgabeT8(regt_1_ausgabet8), .AusgabeT9(regt_1_ausgabet9));
  RegS regs_1 (
    .Clk(Clk), .Eingabe(Data), .EnableS0(demultiplexer_1_out16), .EnableS1(demultiplexer_1_out17),
    .EnableS2(demultiplexer_1_out18), .EnableS3(demultiplexer_1_out19), .EnableS4(demultiplexer_1_out20),
    .EnableS5(demultiplexer_1_out21), .EnableS6(demultiplexer_1_out22), .EnableS7(demultiplexer_1_out23),
    .AusgabeS0(regs_1_ausgabes0), .AusgabeS1(regs_1_ausgabes1), .AusgabeS2(regs_1_ausgabes2),
    .AusgabeS3(regs_1_ausgabes3), .AusgabeS4(regs_1_ausgabes4), .AusgabeS5(regs_1_ausgabes5),
    .AusgabeS6(regs_1_ausgabes6), .AusgabeS7(regs_1_ausgabes7));
  RegK regk_1 (
    .Clk(Clk), .Eingabe(Data), .EnableK0(demultiplexer_1_out26), .EnableK1(demultiplexer_1_out27),
    .AusgabeK0(regk_1_ausgabek0), .AusgabeK1(regk_1_ausgabek1));
  RegGP reggp_1 (.Clk(Clk), .Eingabe(Data), .Enable(demultiplexer_1_out28), .Ausgabe(reggp_1_ausgabe));
  RegSP regsp_1 (.Clk(Clk), .Eingabe(Data), .Enable(demultiplexer_1_out29), .Ausgabe(regsp_1_ausgabe));
  RegFP regfp_1 (.Clk(Clk), .Eingabe(Data), .Enable(demultiplexer_1_out30), .Ausgabe(regfp_1_ausgabe));
  RegRA regra_1 (.Clk(Clk), .Eingabe(Data), .Enable(demultiplexer_1_out31), .Ausgabe(regra_1_ausgabe));
  Multiplexer #(.select(5), .width(32)) multiplexer_1 (
    .in0(regzero_1_ausgabe), .in1(out_8), .in2(regv_1_ausgabev0), .in3(regv_1_ausgabev1),
    .in4(rega_1_ausgabea0), .in5(rega_1_ausgabea1), .in6(rega_1_ausgabea2), .in7(rega_1_ausgabea3),
    .in8(out_9), .in9(out_10), .in10(regt_1_ausgabet2), .in11(regt_1_ausgabet3), .in12(regt_1_ausgabet4),
    .in13(regt_1_ausgabet5), .in14(regt_1_ausgabet6), .in15(regt_1_ausgabet7), .in16(regs_1_ausgabes0),
    .in17(regs_1_ausgabes1), .in18(regs_1_ausgabes2), .in19(regs_1_ausgabes3), .in20(regs_1_ausgabes4),
    .in21(regs_1_ausgabes5), .in22(regs_1_ausgabes6), .in23(regs_1_ausgabes7), .in24(regt_1_ausgabet8),
    .in25(regt_1_ausgabet9), .in26(regk_1_ausgabek0), .in27(regk_1_ausgabek1), .in28(reggp_1_ausgabe),
    .in29(regsp_1_ausgabe), .in30(regfp_1_ausgabe), .in31(regra_1_ausgabe), .out(XBus), .sel(XSel));
  Multiplexer #(.select(5), .width(32)) multiplexer_2 (
    .in0(regzero_1_ausgabe), .in1(out_8), .in2(regv_1_ausgabev0), .in3(regv_1_ausgabev1),
    .in4(rega_1_ausgabea0), .in5(rega_1_ausgabea1), .in6(rega_1_ausgabea2), .in7(rega_1_ausgabea3),
    .in8(out_9), .in9(out_10), .in10(regt_1_ausgabet2), .in11(regt_1_ausgabet3), .in12(regt_1_ausgabet4),
    .in13(regt_1_ausgabet5), .in14(regt_1_ausgabet6), .in15(regt_1_ausgabet7), .in16(regs_1_ausgabes0),
    .in17(regs_1_ausgabes1), .in18(regs_1_ausgabes2), .in19(regs_1_ausgabes3), .in20(regs_1_ausgabes4),
    .in21(regs_1_ausgabes5), .in22(regs_1_ausgabes6), .in23(regs_1_ausgabes7), .in24(regt_1_ausgabet8),
    .in25(regt_1_ausgabet9), .in26(regk_1_ausgabek0), .in27(regk_1_ausgabek1), .in28(reggp_1_ausgabe),
    .in29(regsp_1_ausgabe), .in30(regfp_1_ausgabe), .in31(regra_1_ausgabe), .out(YBus), .sel(YSel));
endmodule

module RegFile32x32BitDisplay (
  input  [4:0] XSel,
  input  [31:0] Data,
  input  Clk,
  input  [4:0] WSel,
  input  WR,
  input  [4:0] YSel,
  output [31:0] XBus,
  output [31:0] at,
  output [31:0] v0,
  output [31:0] v1,
  output [31:0] a0,
  output [31:0] a1,
  output [31:0] a2,
  output [31:0] a3,
  output [31:0] t0,
  output [31:0] t1,
  output [31:0] t2,
  output [31:0] t3,
  output [31:0] t4,
  output [31:0] t5,
  output [31:0] t6,
  output [31:0] t7,
  output [31:0] t8,
  output [31:0] t9,
  output [31:0] s0,
  output [31:0] s1,
  output [31:0] s2,
  output [31:0] s3,
  output [31:0] s4,
  output [31:0] s5,
  output [31:0] s6,
  output [31:0] s7,
  output [31:0] k0,
  output [31:0] k1,
  output [31:0] gp,
  output [31:0] sp,
  output [31:0] fp,
  output [31:0] ra,
  output [31:0] YBus
);

  wire demultiplexer_1_out0, demultiplexer_1_out1, demultiplexer_1_out2, demultiplexer_1_out3,
       demultiplexer_1_out4, demultiplexer_1_out5, demultiplexer_1_out6, demultiplexer_1_out7,
       demultiplexer_1_out8, demultiplexer_1_out9, demultiplexer_1_out10, demultiplexer_1_out11,
       demultiplexer_1_out12, demultiplexer_1_out13, demultiplexer_1_out14, demultiplexer_1_out15,
       demultiplexer_1_out16, demultiplexer_1_out17, demultiplexer_1_out18, demultiplexer_1_out19,
       demultiplexer_1_out20, demultiplexer_1_out21, demultiplexer_1_out22, demultiplexer_1_out23,
       demultiplexer_1_out24, demultiplexer_1_out25, demultiplexer_1_out26, demultiplexer_1_out27,
       demultiplexer_1_out28, demultiplexer_1_out29, demultiplexer_1_out30, demultiplexer_1_out31;
  wire [31:0] regzero_1_ausgabe;

  Demultiplexer #(.select(5)) demultiplexer_1 (
    .out0(demultiplexer_1_out0), .out1(demultiplexer_1_out1), .out2(demultiplexer_1_out2),
    .out3(demultiplexer_1_out3), .out4(demultiplexer_1_out4), .out5(demultiplexer_1_out5),
    .out6(demultiplexer_1_out6), .out7(demultiplexer_1_out7), .out8(demultiplexer_1_out8),
    .out9(demultiplexer_1_out9), .out10(demultiplexer_1_out10), .out11(demultiplexer_1_out11),
    .out12(demultiplexer_1_out12), .out13(demultiplexer_1_out13), .out14(demultiplexer_1_out14),
    .out15(demultiplexer_1_out15), .out16(demultiplexer_1_out16), .out17(demultiplexer_1_out17),
    .out18(demultiplexer_1_out18), .out19(demultiplexer_1_out19), .out20(demultiplexer_1_out20),
    .out21(demultiplexer_1_out21), .out22(demultiplexer_1_out22), .out23(demultiplexer_1_out23),
    .out24(demultiplexer_1_out24), .out25(demultiplexer_1_out25), .out26(demultiplexer_1_out26),
    .out27(demultiplexer_1_out27), .out28(demultiplexer_1_out28), .out29(demultiplexer_1_out29),
    .out30(demultiplexer_1_out30), .out31(demultiplexer_1_out31), .in(WR), .sel(WSel));
  RegZERO regzero_1 (.Enable(demultiplexer_1_out0), .Ausgabe(regzero_1_ausgabe));  // open: Display
  RegAT regat_1 (.Clk(Clk), .Eingabe(Data), .Enable(demultiplexer_1_out1), .Ausgabe(at));
  RegV regv_1 (
    .Clk(Clk), .Eingabe(Data), .EnableV0(demultiplexer_1_out2), .EnableV1(demultiplexer_1_out3),
    .AusgabeV0(v0), .AusgabeV1(v1));
  RegA rega_1 (
    .Clk(Clk), .Eingabe(Data), .EnableA0(demultiplexer_1_out4), .EnableA1(demultiplexer_1_out5),
    .EnableA2(demultiplexer_1_out6), .EnableA3(demultiplexer_1_out7), .AusgabeA0(a0), .AusgabeA1(a1),
    .AusgabeA2(a2), .AusgabeA3(a3));
  RegT regt_1 (
    .Clk(Clk), .Eingabe(Data), .EnableT0(demultiplexer_1_out8), .EnableT1(demultiplexer_1_out9),
    .EnableT2(demultiplexer_1_out10), .EnableT3(demultiplexer_1_out11), .EnableT4(demultiplexer_1_out12),
    .EnableT5(demultiplexer_1_out13), .EnableT6(demultiplexer_1_out14), .EnableT7(demultiplexer_1_out15),
    .EnableT8(demultiplexer_1_out24), .EnableT9(demultiplexer_1_out25), .AusgabeT0(t0), .AusgabeT1(t1),
    .AusgabeT2(t2), .AusgabeT3(t3), .AusgabeT4(t4), .AusgabeT5(t5), .AusgabeT6(t6), .AusgabeT7(t7),
    .AusgabeT8(t8), .AusgabeT9(t9));
  RegS regs_1 (
    .Clk(Clk), .Eingabe(Data), .EnableS0(demultiplexer_1_out16), .EnableS1(demultiplexer_1_out17),
    .EnableS2(demultiplexer_1_out18), .EnableS3(demultiplexer_1_out19), .EnableS4(demultiplexer_1_out20),
    .EnableS5(demultiplexer_1_out21), .EnableS6(demultiplexer_1_out22), .EnableS7(demultiplexer_1_out23),
    .AusgabeS0(s0), .AusgabeS1(s1), .AusgabeS2(s2), .AusgabeS3(s3), .AusgabeS4(s4), .AusgabeS5(s5),
    .AusgabeS6(s6), .AusgabeS7(s7));
  RegK regk_1 (
    .Clk(Clk), .Eingabe(Data), .EnableK0(demultiplexer_1_out26), .EnableK1(demultiplexer_1_out27),
    .AusgabeK0(k0), .AusgabeK1(k1));
  RegGP reggp_1 (.Clk(Clk), .Eingabe(Data), .Enable(demultiplexer_1_out28), .Ausgabe(gp));
  RegSP regsp_1 (.Clk(Clk), .Eingabe(Data), .Enable(demultiplexer_1_out29), .Ausgabe(sp));
  RegFP regfp_1 (.Clk(Clk), .Eingabe(Data), .Enable(demultiplexer_1_out30), .Ausgabe(fp));
  RegRA regra_1 (.Clk(Clk), .Eingabe(Data), .Enable(demultiplexer_1_out31), .Ausgabe(ra));
  Multiplexer #(.select(5), .width(32)) multiplexer_1 (
    .in0(regzero_1_ausgabe), .in1(at), .in2(v0), .in3(v1), .in4(a0), .in5(a1), .in6(a2), .in7(a3), .in8(t0),
    .in9(t1), .in10(t2), .in11(t3), .in12(t4), .in13(t5), .in14(t6), .in15(t7), .in16(s0), .in17(s1),
    .in18(s2), .in19(s3), .in20(s4), .in21(s5), .in22(s6), .in23(s7), .in24(t8), .in25(t9), .in26(k0),
    .in27(k1), .in28(gp), .in29(sp), .in30(fp), .in31(ra), .out(XBus), .sel(XSel));
  Multiplexer #(.select(5), .width(32)) multiplexer_2 (
    .in0(regzero_1_ausgabe), .in1(at), .in2(v0), .in3(v1), .in4(a0), .in5(a1), .in6(a2), .in7(a3), .in8(t0),
    .in9(t1), .in10(t2), .in11(t3), .in12(t4), .in13(t5), .in14(t6), .in15(t7), .in16(s0), .in17(s1),
    .in18(s2), .in19(s3), .in20(s4), .in21(s5), .in22(s6), .in23(s7), .in24(t8), .in25(t9), .in26(k0),
    .in27(k1), .in28(gp), .in29(sp), .in30(fp), .in31(ra), .out(YBus), .sel(YSel));
endmodule

module FPRegFile (
  input  [4:0] XSel,
  input  [31:0] Data,
  input  Clk,
  input  [4:0] WSel,
  input  WR,
  input  [4:0] YSel,
  output [31:0] XBus,
  output [31:0] out_8,
  output [31:0] out_9,
  output [31:0] out_10,
  output [31:0] out_11,
  output [31:0] YBus
);

  wire demultiplexer_1_out0, demultiplexer_1_out1, demultiplexer_1_out2, demultiplexer_1_out3,
       demultiplexer_1_out4, demultiplexer_1_out5, demultiplexer_1_out6, demultiplexer_1_out7,
       demultiplexer_1_out8, demultiplexer_1_out9, demultiplexer_1_out10, demultiplexer_1_out11,
       demultiplexer_1_out12, demultiplexer_1_out13, demultiplexer_1_out14, demultiplexer_1_out15,
       demultiplexer_1_out16, demultiplexer_1_out17, demultiplexer_1_out18, demultiplexer_1_out19,
       demultiplexer_1_out20, demultiplexer_1_out21, demultiplexer_1_out22, demultiplexer_1_out23,
       demultiplexer_1_out24, demultiplexer_1_out25, demultiplexer_1_out26, demultiplexer_1_out27,
       demultiplexer_1_out28, demultiplexer_1_out29, demultiplexer_1_out30, demultiplexer_1_out31;
  wire [31:0] fpreg32bit_5_ausgabe, fpreg32bit_6_ausgabe, fpreg32bit_7_ausgabe, fpreg32bit_8_ausgabe,
       fpreg32bit_9_ausgabe, fpreg32bit_10_ausgabe, fpreg32bit_11_ausgabe, fpreg32bit_12_ausgabe,
       fpreg32bit_13_ausgabe, fpreg32bit_14_ausgabe, fpreg32bit_15_ausgabe, fpreg32bit_16_ausgabe,
       fpreg32bit_17_ausgabe, fpreg32bit_18_ausgabe, fpreg32bit_19_ausgabe, fpreg32bit_20_ausgabe,
       fpreg32bit_21_ausgabe, fpreg32bit_22_ausgabe, fpreg32bit_23_ausgabe, fpreg32bit_24_ausgabe,
       fpreg32bit_25_ausgabe, fpreg32bit_26_ausgabe, fpreg32bit_27_ausgabe, fpreg32bit_28_ausgabe,
       fpreg32bit_29_ausgabe, fpreg32bit_30_ausgabe, fpreg32bit_31_ausgabe, fpreg32bit_32_ausgabe;

  Demultiplexer #(.select(5)) demultiplexer_1 (
    .out0(demultiplexer_1_out0), .out1(demultiplexer_1_out1), .out2(demultiplexer_1_out2),
    .out3(demultiplexer_1_out3), .out4(demultiplexer_1_out4), .out5(demultiplexer_1_out5),
    .out6(demultiplexer_1_out6), .out7(demultiplexer_1_out7), .out8(demultiplexer_1_out8),
    .out9(demultiplexer_1_out9), .out10(demultiplexer_1_out10), .out11(demultiplexer_1_out11),
    .out12(demultiplexer_1_out12), .out13(demultiplexer_1_out13), .out14(demultiplexer_1_out14),
    .out15(demultiplexer_1_out15), .out16(demultiplexer_1_out16), .out17(demultiplexer_1_out17),
    .out18(demultiplexer_1_out18), .out19(demultiplexer_1_out19), .out20(demultiplexer_1_out20),
    .out21(demultiplexer_1_out21), .out22(demultiplexer_1_out22), .out23(demultiplexer_1_out23),
    .out24(demultiplexer_1_out24), .out25(demultiplexer_1_out25), .out26(demultiplexer_1_out26),
    .out27(demultiplexer_1_out27), .out28(demultiplexer_1_out28), .out29(demultiplexer_1_out29),
    .out30(demultiplexer_1_out30), .out31(demultiplexer_1_out31), .in(WR), .sel(WSel));
  FPReg32Bit fpreg32bit_1 (.Eingabe(Data), .Clk(Clk), .Enable(demultiplexer_1_out0), .Ausgabe(out_8));
  FPReg32Bit fpreg32bit_2 (.Eingabe(Data), .Clk(Clk), .Enable(demultiplexer_1_out1), .Ausgabe(out_9));
  FPReg32Bit fpreg32bit_3 (.Eingabe(Data), .Clk(Clk), .Enable(demultiplexer_1_out2), .Ausgabe(out_10));
  FPReg32Bit fpreg32bit_4 (.Eingabe(Data), .Clk(Clk), .Enable(demultiplexer_1_out3), .Ausgabe(out_11));
  FPReg32Bit fpreg32bit_5 (.Eingabe(Data), .Clk(Clk), .Enable(demultiplexer_1_out4), .Ausgabe(fpreg32bit_5_ausgabe));
  FPReg32Bit fpreg32bit_6 (.Eingabe(Data), .Clk(Clk), .Enable(demultiplexer_1_out5), .Ausgabe(fpreg32bit_6_ausgabe));
  FPReg32Bit fpreg32bit_7 (.Eingabe(Data), .Clk(Clk), .Enable(demultiplexer_1_out6), .Ausgabe(fpreg32bit_7_ausgabe));
  FPReg32Bit fpreg32bit_8 (.Eingabe(Data), .Clk(Clk), .Enable(demultiplexer_1_out7), .Ausgabe(fpreg32bit_8_ausgabe));
  FPReg32Bit fpreg32bit_9 (.Eingabe(Data), .Clk(Clk), .Enable(demultiplexer_1_out8), .Ausgabe(fpreg32bit_9_ausgabe));
  FPReg32Bit fpreg32bit_10 (.Eingabe(Data), .Clk(Clk), .Enable(demultiplexer_1_out9), .Ausgabe(fpreg32bit_10_ausgabe));
  FPReg32Bit fpreg32bit_11 (.Eingabe(Data), .Clk(Clk), .Enable(demultiplexer_1_out10), .Ausgabe(fpreg32bit_11_ausgabe));
  FPReg32Bit fpreg32bit_12 (.Eingabe(Data), .Clk(Clk), .Enable(demultiplexer_1_out11), .Ausgabe(fpreg32bit_12_ausgabe));
  FPReg32Bit fpreg32bit_13 (.Eingabe(Data), .Clk(Clk), .Enable(demultiplexer_1_out12), .Ausgabe(fpreg32bit_13_ausgabe));
  FPReg32Bit fpreg32bit_14 (.Eingabe(Data), .Clk(Clk), .Enable(demultiplexer_1_out13), .Ausgabe(fpreg32bit_14_ausgabe));
  FPReg32Bit fpreg32bit_15 (.Eingabe(Data), .Clk(Clk), .Enable(demultiplexer_1_out14), .Ausgabe(fpreg32bit_15_ausgabe));
  FPReg32Bit fpreg32bit_16 (.Eingabe(Data), .Clk(Clk), .Enable(demultiplexer_1_out15), .Ausgabe(fpreg32bit_16_ausgabe));
  FPReg32Bit fpreg32bit_17 (.Eingabe(Data), .Clk(Clk), .Enable(demultiplexer_1_out16), .Ausgabe(fpreg32bit_17_ausgabe));
  FPReg32Bit fpreg32bit_18 (.Eingabe(Data), .Clk(Clk), .Enable(demultiplexer_1_out17), .Ausgabe(fpreg32bit_18_ausgabe));
  FPReg32Bit fpreg32bit_19 (.Eingabe(Data), .Clk(Clk), .Enable(demultiplexer_1_out18), .Ausgabe(fpreg32bit_19_ausgabe));
  FPReg32Bit fpreg32bit_20 (.Eingabe(Data), .Clk(Clk), .Enable(demultiplexer_1_out19), .Ausgabe(fpreg32bit_20_ausgabe));
  FPReg32Bit fpreg32bit_21 (.Eingabe(Data), .Clk(Clk), .Enable(demultiplexer_1_out20), .Ausgabe(fpreg32bit_21_ausgabe));
  FPReg32Bit fpreg32bit_22 (.Eingabe(Data), .Clk(Clk), .Enable(demultiplexer_1_out21), .Ausgabe(fpreg32bit_22_ausgabe));
  FPReg32Bit fpreg32bit_23 (.Eingabe(Data), .Clk(Clk), .Enable(demultiplexer_1_out22), .Ausgabe(fpreg32bit_23_ausgabe));
  FPReg32Bit fpreg32bit_24 (.Eingabe(Data), .Clk(Clk), .Enable(demultiplexer_1_out23), .Ausgabe(fpreg32bit_24_ausgabe));
  FPReg32Bit fpreg32bit_25 (.Eingabe(Data), .Clk(Clk), .Enable(demultiplexer_1_out24), .Ausgabe(fpreg32bit_25_ausgabe));
  FPReg32Bit fpreg32bit_26 (.Eingabe(Data), .Clk(Clk), .Enable(demultiplexer_1_out25), .Ausgabe(fpreg32bit_26_ausgabe));
  FPReg32Bit fpreg32bit_27 (.Eingabe(Data), .Clk(Clk), .Enable(demultiplexer_1_out26), .Ausgabe(fpreg32bit_27_ausgabe));
  FPReg32Bit fpreg32bit_28 (.Eingabe(Data), .Clk(Clk), .Enable(demultiplexer_1_out27), .Ausgabe(fpreg32bit_28_ausgabe));
  FPReg32Bit fpreg32bit_29 (.Eingabe(Data), .Clk(Clk), .Enable(demultiplexer_1_out28), .Ausgabe(fpreg32bit_29_ausgabe));
  FPReg32Bit fpreg32bit_30 (.Eingabe(Data), .Clk(Clk), .Enable(demultiplexer_1_out29), .Ausgabe(fpreg32bit_30_ausgabe));
  FPReg32Bit fpreg32bit_31 (.Eingabe(Data), .Clk(Clk), .Enable(demultiplexer_1_out30), .Ausgabe(fpreg32bit_31_ausgabe));
  FPReg32Bit fpreg32bit_32 (.Eingabe(Data), .Clk(Clk), .Enable(demultiplexer_1_out31), .Ausgabe(fpreg32bit_32_ausgabe));
  Multiplexer #(.select(5), .width(32)) multiplexer_1 (
    .in0(out_8), .in1(out_9), .in2(out_10), .in3(out_11), .in4(fpreg32bit_5_ausgabe),
    .in5(fpreg32bit_6_ausgabe), .in6(fpreg32bit_7_ausgabe), .in7(fpreg32bit_8_ausgabe),
    .in8(fpreg32bit_9_ausgabe), .in9(fpreg32bit_10_ausgabe), .in10(fpreg32bit_11_ausgabe),
    .in11(fpreg32bit_12_ausgabe), .in12(fpreg32bit_13_ausgabe), .in13(fpreg32bit_14_ausgabe),
    .in14(fpreg32bit_15_ausgabe), .in15(fpreg32bit_16_ausgabe), .in16(fpreg32bit_17_ausgabe),
    .in17(fpreg32bit_18_ausgabe), .in18(fpreg32bit_19_ausgabe), .in19(fpreg32bit_20_ausgabe),
    .in20(fpreg32bit_21_ausgabe), .in21(fpreg32bit_22_ausgabe), .in22(fpreg32bit_23_ausgabe),
    .in23(fpreg32bit_24_ausgabe), .in24(fpreg32bit_25_ausgabe), .in25(fpreg32bit_26_ausgabe),
    .in26(fpreg32bit_27_ausgabe), .in27(fpreg32bit_28_ausgabe), .in28(fpreg32bit_29_ausgabe),
    .in29(fpreg32bit_30_ausgabe), .in30(fpreg32bit_31_ausgabe), .in31(fpreg32bit_32_ausgabe), .out(XBus),
    .sel(XSel));
  Multiplexer #(.select(5), .width(32)) multiplexer_2 (
    .in0(out_8), .in1(out_9), .in2(out_10), .in3(out_11), .in4(fpreg32bit_5_ausgabe),
    .in5(fpreg32bit_6_ausgabe), .in6(fpreg32bit_7_ausgabe), .in7(fpreg32bit_8_ausgabe),
    .in8(fpreg32bit_9_ausgabe), .in9(fpreg32bit_10_ausgabe), .in10(fpreg32bit_11_ausgabe),
    .in11(fpreg32bit_12_ausgabe), .in12(fpreg32bit_13_ausgabe), .in13(fpreg32bit_14_ausgabe),
    .in14(fpreg32bit_15_ausgabe), .in15(fpreg32bit_16_ausgabe), .in16(fpreg32bit_17_ausgabe),
    .in17(fpreg32bit_18_ausgabe), .in18(fpreg32bit_19_ausgabe), .in19(fpreg32bit_20_ausgabe),
    .in20(fpreg32bit_21_ausgabe), .in21(fpreg32bit_22_ausgabe), .in22(fpreg32bit_23_ausgabe),
    .in23(fpreg32bit_24_ausgabe), .in24(fpreg32bit_25_ausgabe), .in25(fpreg32bit_26_ausgabe),
    .in26(fpreg32bit_27_ausgabe), .in27(fpreg32bit_28_ausgabe), .in28(fpreg32bit_29_ausgabe),
    .in29(fpreg32bit_30_ausgabe), .in30(fpreg32bit_31_ausgabe), .in31(fpreg32bit_32_ausgabe), .out(YBus),
    .sel(YSel));
endmodule

module TwosComplement (
  input  Sel0,
  input  Sel1,
  input  [1:0] DisableforComparator,
  output twosComplementSel
);

  wire and_1_out, and_2_out, not_1_out, not_2_out;

  not not_1 (not_1_out, Sel0);
  and and_1 (and_1_out, not_1_out, Sel1);
  not not_2 (not_2_out, DisableforComparator[0]);
  and and_2 (and_2_out, not_2_out, DisableforComparator[1]);
  Multiplexer multiplexer_1 (.in0(and_1_out), .in1(1'b0), .out(twosComplementSel), .sel(and_2_out));

  // Notes on the sheet:
  //   when doing comparator instructions, two's complement must be turned off because of instruction overlapping
endmodule

module Increment (
  input  S0,
  input  S1,
  input  S2,
  output out_4
);

  wire not_1_out, not_2_out;

  not not_1 (not_1_out, S0);
  not not_2 (not_2_out, S1);
  and and_1 (out_4, not_1_out, not_2_out, S2);
endmodule

module Decrement (
  input  S0,
  input  S1,
  input  S2,
  output out_4
);

  wire not_1_out;

  not not_1 (not_1_out, S1);
  and and_1 (out_4, S0, not_1_out, S2);
endmodule

module Equal (
  input  [31:0] A,
  input  [31:0] B,
  output AequalB
);

  wire [31:0] xor_1_out;

  assign xor_1_out = A ^ B;  // XOR_Gate xor_1, 32 bits wide
  nor nor_1 (AequalB, xor_1_out[31], xor_1_out[30], xor_1_out[29], xor_1_out[28], xor_1_out[27], xor_1_out[26], xor_1_out[25], xor_1_out[24], xor_1_out[23], xor_1_out[22], xor_1_out[21], xor_1_out[20], xor_1_out[19], xor_1_out[18], xor_1_out[17], xor_1_out[16], xor_1_out[15], xor_1_out[14], xor_1_out[13], xor_1_out[12], xor_1_out[11], xor_1_out[10], xor_1_out[9], xor_1_out[8], xor_1_out[7], xor_1_out[6], xor_1_out[5], xor_1_out[4], xor_1_out[3], xor_1_out[2], xor_1_out[1], xor_1_out[0]);
endmodule

module Less (
  input  CoutSUBLESS,
  output AlessB
);

  not not_1 (AlessB, CoutSUBLESS);
endmodule

module HA1Bit (
  input  A,
  input  B,
  output Cout,
  output S
);

  xor xor_1 (S, A, B);
  and and_1 (Cout, A, B);
endmodule

module FA1Bit (
  input  Cin,
  input  A,
  input  B,
  output Cout,
  output S
);

  wire ha1bit_1_cout, ha1bit_1_s, ha1bit_2_cout;

  HA1Bit ha1bit_1 (.B(B), .A(A), .Cout(ha1bit_1_cout), .S(ha1bit_1_s));
  HA1Bit ha1bit_2 (.B(ha1bit_1_s), .A(Cin), .Cout(ha1bit_2_cout), .S(S));
  or or_1 (Cout, ha1bit_2_cout, ha1bit_1_cout);
endmodule

module Adder8Bit (
  input  Cin,
  input  [7:0] A,
  input  [7:0] B,
  output [7:0] S,
  output Cout
);

  wire fa1bit_1_cout, fa1bit_2_cout, fa1bit_3_cout, fa1bit_4_cout, fa1bit_5_cout, fa1bit_6_cout,
       fa1bit_7_cout;

  FA1Bit fa1bit_1 (.Cin(Cin), .A(A[0]), .B(B[0]), .Cout(fa1bit_1_cout), .S(S[0]));
  FA1Bit fa1bit_2 (.Cin(fa1bit_1_cout), .A(A[1]), .B(B[1]), .Cout(fa1bit_2_cout), .S(S[1]));
  FA1Bit fa1bit_3 (.Cin(fa1bit_2_cout), .A(A[2]), .B(B[2]), .Cout(fa1bit_3_cout), .S(S[2]));
  FA1Bit fa1bit_4 (.Cin(fa1bit_3_cout), .A(A[3]), .B(B[3]), .Cout(fa1bit_4_cout), .S(S[3]));
  FA1Bit fa1bit_5 (.Cin(fa1bit_4_cout), .A(A[4]), .B(B[4]), .Cout(fa1bit_5_cout), .S(S[4]));
  FA1Bit fa1bit_6 (.Cin(fa1bit_5_cout), .A(A[5]), .B(B[5]), .Cout(fa1bit_6_cout), .S(S[5]));
  FA1Bit fa1bit_7 (.Cin(fa1bit_6_cout), .A(A[6]), .B(B[6]), .Cout(fa1bit_7_cout), .S(S[6]));
  FA1Bit fa1bit_8 (.Cin(fa1bit_7_cout), .A(A[7]), .B(B[7]), .Cout(Cout), .S(S[7]));
endmodule

module Adder32Bit (
  input  Cin,
  input  [31:0] A,
  input  [31:0] B,
  output [31:0] S,
  output Cout
);

  wire adder8bit_1_cout, adder8bit_2_cout, adder8bit_3_cout;

  Adder8Bit adder8bit_1 (.Cin(Cin), .A(B[7:0]), .B(A[7:0]), .S(S[7:0]), .Cout(adder8bit_1_cout));
  Adder8Bit adder8bit_2 (.Cin(adder8bit_1_cout), .A(B[15:8]), .B(A[15:8]), .S(S[15:8]), .Cout(adder8bit_2_cout));
  Adder8Bit adder8bit_3 (.Cin(adder8bit_2_cout), .A(B[23:16]), .B(A[23:16]), .S(S[23:16]), .Cout(adder8bit_3_cout));
  Adder8Bit adder8bit_4 (.Cin(adder8bit_3_cout), .A(B[31:24]), .B(A[31:24]), .S(S[31:24]), .Cout(Cout));
endmodule

module Subtractor32Bit (
  input  [31:0] A,
  input  [31:0] B,
  output [31:0] S,
  output Cout
);

  wire adder8bit_1_cout, adder8bit_2_cout, adder8bit_3_cout;
  wire [31:0] not_1_out;

  assign not_1_out = ~B;  // NOT_Gate not_1, 32 bits wide
  Adder8Bit adder8bit_1 (.Cin(1'b1), .A(A[7:0]), .B(not_1_out[7:0]), .S(S[7:0]), .Cout(adder8bit_1_cout));
  Adder8Bit adder8bit_2 (
    .Cin(adder8bit_1_cout), .A(A[15:8]), .B(not_1_out[15:8]), .S(S[15:8]), .Cout(adder8bit_2_cout));
  Adder8Bit adder8bit_3 (
    .Cin(adder8bit_2_cout), .A(A[23:16]), .B(not_1_out[23:16]), .S(S[23:16]), .Cout(adder8bit_3_cout));
  Adder8Bit adder8bit_4 (.Cin(adder8bit_3_cout), .A(A[31:24]), .B(not_1_out[31:24]), .S(S[31:24]), .Cout(Cout));
endmodule
module Multiplier32Bit (
  input  [31:0] A,
  input  [31:0] B,
  output [31:0] Product
);

  wire and_1_out, and_2_out, and_3_out, and_4_out, and_5_out, and_6_out, and_7_out, and_8_out, and_9_out,
       and_10_out, and_11_out, and_12_out, and_13_out, and_14_out, and_15_out, and_16_out, and_17_out,
       and_18_out, and_19_out, and_20_out, and_21_out, and_22_out, and_23_out, and_24_out, and_25_out,
       and_26_out, and_27_out, and_28_out, and_29_out, and_30_out, and_31_out, and_32_out, and_33_out,
       and_34_out, and_35_out, and_36_out, and_37_out, and_38_out, and_39_out, and_40_out, and_41_out,
       and_42_out, and_43_out, and_44_out, and_45_out, and_46_out, and_47_out, and_48_out, and_49_out,
       and_50_out, and_51_out, and_52_out, and_53_out, and_54_out, and_55_out, and_56_out, and_57_out,
       and_58_out, and_59_out, and_60_out, and_61_out, and_62_out, and_63_out, and_64_out, and_65_out,
       and_66_out, and_67_out, and_68_out, and_69_out, and_70_out, and_71_out, and_72_out, and_73_out,
       and_74_out, and_75_out, and_76_out, and_77_out, and_78_out, and_79_out, and_80_out, and_81_out,
       and_82_out, and_83_out, and_84_out, and_85_out, and_86_out, and_87_out, and_88_out, and_89_out,
       and_90_out, and_91_out, and_92_out, and_93_out, and_94_out, and_95_out, and_96_out, and_97_out,
       and_98_out, and_99_out, and_100_out, and_101_out, and_102_out, and_103_out, and_104_out, and_105_out,
       and_106_out, and_107_out, and_108_out, and_109_out, and_110_out, and_111_out, and_112_out,
       and_113_out, and_114_out, and_115_out, and_116_out, and_117_out, and_118_out, and_119_out,
       and_120_out, and_121_out, and_122_out, and_123_out, and_124_out, and_125_out, and_126_out,
       and_127_out, and_128_out, and_129_out, and_130_out, and_131_out, and_132_out, and_133_out,
       and_134_out, and_135_out, and_136_out, and_137_out, and_138_out, and_139_out, and_140_out,
       and_141_out, and_142_out, and_143_out, and_144_out, and_145_out, and_146_out, and_147_out,
       and_148_out, and_149_out, and_150_out, and_151_out, and_152_out, and_153_out, and_154_out,
       and_155_out, and_156_out, and_157_out, and_158_out, and_159_out, and_160_out, and_161_out,
       and_162_out, and_163_out, and_164_out, and_165_out, and_166_out, and_167_out, and_168_out,
       and_169_out, and_170_out, and_171_out, and_172_out, and_173_out, and_174_out, and_175_out,
       and_176_out, and_177_out, and_178_out, and_179_out, and_180_out, and_181_out, and_182_out,
       and_183_out, and_184_out, and_185_out, and_186_out, and_187_out, and_188_out, and_189_out,
       and_190_out, and_191_out, and_192_out, and_193_out, and_194_out, and_195_out, and_196_out,
       and_197_out, and_198_out, and_199_out, and_200_out, and_201_out, and_202_out, and_203_out,
       and_204_out, and_205_out, and_206_out, and_207_out, and_208_out, and_209_out, and_210_out,
       and_211_out, and_212_out, and_213_out, and_214_out, and_215_out, and_216_out, and_217_out,
       and_218_out, and_219_out, and_220_out, and_221_out, and_222_out, and_223_out, and_224_out,
       and_225_out, and_226_out, and_227_out, and_228_out, and_229_out, and_230_out, and_231_out,
       and_232_out, and_233_out, and_234_out, and_235_out, and_236_out, and_237_out, and_238_out,
       and_239_out, and_240_out, and_241_out, and_242_out, and_243_out, and_244_out, and_245_out,
       and_246_out, and_247_out, and_248_out, and_249_out, and_250_out, and_251_out, and_252_out,
       and_253_out, and_254_out, and_255_out, fa1bit_2_cout, fa1bit_2_s, fa1bit_3_cout, fa1bit_3_s,
       fa1bit_4_cout, fa1bit_5_cout, fa1bit_5_s, fa1bit_6_cout, fa1bit_6_s, fa1bit_7_cout, fa1bit_8_cout,
       fa1bit_8_s, fa1bit_9_cout, fa1bit_9_s, fa1bit_10_cout, fa1bit_10_s, fa1bit_11_cout, fa1bit_12_cout,
       fa1bit_12_s, fa1bit_13_cout, fa1bit_13_s, fa1bit_14_cout, fa1bit_14_s, fa1bit_15_cout, fa1bit_15_s,
       fa1bit_16_cout, fa1bit_17_cout, fa1bit_17_s, fa1bit_18_cout, fa1bit_18_s, fa1bit_19_cout, fa1bit_19_s,
       fa1bit_20_cout, fa1bit_20_s, fa1bit_21_cout, fa1bit_21_s, fa1bit_22_cout, fa1bit_23_cout, fa1bit_23_s,
       fa1bit_24_cout, fa1bit_24_s, fa1bit_25_cout, fa1bit_25_s, fa1bit_26_cout, fa1bit_26_s, fa1bit_27_cout,
       fa1bit_27_s, fa1bit_28_cout, fa1bit_28_s, fa1bit_29_cout, fa1bit_30_cout, fa1bit_30_s, fa1bit_31_cout,
       fa1bit_31_s, fa1bit_32_cout, fa1bit_32_s, fa1bit_33_cout, fa1bit_33_s, fa1bit_34_cout, fa1bit_34_s,
       fa1bit_35_cout, fa1bit_35_s, fa1bit_36_cout, fa1bit_36_s, fa1bit_37_cout, fa1bit_38_cout, fa1bit_38_s,
       fa1bit_39_cout, fa1bit_39_s, fa1bit_40_cout, fa1bit_40_s, fa1bit_41_cout, fa1bit_41_s, fa1bit_42_cout,
       fa1bit_42_s, fa1bit_43_cout, fa1bit_43_s, fa1bit_44_cout, fa1bit_44_s, fa1bit_45_cout, fa1bit_45_s,
       fa1bit_46_cout, fa1bit_47_cout, fa1bit_47_s, fa1bit_48_cout, fa1bit_48_s, fa1bit_49_cout, fa1bit_49_s,
       fa1bit_50_cout, fa1bit_50_s, fa1bit_51_cout, fa1bit_51_s, fa1bit_52_cout, fa1bit_52_s, fa1bit_53_cout,
       fa1bit_53_s, fa1bit_54_cout, fa1bit_54_s, fa1bit_55_cout, fa1bit_55_s, fa1bit_56_cout, fa1bit_56_s,
       fa1bit_57_cout, fa1bit_57_s, fa1bit_58_cout, fa1bit_58_s, fa1bit_59_cout, fa1bit_59_s, fa1bit_60_cout,
       fa1bit_60_s, fa1bit_61_cout, fa1bit_61_s, fa1bit_62_cout, fa1bit_62_s, fa1bit_63_cout, fa1bit_63_s,
       fa1bit_64_cout, fa1bit_64_s, fa1bit_65_cout, fa1bit_66_cout, fa1bit_66_s, fa1bit_67_cout, fa1bit_67_s,
       fa1bit_68_cout, fa1bit_68_s, fa1bit_69_cout, fa1bit_69_s, fa1bit_70_cout, fa1bit_70_s, fa1bit_71_cout,
       fa1bit_71_s, fa1bit_72_cout, fa1bit_72_s, fa1bit_73_cout, fa1bit_73_s, fa1bit_74_cout, fa1bit_74_s,
       fa1bit_75_cout, fa1bit_75_s, fa1bit_76_cout, fa1bit_77_cout, fa1bit_77_s, fa1bit_78_cout, fa1bit_78_s,
       fa1bit_79_cout, fa1bit_79_s, fa1bit_80_cout, fa1bit_80_s, fa1bit_81_cout, fa1bit_81_s, fa1bit_82_cout,
       fa1bit_82_s, fa1bit_83_cout, fa1bit_83_s, fa1bit_84_cout, fa1bit_84_s, fa1bit_85_cout, fa1bit_85_s,
       fa1bit_86_cout, fa1bit_86_s, fa1bit_87_cout, fa1bit_87_s, fa1bit_88_cout, fa1bit_89_cout, fa1bit_89_s,
       fa1bit_90_cout, fa1bit_90_s, fa1bit_91_cout, fa1bit_91_s, fa1bit_92_cout, fa1bit_92_s, fa1bit_93_cout,
       fa1bit_93_s, fa1bit_94_cout, fa1bit_94_s, fa1bit_95_cout, fa1bit_95_s, fa1bit_96_cout, fa1bit_96_s,
       fa1bit_97_cout, fa1bit_97_s, fa1bit_98_cout, fa1bit_98_s, fa1bit_99_cout, fa1bit_99_s,
       fa1bit_100_cout, fa1bit_100_s, fa1bit_101_cout, fa1bit_102_cout, fa1bit_102_s, fa1bit_103_cout,
       fa1bit_103_s, fa1bit_104_cout, fa1bit_104_s, fa1bit_105_cout, fa1bit_105_s, fa1bit_106_cout,
       fa1bit_106_s, fa1bit_107_cout, fa1bit_107_s, fa1bit_108_cout, fa1bit_108_s, fa1bit_109_cout,
       fa1bit_109_s, fa1bit_110_cout, fa1bit_110_s, fa1bit_111_cout, fa1bit_111_s, fa1bit_112_cout,
       fa1bit_112_s, fa1bit_113_cout, fa1bit_113_s, fa1bit_114_cout, fa1bit_115_cout, fa1bit_115_s,
       fa1bit_116_cout, fa1bit_116_s, fa1bit_117_cout, fa1bit_117_s, fa1bit_118_cout, fa1bit_118_s,
       fa1bit_119_cout, fa1bit_119_s, fa1bit_120_cout, fa1bit_120_s, fa1bit_121_cout, fa1bit_121_s,
       fa1bit_122_cout, fa1bit_122_s, fa1bit_123_cout, fa1bit_123_s, fa1bit_124_cout, fa1bit_124_s,
       fa1bit_125_cout, fa1bit_125_s, fa1bit_126_cout, fa1bit_126_s, fa1bit_127_cout, fa1bit_127_s,
       fa1bit_128_cout, fa1bit_129_cout, fa1bit_129_s, fa1bit_130_cout, fa1bit_130_s, fa1bit_131_cout,
       fa1bit_131_s, fa1bit_132_cout, fa1bit_132_s, fa1bit_133_cout, fa1bit_133_s, fa1bit_134_cout,
       fa1bit_134_s, fa1bit_135_cout, fa1bit_135_s, fa1bit_136_cout, fa1bit_136_s, fa1bit_137_cout,
       fa1bit_137_s, fa1bit_138_cout, fa1bit_138_s, fa1bit_139_cout, fa1bit_139_s, fa1bit_140_cout,
       fa1bit_140_s, fa1bit_141_cout, fa1bit_141_s, fa1bit_142_cout, fa1bit_143_cout, fa1bit_143_s,
       fa1bit_144_cout, fa1bit_144_s, fa1bit_145_cout, fa1bit_145_s, fa1bit_146_cout, fa1bit_146_s,
       fa1bit_147_cout, fa1bit_147_s, fa1bit_148_cout, fa1bit_148_s, fa1bit_149_cout, fa1bit_149_s,
       fa1bit_150_cout, fa1bit_150_s, fa1bit_151_cout, fa1bit_151_s, fa1bit_152_cout, fa1bit_152_s,
       fa1bit_153_cout, fa1bit_153_s, fa1bit_154_cout, fa1bit_154_s, fa1bit_155_cout, fa1bit_156_cout,
       fa1bit_156_s, fa1bit_157_cout, fa1bit_157_s, fa1bit_158_cout, fa1bit_158_s, fa1bit_159_cout,
       fa1bit_159_s, fa1bit_160_cout, fa1bit_160_s, fa1bit_161_cout, fa1bit_161_s, fa1bit_162_cout,
       fa1bit_162_s, fa1bit_163_cout, fa1bit_163_s, fa1bit_164_cout, fa1bit_164_s, fa1bit_165_cout,
       fa1bit_165_s, fa1bit_166_cout, fa1bit_166_s, fa1bit_167_cout, fa1bit_168_cout, fa1bit_168_s,
       fa1bit_169_cout, fa1bit_169_s, fa1bit_170_cout, fa1bit_170_s, fa1bit_171_cout, fa1bit_171_s,
       fa1bit_172_cout, fa1bit_172_s, fa1bit_173_cout, fa1bit_173_s, fa1bit_174_cout, fa1bit_174_s,
       fa1bit_175_cout, fa1bit_175_s, fa1bit_176_cout, fa1bit_176_s, fa1bit_177_cout, fa1bit_177_s,
       fa1bit_178_cout, fa1bit_179_cout, fa1bit_179_s, fa1bit_180_cout, fa1bit_180_s, fa1bit_181_cout,
       fa1bit_181_s, fa1bit_182_cout, fa1bit_182_s, fa1bit_183_cout, fa1bit_183_s, fa1bit_184_cout,
       fa1bit_184_s, fa1bit_185_cout, fa1bit_185_s, fa1bit_186_cout, fa1bit_186_s, fa1bit_187_cout,
       fa1bit_187_s, fa1bit_188_cout, fa1bit_189_cout, fa1bit_189_s, fa1bit_190_cout, fa1bit_190_s,
       fa1bit_191_cout, fa1bit_191_s, fa1bit_192_cout, fa1bit_192_s, fa1bit_193_cout, fa1bit_193_s,
       fa1bit_194_cout, fa1bit_194_s, fa1bit_195_cout, fa1bit_195_s, fa1bit_196_cout, fa1bit_196_s,
       fa1bit_197_cout, fa1bit_198_cout, fa1bit_198_s, fa1bit_199_cout, fa1bit_199_s, fa1bit_200_cout,
       fa1bit_200_s, fa1bit_201_cout, fa1bit_201_s, fa1bit_202_cout, fa1bit_202_s, fa1bit_203_cout,
       fa1bit_203_s, fa1bit_204_cout, fa1bit_204_s, fa1bit_205_cout, fa1bit_206_cout, fa1bit_206_s,
       fa1bit_207_cout, fa1bit_207_s, fa1bit_208_cout, fa1bit_208_s, fa1bit_209_cout, fa1bit_209_s,
       fa1bit_210_cout, fa1bit_210_s, fa1bit_211_cout, fa1bit_211_s, fa1bit_212_cout, fa1bit_213_cout,
       fa1bit_213_s, fa1bit_214_cout, fa1bit_214_s, fa1bit_215_cout, fa1bit_215_s, fa1bit_216_cout,
       fa1bit_216_s, fa1bit_217_cout, fa1bit_217_s, fa1bit_218_cout, fa1bit_218_s, fa1bit_219_cout,
       fa1bit_220_cout, fa1bit_220_s, fa1bit_221_cout, fa1bit_221_s, fa1bit_222_cout, fa1bit_222_s,
       fa1bit_223_cout, fa1bit_223_s, fa1bit_224_cout, fa1bit_224_s, fa1bit_225_cout, fa1bit_226_cout,
       fa1bit_226_s, fa1bit_227_cout, fa1bit_227_s, fa1bit_228_cout, fa1bit_228_s, fa1bit_229_cout,
       fa1bit_229_s, fa1bit_230_cout, fa1bit_231_cout, fa1bit_231_s, fa1bit_232_cout, fa1bit_232_s,
       fa1bit_233_cout, fa1bit_233_s, fa1bit_234_cout, fa1bit_235_cout, fa1bit_235_s, fa1bit_236_cout,
       fa1bit_236_s, fa1bit_237_cout, fa1bit_238_cout, fa1bit_238_s, fa1bit_239_cout, fa1bit_240_cout;

  FA1Bit fa1bit_1 (.Cin(fa1bit_4_cout), .A(and_1_out), .B(fa1bit_2_cout), .Cout(Product[31]), .S(Product[30]));
  FA1Bit fa1bit_2 (.Cin(fa1bit_6_cout), .A(and_2_out), .B(fa1bit_3_cout), .Cout(fa1bit_2_cout), .S(fa1bit_2_s));
  and and_1 (and_1_out, A[15], B[15]);
  FA1Bit fa1bit_3 (.Cin(fa1bit_9_cout), .A(and_4_out), .B(fa1bit_5_cout), .Cout(fa1bit_3_cout), .S(fa1bit_3_s));
  and and_2 (and_2_out, A[15], B[14]);
  and and_3 (and_3_out, A[14], B[15]);
  FA1Bit fa1bit_4 (.Cin(fa1bit_7_cout), .A(and_3_out), .B(fa1bit_2_s), .Cout(fa1bit_4_cout), .S(Product[29]));
  FA1Bit fa1bit_5 (.Cin(fa1bit_13_cout), .A(and_7_out), .B(fa1bit_8_cout), .Cout(fa1bit_5_cout), .S(fa1bit_5_s));
  and and_4 (and_4_out, A[15], B[13]);
  and and_5 (and_5_out, A[14], B[14]);
  FA1Bit fa1bit_6 (.Cin(fa1bit_10_cout), .A(and_5_out), .B(fa1bit_3_s), .Cout(fa1bit_6_cout), .S(fa1bit_6_s));
  and and_6 (and_6_out, A[13], B[15]);
  FA1Bit fa1bit_7 (.Cin(fa1bit_11_cout), .A(and_6_out), .B(fa1bit_6_s), .Cout(fa1bit_7_cout), .S(Product[28]));
  FA1Bit fa1bit_8 (.Cin(fa1bit_18_cout), .A(and_11_out), .B(fa1bit_12_cout), .Cout(fa1bit_8_cout), .S(fa1bit_8_s));
  and and_7 (and_7_out, A[15], B[12]);
  and and_8 (and_8_out, A[14], B[13]);
  FA1Bit fa1bit_9 (.Cin(fa1bit_14_cout), .A(and_8_out), .B(fa1bit_5_s), .Cout(fa1bit_9_cout), .S(fa1bit_9_s));
  and and_9 (and_9_out, A[13], B[14]);
  FA1Bit fa1bit_10 (.Cin(fa1bit_15_cout), .A(and_9_out), .B(fa1bit_9_s), .Cout(fa1bit_10_cout), .S(fa1bit_10_s));
  and and_10 (and_10_out, A[12], B[15]);
  FA1Bit fa1bit_11 (.Cin(fa1bit_16_cout), .A(and_10_out), .B(fa1bit_10_s), .Cout(fa1bit_11_cout), .S(Product[27]));
  FA1Bit fa1bit_12 (.Cin(fa1bit_24_cout), .A(and_16_out), .B(fa1bit_17_cout), .Cout(fa1bit_12_cout), .S(fa1bit_12_s));
  and and_11 (and_11_out, A[15], B[11]);
  and and_12 (and_12_out, A[14], B[12]);
  FA1Bit fa1bit_13 (.Cin(fa1bit_19_cout), .A(and_12_out), .B(fa1bit_8_s), .Cout(fa1bit_13_cout), .S(fa1bit_13_s));
  and and_13 (and_13_out, A[13], B[13]);
  FA1Bit fa1bit_14 (.Cin(fa1bit_20_cout), .A(and_13_out), .B(fa1bit_13_s), .Cout(fa1bit_14_cout), .S(fa1bit_14_s));
  and and_14 (and_14_out, A[12], B[14]);
  FA1Bit fa1bit_15 (.Cin(fa1bit_21_cout), .A(and_14_out), .B(fa1bit_14_s), .Cout(fa1bit_15_cout), .S(fa1bit_15_s));
  and and_15 (and_15_out, A[11], B[15]);
  FA1Bit fa1bit_16 (.Cin(fa1bit_22_cout), .A(and_15_out), .B(fa1bit_15_s), .Cout(fa1bit_16_cout), .S(Product[26]));
  FA1Bit fa1bit_17 (.Cin(fa1bit_31_cout), .A(and_22_out), .B(fa1bit_23_cout), .Cout(fa1bit_17_cout), .S(fa1bit_17_s));
  and and_16 (and_16_out, A[15], B[10]);
  and and_17 (and_17_out, A[14], B[11]);
  FA1Bit fa1bit_18 (.Cin(fa1bit_25_cout), .A(and_17_out), .B(fa1bit_12_s), .Cout(fa1bit_18_cout), .S(fa1bit_18_s));
  and and_18 (and_18_out, A[13], B[12]);
  FA1Bit fa1bit_19 (.Cin(fa1bit_26_cout), .A(and_18_out), .B(fa1bit_18_s), .Cout(fa1bit_19_cout), .S(fa1bit_19_s));
  and and_19 (and_19_out, A[12], B[13]);
  FA1Bit fa1bit_20 (.Cin(fa1bit_27_cout), .A(and_19_out), .B(fa1bit_19_s), .Cout(fa1bit_20_cout), .S(fa1bit_20_s));
  and and_20 (and_20_out, A[11], B[14]);
  FA1Bit fa1bit_21 (.Cin(fa1bit_28_cout), .A(and_20_out), .B(fa1bit_20_s), .Cout(fa1bit_21_cout), .S(fa1bit_21_s));
  and and_21 (and_21_out, A[10], B[15]);
  FA1Bit fa1bit_22 (.Cin(fa1bit_29_cout), .A(and_21_out), .B(fa1bit_21_s), .Cout(fa1bit_22_cout), .S(Product[25]));
  FA1Bit fa1bit_23 (.Cin(fa1bit_39_cout), .A(and_29_out), .B(fa1bit_30_cout), .Cout(fa1bit_23_cout), .S(fa1bit_23_s));
  and and_22 (and_22_out, A[15], B[9]);
  and and_23 (and_23_out, A[14], B[10]);
  FA1Bit fa1bit_24 (.Cin(fa1bit_32_cout), .A(and_23_out), .B(fa1bit_17_s), .Cout(fa1bit_24_cout), .S(fa1bit_24_s));
  and and_24 (and_24_out, A[13], B[11]);
  FA1Bit fa1bit_25 (.Cin(fa1bit_33_cout), .A(and_24_out), .B(fa1bit_24_s), .Cout(fa1bit_25_cout), .S(fa1bit_25_s));
  and and_25 (and_25_out, A[12], B[12]);
  FA1Bit fa1bit_26 (.Cin(fa1bit_34_cout), .A(and_25_out), .B(fa1bit_25_s), .Cout(fa1bit_26_cout), .S(fa1bit_26_s));
  and and_26 (and_26_out, A[11], B[13]);
  FA1Bit fa1bit_27 (.Cin(fa1bit_35_cout), .A(and_26_out), .B(fa1bit_26_s), .Cout(fa1bit_27_cout), .S(fa1bit_27_s));
  and and_27 (and_27_out, A[10], B[14]);
  FA1Bit fa1bit_28 (.Cin(fa1bit_36_cout), .A(and_27_out), .B(fa1bit_27_s), .Cout(fa1bit_28_cout), .S(fa1bit_28_s));
  and and_28 (and_28_out, A[9], B[15]);
  FA1Bit fa1bit_29 (.Cin(fa1bit_37_cout), .A(and_28_out), .B(fa1bit_28_s), .Cout(fa1bit_29_cout), .S(Product[24]));
  FA1Bit fa1bit_30 (.Cin(fa1bit_48_cout), .A(and_37_out), .B(fa1bit_38_cout), .Cout(fa1bit_30_cout), .S(fa1bit_30_s));
  and and_29 (and_29_out, A[15], B[8]);
  and and_30 (and_30_out, A[14], B[9]);
  FA1Bit fa1bit_31 (.Cin(fa1bit_40_cout), .A(and_30_out), .B(fa1bit_23_s), .Cout(fa1bit_31_cout), .S(fa1bit_31_s));
  and and_31 (and_31_out, A[13], B[10]);
  FA1Bit fa1bit_32 (.Cin(fa1bit_41_cout), .A(and_31_out), .B(fa1bit_31_s), .Cout(fa1bit_32_cout), .S(fa1bit_32_s));
  and and_32 (and_32_out, A[12], B[11]);
  FA1Bit fa1bit_33 (.Cin(fa1bit_42_cout), .A(and_32_out), .B(fa1bit_32_s), .Cout(fa1bit_33_cout), .S(fa1bit_33_s));
  and and_33 (and_33_out, A[11], B[12]);
  FA1Bit fa1bit_34 (.Cin(fa1bit_43_cout), .A(and_33_out), .B(fa1bit_33_s), .Cout(fa1bit_34_cout), .S(fa1bit_34_s));
  and and_34 (and_34_out, A[10], B[13]);
  FA1Bit fa1bit_35 (.Cin(fa1bit_44_cout), .A(and_34_out), .B(fa1bit_34_s), .Cout(fa1bit_35_cout), .S(fa1bit_35_s));
  and and_35 (and_35_out, A[9], B[14]);
  FA1Bit fa1bit_36 (.Cin(fa1bit_45_cout), .A(and_35_out), .B(fa1bit_35_s), .Cout(fa1bit_36_cout), .S(fa1bit_36_s));
  and and_36 (and_36_out, A[8], B[15]);
  FA1Bit fa1bit_37 (.Cin(fa1bit_46_cout), .A(and_36_out), .B(fa1bit_36_s), .Cout(fa1bit_37_cout), .S(Product[23]));
  FA1Bit fa1bit_38 (.Cin(fa1bit_57_cout), .A(and_45_out), .B(fa1bit_47_cout), .Cout(fa1bit_38_cout), .S(fa1bit_38_s));
  and and_37 (and_37_out, A[15], B[7]);
  and and_38 (and_38_out, A[14], B[8]);
  FA1Bit fa1bit_39 (.Cin(fa1bit_49_cout), .A(and_38_out), .B(fa1bit_30_s), .Cout(fa1bit_39_cout), .S(fa1bit_39_s));
  and and_39 (and_39_out, A[13], B[9]);
  FA1Bit fa1bit_40 (.Cin(fa1bit_50_cout), .A(and_39_out), .B(fa1bit_39_s), .Cout(fa1bit_40_cout), .S(fa1bit_40_s));
  and and_40 (and_40_out, A[12], B[10]);
  FA1Bit fa1bit_41 (.Cin(fa1bit_51_cout), .A(and_40_out), .B(fa1bit_40_s), .Cout(fa1bit_41_cout), .S(fa1bit_41_s));
  and and_41 (and_41_out, A[11], B[11]);
  FA1Bit fa1bit_42 (.Cin(fa1bit_52_cout), .A(and_41_out), .B(fa1bit_41_s), .Cout(fa1bit_42_cout), .S(fa1bit_42_s));
  and and_42 (and_42_out, A[10], B[12]);
  FA1Bit fa1bit_43 (.Cin(fa1bit_53_cout), .A(and_42_out), .B(fa1bit_42_s), .Cout(fa1bit_43_cout), .S(fa1bit_43_s));
  and and_43 (and_43_out, A[9], B[13]);
  FA1Bit fa1bit_44 (.Cin(fa1bit_54_cout), .A(and_43_out), .B(fa1bit_43_s), .Cout(fa1bit_44_cout), .S(fa1bit_44_s));
  and and_44 (and_44_out, A[8], B[14]);
  FA1Bit fa1bit_45 (.Cin(fa1bit_55_cout), .A(and_44_out), .B(fa1bit_44_s), .Cout(fa1bit_45_cout), .S(fa1bit_45_s));
  FA1Bit fa1bit_46 (.Cin(fa1bit_65_cout), .A(and_53_out), .B(fa1bit_45_s), .Cout(fa1bit_46_cout), .S(Product[22]));
  FA1Bit fa1bit_47 (.Cin(fa1bit_67_cout), .A(and_54_out), .B(fa1bit_56_cout), .Cout(fa1bit_47_cout), .S(fa1bit_47_s));
  and and_45 (and_45_out, A[15], B[6]);
  and and_46 (and_46_out, A[14], B[7]);
  FA1Bit fa1bit_48 (.Cin(fa1bit_58_cout), .A(and_46_out), .B(fa1bit_38_s), .Cout(fa1bit_48_cout), .S(fa1bit_48_s));
  and and_47 (and_47_out, A[13], B[8]);
  FA1Bit fa1bit_49 (.Cin(fa1bit_59_cout), .A(and_47_out), .B(fa1bit_48_s), .Cout(fa1bit_49_cout), .S(fa1bit_49_s));
  and and_48 (and_48_out, A[12], B[9]);
  FA1Bit fa1bit_50 (.Cin(fa1bit_60_cout), .A(and_48_out), .B(fa1bit_49_s), .Cout(fa1bit_50_cout), .S(fa1bit_50_s));
  and and_49 (and_49_out, A[11], B[10]);
  FA1Bit fa1bit_51 (.Cin(fa1bit_61_cout), .A(and_49_out), .B(fa1bit_50_s), .Cout(fa1bit_51_cout), .S(fa1bit_51_s));
  and and_50 (and_50_out, A[10], B[11]);
  FA1Bit fa1bit_52 (.Cin(fa1bit_62_cout), .A(and_50_out), .B(fa1bit_51_s), .Cout(fa1bit_52_cout), .S(fa1bit_52_s));
  and and_51 (and_51_out, A[9], B[12]);
  FA1Bit fa1bit_53 (.Cin(fa1bit_63_cout), .A(and_51_out), .B(fa1bit_52_s), .Cout(fa1bit_53_cout), .S(fa1bit_53_s));
  and and_52 (and_52_out, A[8], B[13]);
  FA1Bit fa1bit_54 (.Cin(fa1bit_64_cout), .A(and_52_out), .B(fa1bit_53_s), .Cout(fa1bit_54_cout), .S(fa1bit_54_s));
  FA1Bit fa1bit_55 (.Cin(fa1bit_75_cout), .A(and_62_out), .B(fa1bit_54_s), .Cout(fa1bit_55_cout), .S(fa1bit_55_s));
  and and_53 (and_53_out, A[7], B[15]);
  FA1Bit fa1bit_56 (.Cin(fa1bit_78_cout), .A(and_64_out), .B(fa1bit_66_cout), .Cout(fa1bit_56_cout), .S(fa1bit_56_s));
  and and_54 (and_54_out, A[15], B[5]);
  and and_55 (and_55_out, A[14], B[6]);
  FA1Bit fa1bit_57 (.Cin(fa1bit_68_cout), .A(and_55_out), .B(fa1bit_47_s), .Cout(fa1bit_57_cout), .S(fa1bit_57_s));
  and and_56 (and_56_out, A[13], B[7]);
  FA1Bit fa1bit_58 (.Cin(fa1bit_69_cout), .A(and_56_out), .B(fa1bit_57_s), .Cout(fa1bit_58_cout), .S(fa1bit_58_s));
  and and_57 (and_57_out, A[12], B[8]);
  FA1Bit fa1bit_59 (.Cin(fa1bit_70_cout), .A(and_57_out), .B(fa1bit_58_s), .Cout(fa1bit_59_cout), .S(fa1bit_59_s));
  and and_58 (and_58_out, A[11], B[9]);
  FA1Bit fa1bit_60 (.Cin(fa1bit_71_cout), .A(and_58_out), .B(fa1bit_59_s), .Cout(fa1bit_60_cout), .S(fa1bit_60_s));
  and and_59 (and_59_out, A[10], B[10]);
  FA1Bit fa1bit_61 (.Cin(fa1bit_72_cout), .A(and_59_out), .B(fa1bit_60_s), .Cout(fa1bit_61_cout), .S(fa1bit_61_s));
  and and_60 (and_60_out, A[9], B[11]);
  FA1Bit fa1bit_62 (.Cin(fa1bit_73_cout), .A(and_60_out), .B(fa1bit_61_s), .Cout(fa1bit_62_cout), .S(fa1bit_62_s));
  and and_61 (and_61_out, A[8], B[12]);
  FA1Bit fa1bit_63 (.Cin(fa1bit_74_cout), .A(and_61_out), .B(fa1bit_62_s), .Cout(fa1bit_63_cout), .S(fa1bit_63_s));
  FA1Bit fa1bit_64 (.Cin(fa1bit_86_cout), .A(and_72_out), .B(fa1bit_63_s), .Cout(fa1bit_64_cout), .S(fa1bit_64_s));
  and and_62 (and_62_out, A[7], B[14]);
  and and_63 (and_63_out, A[6], B[15]);
  FA1Bit fa1bit_65 (.Cin(fa1bit_76_cout), .A(and_63_out), .B(fa1bit_55_s), .Cout(fa1bit_65_cout), .S(Product[21]));
  FA1Bit fa1bit_66 (.Cin(fa1bit_90_cout), .A(and_75_out), .B(fa1bit_77_cout), .Cout(fa1bit_66_cout), .S(fa1bit_66_s));
  and and_64 (and_64_out, A[15], B[4]);
  and and_65 (and_65_out, A[14], B[5]);
  FA1Bit fa1bit_67 (.Cin(fa1bit_79_cout), .A(and_65_out), .B(fa1bit_56_s), .Cout(fa1bit_67_cout), .S(fa1bit_67_s));
  and and_66 (and_66_out, A[13], B[6]);
  FA1Bit fa1bit_68 (.Cin(fa1bit_80_cout), .A(and_66_out), .B(fa1bit_67_s), .Cout(fa1bit_68_cout), .S(fa1bit_68_s));
  and and_67 (and_67_out, A[12], B[7]);
  FA1Bit fa1bit_69 (.Cin(fa1bit_81_cout), .A(and_67_out), .B(fa1bit_68_s), .Cout(fa1bit_69_cout), .S(fa1bit_69_s));
  and and_68 (and_68_out, A[11], B[8]);
  FA1Bit fa1bit_70 (.Cin(fa1bit_82_cout), .A(and_68_out), .B(fa1bit_69_s), .Cout(fa1bit_70_cout), .S(fa1bit_70_s));
  and and_69 (and_69_out, A[10], B[9]);
  FA1Bit fa1bit_71 (.Cin(fa1bit_83_cout), .A(and_69_out), .B(fa1bit_70_s), .Cout(fa1bit_71_cout), .S(fa1bit_71_s));
  and and_70 (and_70_out, A[9], B[10]);
  FA1Bit fa1bit_72 (.Cin(fa1bit_84_cout), .A(and_70_out), .B(fa1bit_71_s), .Cout(fa1bit_72_cout), .S(fa1bit_72_s));
  and and_71 (and_71_out, A[8], B[11]);
  FA1Bit fa1bit_73 (.Cin(fa1bit_85_cout), .A(and_71_out), .B(fa1bit_72_s), .Cout(fa1bit_73_cout), .S(fa1bit_73_s));
  FA1Bit fa1bit_74 (.Cin(fa1bit_98_cout), .A(and_83_out), .B(fa1bit_73_s), .Cout(fa1bit_74_cout), .S(fa1bit_74_s));
  and and_72 (and_72_out, A[7], B[13]);
  and and_73 (and_73_out, A[6], B[14]);
  FA1Bit fa1bit_75 (.Cin(fa1bit_87_cout), .A(and_73_out), .B(fa1bit_64_s), .Cout(fa1bit_75_cout), .S(fa1bit_75_s));
  and and_74 (and_74_out, A[5], B[15]);
  FA1Bit fa1bit_76 (.Cin(fa1bit_88_cout), .A(and_74_out), .B(fa1bit_75_s), .Cout(fa1bit_76_cout), .S(Product[20]));
  FA1Bit fa1bit_77 (.Cin(fa1bit_102_cout), .A(and_88_out), .B(fa1bit_89_cout), .Cout(fa1bit_77_cout), .S(fa1bit_77_s));
  and and_75 (and_75_out, A[15], B[3]);
  and and_76 (and_76_out, A[14], B[4]);
  FA1Bit fa1bit_78 (.Cin(fa1bit_91_cout), .A(and_76_out), .B(fa1bit_66_s), .Cout(fa1bit_78_cout), .S(fa1bit_78_s));
  and and_77 (and_77_out, A[13], B[5]);
  FA1Bit fa1bit_79 (.Cin(fa1bit_92_cout), .A(and_77_out), .B(fa1bit_78_s), .Cout(fa1bit_79_cout), .S(fa1bit_79_s));
  and and_78 (and_78_out, A[12], B[6]);
  FA1Bit fa1bit_80 (.Cin(fa1bit_93_cout), .A(and_78_out), .B(fa1bit_79_s), .Cout(fa1bit_80_cout), .S(fa1bit_80_s));
  and and_79 (and_79_out, A[11], B[7]);
  FA1Bit fa1bit_81 (.Cin(fa1bit_94_cout), .A(and_79_out), .B(fa1bit_80_s), .Cout(fa1bit_81_cout), .S(fa1bit_81_s));
  and and_80 (and_80_out, A[10], B[8]);
  FA1Bit fa1bit_82 (.Cin(fa1bit_95_cout), .A(and_80_out), .B(fa1bit_81_s), .Cout(fa1bit_82_cout), .S(fa1bit_82_s));
  and and_81 (and_81_out, A[9], B[9]);
  FA1Bit fa1bit_83 (.Cin(fa1bit_96_cout), .A(and_81_out), .B(fa1bit_82_s), .Cout(fa1bit_83_cout), .S(fa1bit_83_s));
  and and_82 (and_82_out, A[8], B[10]);
  FA1Bit fa1bit_84 (.Cin(fa1bit_97_cout), .A(and_82_out), .B(fa1bit_83_s), .Cout(fa1bit_84_cout), .S(fa1bit_84_s));
  FA1Bit fa1bit_85 (.Cin(fa1bit_110_cout), .A(and_96_out), .B(fa1bit_84_s), .Cout(fa1bit_85_cout), .S(fa1bit_85_s));
  and and_83 (and_83_out, A[7], B[12]);
  and and_84 (and_84_out, A[6], B[13]);
  FA1Bit fa1bit_86 (.Cin(fa1bit_99_cout), .A(and_84_out), .B(fa1bit_74_s), .Cout(fa1bit_86_cout), .S(fa1bit_86_s));
  and and_85 (and_85_out, A[5], B[14]);
  FA1Bit fa1bit_87 (.Cin(fa1bit_100_cout), .A(and_85_out), .B(fa1bit_86_s), .Cout(fa1bit_87_cout), .S(fa1bit_87_s));
  and and_86 (and_86_out, A[4], B[15]);
  FA1Bit fa1bit_88 (.Cin(fa1bit_101_cout), .A(and_86_out), .B(fa1bit_87_s), .Cout(fa1bit_88_cout), .S(Product[19]));
  and and_87 (and_87_out, A[15], B[1]);
  FA1Bit fa1bit_89 (.Cin(fa1bit_115_cout), .A(1'b0), .B(and_87_out), .Cout(fa1bit_89_cout), .S(fa1bit_89_s));
  and and_88 (and_88_out, A[15], B[2]);
  and and_89 (and_89_out, A[14], B[3]);
  FA1Bit fa1bit_90 (.Cin(fa1bit_103_cout), .A(and_89_out), .B(fa1bit_77_s), .Cout(fa1bit_90_cout), .S(fa1bit_90_s));
  and and_90 (and_90_out, A[13], B[4]);
  FA1Bit fa1bit_91 (.Cin(fa1bit_104_cout), .A(and_90_out), .B(fa1bit_90_s), .Cout(fa1bit_91_cout), .S(fa1bit_91_s));
  and and_91 (and_91_out, A[12], B[5]);
  FA1Bit fa1bit_92 (.Cin(fa1bit_105_cout), .A(and_91_out), .B(fa1bit_91_s), .Cout(fa1bit_92_cout), .S(fa1bit_92_s));
  and and_92 (and_92_out, A[11], B[6]);
  FA1Bit fa1bit_93 (.Cin(fa1bit_106_cout), .A(and_92_out), .B(fa1bit_92_s), .Cout(fa1bit_93_cout), .S(fa1bit_93_s));
  and and_93 (and_93_out, A[10], B[7]);
  FA1Bit fa1bit_94 (.Cin(fa1bit_107_cout), .A(and_93_out), .B(fa1bit_93_s), .Cout(fa1bit_94_cout), .S(fa1bit_94_s));
  and and_94 (and_94_out, A[9], B[8]);
  FA1Bit fa1bit_95 (.Cin(fa1bit_108_cout), .A(and_94_out), .B(fa1bit_94_s), .Cout(fa1bit_95_cout), .S(fa1bit_95_s));
  and and_95 (and_95_out, A[8], B[9]);
  FA1Bit fa1bit_96 (.Cin(fa1bit_109_cout), .A(and_95_out), .B(fa1bit_95_s), .Cout(fa1bit_96_cout), .S(fa1bit_96_s));
  FA1Bit fa1bit_97 (.Cin(fa1bit_123_cout), .A(and_109_out), .B(fa1bit_96_s), .Cout(fa1bit_97_cout), .S(fa1bit_97_s));
  and and_96 (and_96_out, A[7], B[11]);
  and and_97 (and_97_out, A[6], B[12]);
  FA1Bit fa1bit_98 (.Cin(fa1bit_111_cout), .A(and_97_out), .B(fa1bit_85_s), .Cout(fa1bit_98_cout), .S(fa1bit_98_s));
  and and_98 (and_98_out, A[5], B[13]);
  FA1Bit fa1bit_99 (.Cin(fa1bit_112_cout), .A(and_98_out), .B(fa1bit_98_s), .Cout(fa1bit_99_cout), .S(fa1bit_99_s));
  and and_99 (and_99_out, A[4], B[14]);
  FA1Bit fa1bit_100 (.Cin(fa1bit_113_cout), .A(and_99_out), .B(fa1bit_99_s), .Cout(fa1bit_100_cout), .S(fa1bit_100_s));
  and and_100 (and_100_out, A[3], B[15]);
  FA1Bit fa1bit_101 (.Cin(fa1bit_114_cout), .A(and_100_out), .B(fa1bit_100_s), .Cout(fa1bit_101_cout), .S(Product[18]));
  and and_101 (and_101_out, A[14], B[1]);
  and and_102 (and_102_out, A[14], B[2]);
  FA1Bit fa1bit_102 (.Cin(fa1bit_116_cout), .A(and_102_out), .B(fa1bit_89_s), .Cout(fa1bit_102_cout), .S(fa1bit_102_s));
  and and_103 (and_103_out, A[13], B[3]);
  FA1Bit fa1bit_103 (
    .Cin(fa1bit_117_cout), .A(and_103_out), .B(fa1bit_102_s), .Cout(fa1bit_103_cout), .S(fa1bit_103_s));
  and and_104 (and_104_out, A[12], B[4]);
  FA1Bit fa1bit_104 (
    .Cin(fa1bit_118_cout), .A(and_104_out), .B(fa1bit_103_s), .Cout(fa1bit_104_cout), .S(fa1bit_104_s));
  and and_105 (and_105_out, A[11], B[5]);
  FA1Bit fa1bit_105 (
    .Cin(fa1bit_119_cout), .A(and_105_out), .B(fa1bit_104_s), .Cout(fa1bit_105_cout), .S(fa1bit_105_s));
  and and_106 (and_106_out, A[10], B[6]);
  FA1Bit fa1bit_106 (
    .Cin(fa1bit_120_cout), .A(and_106_out), .B(fa1bit_105_s), .Cout(fa1bit_106_cout), .S(fa1bit_106_s));
  and and_107 (and_107_out, A[9], B[7]);
  FA1Bit fa1bit_107 (
    .Cin(fa1bit_121_cout), .A(and_107_out), .B(fa1bit_106_s), .Cout(fa1bit_107_cout), .S(fa1bit_107_s));
  and and_108 (and_108_out, A[8], B[8]);
  FA1Bit fa1bit_108 (
    .Cin(fa1bit_122_cout), .A(and_108_out), .B(fa1bit_107_s), .Cout(fa1bit_108_cout), .S(fa1bit_108_s));
  FA1Bit fa1bit_109 (
    .Cin(fa1bit_136_cout), .A(and_122_out), .B(fa1bit_108_s), .Cout(fa1bit_109_cout), .S(fa1bit_109_s));
  and and_109 (and_109_out, A[7], B[10]);
  and and_110 (and_110_out, A[6], B[11]);
  FA1Bit fa1bit_110 (.Cin(fa1bit_124_cout), .A(and_110_out), .B(fa1bit_97_s), .Cout(fa1bit_110_cout), .S(fa1bit_110_s));
  and and_111 (and_111_out, A[5], B[12]);
  FA1Bit fa1bit_111 (
    .Cin(fa1bit_125_cout), .A(and_111_out), .B(fa1bit_110_s), .Cout(fa1bit_111_cout), .S(fa1bit_111_s));
  and and_112 (and_112_out, A[4], B[13]);
  FA1Bit fa1bit_112 (
    .Cin(fa1bit_126_cout), .A(and_112_out), .B(fa1bit_111_s), .Cout(fa1bit_112_cout), .S(fa1bit_112_s));
  and and_113 (and_113_out, A[3], B[14]);
  FA1Bit fa1bit_113 (
    .Cin(fa1bit_127_cout), .A(and_113_out), .B(fa1bit_112_s), .Cout(fa1bit_113_cout), .S(fa1bit_113_s));
  and and_114 (and_114_out, A[2], B[15]);
  FA1Bit fa1bit_114 (.Cin(fa1bit_128_cout), .A(and_114_out), .B(fa1bit_113_s), .Cout(fa1bit_114_cout), .S(Product[17]));
  and and_115 (and_115_out, A[15], B[0]);
  FA1Bit fa1bit_115 (.Cin(fa1bit_129_cout), .A(and_115_out), .B(and_101_out), .Cout(fa1bit_115_cout), .S(fa1bit_115_s));
  and and_116 (and_116_out, A[13], B[2]);
  FA1Bit fa1bit_116 (
    .Cin(fa1bit_130_cout), .A(and_116_out), .B(fa1bit_115_s), .Cout(fa1bit_116_cout), .S(fa1bit_116_s));
  and and_117 (and_117_out, A[12], B[3]);
  FA1Bit fa1bit_117 (
    .Cin(fa1bit_131_cout), .A(and_117_out), .B(fa1bit_116_s), .Cout(fa1bit_117_cout), .S(fa1bit_117_s));
  and and_118 (and_118_out, A[11], B[4]);
  FA1Bit fa1bit_118 (
    .Cin(fa1bit_132_cout), .A(and_118_out), .B(fa1bit_117_s), .Cout(fa1bit_118_cout), .S(fa1bit_118_s));
  and and_119 (and_119_out, A[10], B[5]);
  FA1Bit fa1bit_119 (
    .Cin(fa1bit_133_cout), .A(and_119_out), .B(fa1bit_118_s), .Cout(fa1bit_119_cout), .S(fa1bit_119_s));
  and and_120 (and_120_out, A[9], B[6]);
  FA1Bit fa1bit_120 (
    .Cin(fa1bit_134_cout), .A(and_120_out), .B(fa1bit_119_s), .Cout(fa1bit_120_cout), .S(fa1bit_120_s));
  and and_121 (and_121_out, A[8], B[7]);
  FA1Bit fa1bit_121 (
    .Cin(fa1bit_135_cout), .A(and_121_out), .B(fa1bit_120_s), .Cout(fa1bit_121_cout), .S(fa1bit_121_s));
  FA1Bit fa1bit_122 (
    .Cin(fa1bit_149_cout), .A(and_136_out), .B(fa1bit_121_s), .Cout(fa1bit_122_cout), .S(fa1bit_122_s));
  and and_122 (and_122_out, A[7], B[9]);
  and and_123 (and_123_out, A[6], B[10]);
  FA1Bit fa1bit_123 (
    .Cin(fa1bit_137_cout), .A(and_123_out), .B(fa1bit_109_s), .Cout(fa1bit_123_cout), .S(fa1bit_123_s));
  and and_124 (and_124_out, A[5], B[11]);
  FA1Bit fa1bit_124 (
    .Cin(fa1bit_138_cout), .A(and_124_out), .B(fa1bit_123_s), .Cout(fa1bit_124_cout), .S(fa1bit_124_s));
  and and_125 (and_125_out, A[4], B[12]);
  FA1Bit fa1bit_125 (
    .Cin(fa1bit_139_cout), .A(and_125_out), .B(fa1bit_124_s), .Cout(fa1bit_125_cout), .S(fa1bit_125_s));
  and and_126 (and_126_out, A[3], B[13]);
  FA1Bit fa1bit_126 (
    .Cin(fa1bit_140_cout), .A(and_126_out), .B(fa1bit_125_s), .Cout(fa1bit_126_cout), .S(fa1bit_126_s));
  and and_127 (and_127_out, A[2], B[14]);
  FA1Bit fa1bit_127 (
    .Cin(fa1bit_141_cout), .A(and_127_out), .B(fa1bit_126_s), .Cout(fa1bit_127_cout), .S(fa1bit_127_s));
  and and_128 (and_128_out, A[1], B[15]);
  FA1Bit fa1bit_128 (.Cin(fa1bit_142_cout), .A(and_128_out), .B(fa1bit_127_s), .Cout(fa1bit_128_cout), .S(Product[16]));
  and and_129 (and_129_out, A[14], B[0]);
  and and_130 (and_130_out, A[13], B[1]);
  FA1Bit fa1bit_129 (.Cin(fa1bit_143_cout), .A(and_129_out), .B(and_130_out), .Cout(fa1bit_129_cout), .S(fa1bit_129_s));
  and and_131 (and_131_out, A[12], B[2]);
  FA1Bit fa1bit_130 (
    .Cin(fa1bit_144_cout), .A(and_131_out), .B(fa1bit_129_s), .Cout(fa1bit_130_cout), .S(fa1bit_130_s));
  and and_132 (and_132_out, A[11], B[3]);
  FA1Bit fa1bit_131 (
    .Cin(fa1bit_145_cout), .A(and_132_out), .B(fa1bit_130_s), .Cout(fa1bit_131_cout), .S(fa1bit_131_s));
  and and_133 (and_133_out, A[10], B[4]);
  FA1Bit fa1bit_132 (
    .Cin(fa1bit_146_cout), .A(and_133_out), .B(fa1bit_131_s), .Cout(fa1bit_132_cout), .S(fa1bit_132_s));
  and and_134 (and_134_out, A[9], B[5]);
  FA1Bit fa1bit_133 (
    .Cin(fa1bit_147_cout), .A(and_134_out), .B(fa1bit_132_s), .Cout(fa1bit_133_cout), .S(fa1bit_133_s));
  and and_135 (and_135_out, A[8], B[6]);
  FA1Bit fa1bit_134 (
    .Cin(fa1bit_148_cout), .A(and_135_out), .B(fa1bit_133_s), .Cout(fa1bit_134_cout), .S(fa1bit_134_s));
  FA1Bit fa1bit_135 (
    .Cin(fa1bit_161_cout), .A(and_150_out), .B(fa1bit_134_s), .Cout(fa1bit_135_cout), .S(fa1bit_135_s));
  and and_136 (and_136_out, A[7], B[8]);
  and and_137 (and_137_out, A[6], B[9]);
  FA1Bit fa1bit_136 (
    .Cin(fa1bit_150_cout), .A(and_137_out), .B(fa1bit_122_s), .Cout(fa1bit_136_cout), .S(fa1bit_136_s));
  and and_138 (and_138_out, A[5], B[10]);
  FA1Bit fa1bit_137 (
    .Cin(fa1bit_151_cout), .A(and_138_out), .B(fa1bit_136_s), .Cout(fa1bit_137_cout), .S(fa1bit_137_s));
  and and_139 (and_139_out, A[4], B[11]);
  FA1Bit fa1bit_138 (
    .Cin(fa1bit_152_cout), .A(and_139_out), .B(fa1bit_137_s), .Cout(fa1bit_138_cout), .S(fa1bit_138_s));
  and and_140 (and_140_out, A[3], B[12]);
  FA1Bit fa1bit_139 (
    .Cin(fa1bit_153_cout), .A(and_140_out), .B(fa1bit_138_s), .Cout(fa1bit_139_cout), .S(fa1bit_139_s));
  and and_141 (and_141_out, A[2], B[13]);
  FA1Bit fa1bit_140 (
    .Cin(fa1bit_154_cout), .A(and_141_out), .B(fa1bit_139_s), .Cout(fa1bit_140_cout), .S(fa1bit_140_s));
  and and_142 (and_142_out, A[1], B[14]);
  FA1Bit fa1bit_141 (
    .Cin(fa1bit_155_cout), .A(and_142_out), .B(fa1bit_140_s), .Cout(fa1bit_141_cout), .S(fa1bit_141_s));
  and and_143 (and_143_out, A[0], B[15]);
  FA1Bit fa1bit_142 (.Cin(1'b0), .A(and_143_out), .B(fa1bit_141_s), .Cout(fa1bit_142_cout), .S(Product[15]));
  and and_144 (and_144_out, A[13], B[0]);
  and and_145 (and_145_out, A[12], B[1]);
  FA1Bit fa1bit_143 (.Cin(fa1bit_156_cout), .A(and_144_out), .B(and_145_out), .Cout(fa1bit_143_cout), .S(fa1bit_143_s));
  and and_146 (and_146_out, A[11], B[2]);
  FA1Bit fa1bit_144 (
    .Cin(fa1bit_157_cout), .A(and_146_out), .B(fa1bit_143_s), .Cout(fa1bit_144_cout), .S(fa1bit_144_s));
  and and_147 (and_147_out, A[10], B[3]);
  FA1Bit fa1bit_145 (
    .Cin(fa1bit_158_cout), .A(and_147_out), .B(fa1bit_144_s), .Cout(fa1bit_145_cout), .S(fa1bit_145_s));
  and and_148 (and_148_out, A[9], B[4]);
  FA1Bit fa1bit_146 (
    .Cin(fa1bit_159_cout), .A(and_148_out), .B(fa1bit_145_s), .Cout(fa1bit_146_cout), .S(fa1bit_146_s));
  and and_149 (and_149_out, A[8], B[5]);
  FA1Bit fa1bit_147 (
    .Cin(fa1bit_160_cout), .A(and_149_out), .B(fa1bit_146_s), .Cout(fa1bit_147_cout), .S(fa1bit_147_s));
  FA1Bit fa1bit_148 (
    .Cin(fa1bit_172_cout), .A(and_163_out), .B(fa1bit_147_s), .Cout(fa1bit_148_cout), .S(fa1bit_148_s));
  and and_150 (and_150_out, A[7], B[7]);
  and and_151 (and_151_out, A[6], B[8]);
  FA1Bit fa1bit_149 (
    .Cin(fa1bit_162_cout), .A(and_151_out), .B(fa1bit_135_s), .Cout(fa1bit_149_cout), .S(fa1bit_149_s));
  and and_152 (and_152_out, A[5], B[9]);
  FA1Bit fa1bit_150 (
    .Cin(fa1bit_163_cout), .A(and_152_out), .B(fa1bit_149_s), .Cout(fa1bit_150_cout), .S(fa1bit_150_s));
  and and_153 (and_153_out, A[4], B[10]);
  FA1Bit fa1bit_151 (
    .Cin(fa1bit_164_cout), .A(and_153_out), .B(fa1bit_150_s), .Cout(fa1bit_151_cout), .S(fa1bit_151_s));
  and and_154 (and_154_out, A[3], B[11]);
  FA1Bit fa1bit_152 (
    .Cin(fa1bit_165_cout), .A(and_154_out), .B(fa1bit_151_s), .Cout(fa1bit_152_cout), .S(fa1bit_152_s));
  and and_155 (and_155_out, A[2], B[12]);
  FA1Bit fa1bit_153 (
    .Cin(fa1bit_166_cout), .A(and_155_out), .B(fa1bit_152_s), .Cout(fa1bit_153_cout), .S(fa1bit_153_s));
  and and_156 (and_156_out, A[1], B[13]);
  FA1Bit fa1bit_154 (
    .Cin(fa1bit_167_cout), .A(and_156_out), .B(fa1bit_153_s), .Cout(fa1bit_154_cout), .S(fa1bit_154_s));
  and and_157 (and_157_out, A[0], B[14]);
  FA1Bit fa1bit_155 (.Cin(1'b0), .A(and_157_out), .B(fa1bit_154_s), .Cout(fa1bit_155_cout), .S(Product[14]));
  and and_158 (and_158_out, A[12], B[0]);
  and and_159 (and_159_out, A[11], B[1]);
  FA1Bit fa1bit_156 (.Cin(fa1bit_168_cout), .A(and_158_out), .B(and_159_out), .Cout(fa1bit_156_cout), .S(fa1bit_156_s));
  and and_160 (and_160_out, A[10], B[2]);
  FA1Bit fa1bit_157 (
    .Cin(fa1bit_169_cout), .A(and_160_out), .B(fa1bit_156_s), .Cout(fa1bit_157_cout), .S(fa1bit_157_s));
  and and_161 (and_161_out, A[9], B[3]);
  FA1Bit fa1bit_158 (
    .Cin(fa1bit_170_cout), .A(and_161_out), .B(fa1bit_157_s), .Cout(fa1bit_158_cout), .S(fa1bit_158_s));
  and and_162 (and_162_out, A[8], B[4]);
  FA1Bit fa1bit_159 (
    .Cin(fa1bit_171_cout), .A(and_162_out), .B(fa1bit_158_s), .Cout(fa1bit_159_cout), .S(fa1bit_159_s));
  FA1Bit fa1bit_160 (
    .Cin(fa1bit_182_cout), .A(and_175_out), .B(fa1bit_159_s), .Cout(fa1bit_160_cout), .S(fa1bit_160_s));
  and and_163 (and_163_out, A[7], B[6]);
  and and_164 (and_164_out, A[6], B[7]);
  FA1Bit fa1bit_161 (
    .Cin(fa1bit_173_cout), .A(and_164_out), .B(fa1bit_148_s), .Cout(fa1bit_161_cout), .S(fa1bit_161_s));
  and and_165 (and_165_out, A[5], B[8]);
  FA1Bit fa1bit_162 (
    .Cin(fa1bit_174_cout), .A(and_165_out), .B(fa1bit_161_s), .Cout(fa1bit_162_cout), .S(fa1bit_162_s));
  and and_166 (and_166_out, A[4], B[9]);
  FA1Bit fa1bit_163 (
    .Cin(fa1bit_175_cout), .A(and_166_out), .B(fa1bit_162_s), .Cout(fa1bit_163_cout), .S(fa1bit_163_s));
  and and_167 (and_167_out, A[3], B[10]);
  FA1Bit fa1bit_164 (
    .Cin(fa1bit_176_cout), .A(and_167_out), .B(fa1bit_163_s), .Cout(fa1bit_164_cout), .S(fa1bit_164_s));
  and and_168 (and_168_out, A[2], B[11]);
  FA1Bit fa1bit_165 (
    .Cin(fa1bit_177_cout), .A(and_168_out), .B(fa1bit_164_s), .Cout(fa1bit_165_cout), .S(fa1bit_165_s));
  and and_169 (and_169_out, A[1], B[12]);
  FA1Bit fa1bit_166 (
    .Cin(fa1bit_178_cout), .A(and_169_out), .B(fa1bit_165_s), .Cout(fa1bit_166_cout), .S(fa1bit_166_s));
  and and_170 (and_170_out, A[0], B[13]);
  FA1Bit fa1bit_167 (.Cin(1'b0), .A(and_170_out), .B(fa1bit_166_s), .Cout(fa1bit_167_cout), .S(Product[13]));
  and and_171 (and_171_out, A[11], B[0]);
  and and_172 (and_172_out, A[10], B[1]);
  FA1Bit fa1bit_168 (.Cin(fa1bit_179_cout), .A(and_171_out), .B(and_172_out), .Cout(fa1bit_168_cout), .S(fa1bit_168_s));
  and and_173 (and_173_out, A[9], B[2]);
  FA1Bit fa1bit_169 (
    .Cin(fa1bit_180_cout), .A(and_173_out), .B(fa1bit_168_s), .Cout(fa1bit_169_cout), .S(fa1bit_169_s));
  and and_174 (and_174_out, A[8], B[3]);
  FA1Bit fa1bit_170 (
    .Cin(fa1bit_181_cout), .A(and_174_out), .B(fa1bit_169_s), .Cout(fa1bit_170_cout), .S(fa1bit_170_s));
  FA1Bit fa1bit_171 (
    .Cin(fa1bit_191_cout), .A(and_186_out), .B(fa1bit_170_s), .Cout(fa1bit_171_cout), .S(fa1bit_171_s));
  and and_175 (and_175_out, A[7], B[5]);
  and and_176 (and_176_out, A[6], B[6]);
  FA1Bit fa1bit_172 (
    .Cin(fa1bit_183_cout), .A(and_176_out), .B(fa1bit_160_s), .Cout(fa1bit_172_cout), .S(fa1bit_172_s));
  and and_177 (and_177_out, A[5], B[7]);
  FA1Bit fa1bit_173 (
    .Cin(fa1bit_184_cout), .A(and_177_out), .B(fa1bit_172_s), .Cout(fa1bit_173_cout), .S(fa1bit_173_s));
  and and_178 (and_178_out, A[4], B[8]);
  FA1Bit fa1bit_174 (
    .Cin(fa1bit_185_cout), .A(and_178_out), .B(fa1bit_173_s), .Cout(fa1bit_174_cout), .S(fa1bit_174_s));
  and and_179 (and_179_out, A[3], B[9]);
  FA1Bit fa1bit_175 (
    .Cin(fa1bit_186_cout), .A(and_179_out), .B(fa1bit_174_s), .Cout(fa1bit_175_cout), .S(fa1bit_175_s));
  and and_180 (and_180_out, A[2], B[10]);
  FA1Bit fa1bit_176 (
    .Cin(fa1bit_187_cout), .A(and_180_out), .B(fa1bit_175_s), .Cout(fa1bit_176_cout), .S(fa1bit_176_s));
  and and_181 (and_181_out, A[1], B[11]);
  FA1Bit fa1bit_177 (
    .Cin(fa1bit_188_cout), .A(and_181_out), .B(fa1bit_176_s), .Cout(fa1bit_177_cout), .S(fa1bit_177_s));
  and and_182 (and_182_out, A[0], B[12]);
  FA1Bit fa1bit_178 (.Cin(1'b0), .A(and_182_out), .B(fa1bit_177_s), .Cout(fa1bit_178_cout), .S(Product[12]));
  and and_183 (and_183_out, A[10], B[0]);
  and and_184 (and_184_out, A[9], B[1]);
  FA1Bit fa1bit_179 (.Cin(fa1bit_189_cout), .A(and_183_out), .B(and_184_out), .Cout(fa1bit_179_cout), .S(fa1bit_179_s));
  and and_185 (and_185_out, A[8], B[2]);
  FA1Bit fa1bit_180 (
    .Cin(fa1bit_190_cout), .A(and_185_out), .B(fa1bit_179_s), .Cout(fa1bit_180_cout), .S(fa1bit_180_s));
  FA1Bit fa1bit_181 (
    .Cin(fa1bit_199_cout), .A(and_196_out), .B(fa1bit_180_s), .Cout(fa1bit_181_cout), .S(fa1bit_181_s));
  and and_186 (and_186_out, A[7], B[4]);
  and and_187 (and_187_out, A[6], B[5]);
  FA1Bit fa1bit_182 (
    .Cin(fa1bit_192_cout), .A(and_187_out), .B(fa1bit_171_s), .Cout(fa1bit_182_cout), .S(fa1bit_182_s));
  and and_188 (and_188_out, A[5], B[6]);
  FA1Bit fa1bit_183 (
    .Cin(fa1bit_193_cout), .A(and_188_out), .B(fa1bit_182_s), .Cout(fa1bit_183_cout), .S(fa1bit_183_s));
  and and_189 (and_189_out, A[4], B[7]);
  FA1Bit fa1bit_184 (
    .Cin(fa1bit_194_cout), .A(and_189_out), .B(fa1bit_183_s), .Cout(fa1bit_184_cout), .S(fa1bit_184_s));
  and and_190 (and_190_out, A[3], B[8]);
  FA1Bit fa1bit_185 (
    .Cin(fa1bit_195_cout), .A(and_190_out), .B(fa1bit_184_s), .Cout(fa1bit_185_cout), .S(fa1bit_185_s));
  and and_191 (and_191_out, A[2], B[9]);
  FA1Bit fa1bit_186 (
    .Cin(fa1bit_196_cout), .A(and_191_out), .B(fa1bit_185_s), .Cout(fa1bit_186_cout), .S(fa1bit_186_s));
  and and_192 (and_192_out, A[1], B[10]);
  FA1Bit fa1bit_187 (
    .Cin(fa1bit_197_cout), .A(and_192_out), .B(fa1bit_186_s), .Cout(fa1bit_187_cout), .S(fa1bit_187_s));
  and and_193 (and_193_out, A[0], B[11]);
  FA1Bit fa1bit_188 (.Cin(1'b0), .A(and_193_out), .B(fa1bit_187_s), .Cout(fa1bit_188_cout), .S(Product[11]));
  and and_194 (and_194_out, A[9], B[0]);
  and and_195 (and_195_out, A[8], B[1]);
  FA1Bit fa1bit_189 (.Cin(fa1bit_198_cout), .A(and_194_out), .B(and_195_out), .Cout(fa1bit_189_cout), .S(fa1bit_189_s));
  FA1Bit fa1bit_190 (
    .Cin(fa1bit_206_cout), .A(and_205_out), .B(fa1bit_189_s), .Cout(fa1bit_190_cout), .S(fa1bit_190_s));
  and and_196 (and_196_out, A[7], B[3]);
  and and_197 (and_197_out, A[6], B[4]);
  FA1Bit fa1bit_191 (
    .Cin(fa1bit_200_cout), .A(and_197_out), .B(fa1bit_181_s), .Cout(fa1bit_191_cout), .S(fa1bit_191_s));
  and and_198 (and_198_out, A[5], B[5]);
  FA1Bit fa1bit_192 (
    .Cin(fa1bit_201_cout), .A(and_198_out), .B(fa1bit_191_s), .Cout(fa1bit_192_cout), .S(fa1bit_192_s));
  and and_199 (and_199_out, A[4], B[6]);
  FA1Bit fa1bit_193 (
    .Cin(fa1bit_202_cout), .A(and_199_out), .B(fa1bit_192_s), .Cout(fa1bit_193_cout), .S(fa1bit_193_s));
  and and_200 (and_200_out, A[3], B[7]);
  FA1Bit fa1bit_194 (
    .Cin(fa1bit_203_cout), .A(and_200_out), .B(fa1bit_193_s), .Cout(fa1bit_194_cout), .S(fa1bit_194_s));
  and and_201 (and_201_out, A[2], B[8]);
  FA1Bit fa1bit_195 (
    .Cin(fa1bit_204_cout), .A(and_201_out), .B(fa1bit_194_s), .Cout(fa1bit_195_cout), .S(fa1bit_195_s));
  and and_202 (and_202_out, A[1], B[9]);
  FA1Bit fa1bit_196 (
    .Cin(fa1bit_205_cout), .A(and_202_out), .B(fa1bit_195_s), .Cout(fa1bit_196_cout), .S(fa1bit_196_s));
  and and_203 (and_203_out, A[0], B[10]);
  FA1Bit fa1bit_197 (.Cin(1'b0), .A(and_203_out), .B(fa1bit_196_s), .Cout(fa1bit_197_cout), .S(Product[10]));
  and and_204 (and_204_out, A[7], B[1]);
  FA1Bit fa1bit_198 (.Cin(fa1bit_213_cout), .A(and_213_out), .B(and_204_out), .Cout(fa1bit_198_cout), .S(fa1bit_198_s));
  and and_205 (and_205_out, A[7], B[2]);
  and and_206 (and_206_out, A[6], B[3]);
  FA1Bit fa1bit_199 (
    .Cin(fa1bit_207_cout), .A(and_206_out), .B(fa1bit_190_s), .Cout(fa1bit_199_cout), .S(fa1bit_199_s));
  and and_207 (and_207_out, A[5], B[4]);
  FA1Bit fa1bit_200 (
    .Cin(fa1bit_208_cout), .A(and_207_out), .B(fa1bit_199_s), .Cout(fa1bit_200_cout), .S(fa1bit_200_s));
  and and_208 (and_208_out, A[4], B[5]);
  FA1Bit fa1bit_201 (
    .Cin(fa1bit_209_cout), .A(and_208_out), .B(fa1bit_200_s), .Cout(fa1bit_201_cout), .S(fa1bit_201_s));
  and and_209 (and_209_out, A[3], B[6]);
  FA1Bit fa1bit_202 (
    .Cin(fa1bit_210_cout), .A(and_209_out), .B(fa1bit_201_s), .Cout(fa1bit_202_cout), .S(fa1bit_202_s));
  and and_210 (and_210_out, A[2], B[7]);
  FA1Bit fa1bit_203 (
    .Cin(fa1bit_211_cout), .A(and_210_out), .B(fa1bit_202_s), .Cout(fa1bit_203_cout), .S(fa1bit_203_s));
  and and_211 (and_211_out, A[1], B[8]);
  FA1Bit fa1bit_204 (
    .Cin(fa1bit_212_cout), .A(and_211_out), .B(fa1bit_203_s), .Cout(fa1bit_204_cout), .S(fa1bit_204_s));
  and and_212 (and_212_out, A[0], B[9]);
  FA1Bit fa1bit_205 (.Cin(1'b0), .A(and_212_out), .B(fa1bit_204_s), .Cout(fa1bit_205_cout), .S(Product[9]));
  and and_213 (and_213_out, A[8], B[0]);
  and and_214 (and_214_out, A[6], B[1]);
  and and_215 (and_215_out, A[6], B[2]);
  FA1Bit fa1bit_206 (
    .Cin(fa1bit_214_cout), .A(and_215_out), .B(fa1bit_198_s), .Cout(fa1bit_206_cout), .S(fa1bit_206_s));
  and and_216 (and_216_out, A[5], B[3]);
  FA1Bit fa1bit_207 (
    .Cin(fa1bit_215_cout), .A(and_216_out), .B(fa1bit_206_s), .Cout(fa1bit_207_cout), .S(fa1bit_207_s));
  and and_217 (and_217_out, A[4], B[4]);
  FA1Bit fa1bit_208 (
    .Cin(fa1bit_216_cout), .A(and_217_out), .B(fa1bit_207_s), .Cout(fa1bit_208_cout), .S(fa1bit_208_s));
  and and_218 (and_218_out, A[3], B[5]);
  FA1Bit fa1bit_209 (
    .Cin(fa1bit_217_cout), .A(and_218_out), .B(fa1bit_208_s), .Cout(fa1bit_209_cout), .S(fa1bit_209_s));
  and and_219 (and_219_out, A[2], B[6]);
  FA1Bit fa1bit_210 (
    .Cin(fa1bit_218_cout), .A(and_219_out), .B(fa1bit_209_s), .Cout(fa1bit_210_cout), .S(fa1bit_210_s));
  and and_220 (and_220_out, A[1], B[7]);
  FA1Bit fa1bit_211 (
    .Cin(fa1bit_219_cout), .A(and_220_out), .B(fa1bit_210_s), .Cout(fa1bit_211_cout), .S(fa1bit_211_s));
  and and_221 (and_221_out, A[0], B[8]);
  FA1Bit fa1bit_212 (.Cin(1'b0), .A(and_221_out), .B(fa1bit_211_s), .Cout(fa1bit_212_cout), .S(Product[8]));
  and and_222 (and_222_out, A[7], B[0]);
  FA1Bit fa1bit_213 (.Cin(fa1bit_220_cout), .A(and_222_out), .B(and_214_out), .Cout(fa1bit_213_cout), .S(fa1bit_213_s));
  and and_223 (and_223_out, A[5], B[2]);
  FA1Bit fa1bit_214 (
    .Cin(fa1bit_221_cout), .A(and_223_out), .B(fa1bit_213_s), .Cout(fa1bit_214_cout), .S(fa1bit_214_s));
  and and_224 (and_224_out, A[4], B[3]);
  FA1Bit fa1bit_215 (
    .Cin(fa1bit_222_cout), .A(and_224_out), .B(fa1bit_214_s), .Cout(fa1bit_215_cout), .S(fa1bit_215_s));
  and and_225 (and_225_out, A[3], B[4]);
  FA1Bit fa1bit_216 (
    .Cin(fa1bit_223_cout), .A(and_225_out), .B(fa1bit_215_s), .Cout(fa1bit_216_cout), .S(fa1bit_216_s));
  and and_226 (and_226_out, A[2], B[5]);
  FA1Bit fa1bit_217 (
    .Cin(fa1bit_224_cout), .A(and_226_out), .B(fa1bit_216_s), .Cout(fa1bit_217_cout), .S(fa1bit_217_s));
  and and_227 (and_227_out, A[1], B[6]);
  FA1Bit fa1bit_218 (
    .Cin(fa1bit_225_cout), .A(and_227_out), .B(fa1bit_217_s), .Cout(fa1bit_218_cout), .S(fa1bit_218_s));
  and and_228 (and_228_out, A[0], B[7]);
  FA1Bit fa1bit_219 (.Cin(1'b0), .A(and_228_out), .B(fa1bit_218_s), .Cout(fa1bit_219_cout), .S(Product[7]));
  and and_229 (and_229_out, A[6], B[0]);
  and and_230 (and_230_out, A[5], B[1]);
  FA1Bit fa1bit_220 (.Cin(fa1bit_226_cout), .A(and_229_out), .B(and_230_out), .Cout(fa1bit_220_cout), .S(fa1bit_220_s));
  and and_231 (and_231_out, A[4], B[2]);
  FA1Bit fa1bit_221 (
    .Cin(fa1bit_227_cout), .A(and_231_out), .B(fa1bit_220_s), .Cout(fa1bit_221_cout), .S(fa1bit_221_s));
  and and_232 (and_232_out, A[3], B[3]);
  FA1Bit fa1bit_222 (
    .Cin(fa1bit_228_cout), .A(and_232_out), .B(fa1bit_221_s), .Cout(fa1bit_222_cout), .S(fa1bit_222_s));
  and and_233 (and_233_out, A[2], B[4]);
  FA1Bit fa1bit_223 (
    .Cin(fa1bit_229_cout), .A(and_233_out), .B(fa1bit_222_s), .Cout(fa1bit_223_cout), .S(fa1bit_223_s));
  and and_234 (and_234_out, A[1], B[5]);
  FA1Bit fa1bit_224 (
    .Cin(fa1bit_230_cout), .A(and_234_out), .B(fa1bit_223_s), .Cout(fa1bit_224_cout), .S(fa1bit_224_s));
  and and_235 (and_235_out, A[0], B[6]);
  FA1Bit fa1bit_225 (.Cin(1'b0), .A(and_235_out), .B(fa1bit_224_s), .Cout(fa1bit_225_cout), .S(Product[6]));
  and and_236 (and_236_out, A[5], B[0]);
  and and_237 (and_237_out, A[4], B[1]);
  FA1Bit fa1bit_226 (.Cin(fa1bit_231_cout), .A(and_236_out), .B(and_237_out), .Cout(fa1bit_226_cout), .S(fa1bit_226_s));
  and and_238 (and_238_out, A[3], B[2]);
  FA1Bit fa1bit_227 (
    .Cin(fa1bit_232_cout), .A(and_238_out), .B(fa1bit_226_s), .Cout(fa1bit_227_cout), .S(fa1bit_227_s));
  and and_239 (and_239_out, A[2], B[3]);
  FA1Bit fa1bit_228 (
    .Cin(fa1bit_233_cout), .A(and_239_out), .B(fa1bit_227_s), .Cout(fa1bit_228_cout), .S(fa1bit_228_s));
  and and_240 (and_240_out, A[1], B[4]);
  FA1Bit fa1bit_229 (
    .Cin(fa1bit_234_cout), .A(and_240_out), .B(fa1bit_228_s), .Cout(fa1bit_229_cout), .S(fa1bit_229_s));
  and and_241 (and_241_out, A[0], B[5]);
  FA1Bit fa1bit_230 (.Cin(1'b0), .A(and_241_out), .B(fa1bit_229_s), .Cout(fa1bit_230_cout), .S(Product[5]));
  and and_242 (and_242_out, A[4], B[0]);
  and and_243 (and_243_out, A[3], B[1]);
  FA1Bit fa1bit_231 (.Cin(fa1bit_235_cout), .A(and_242_out), .B(and_243_out), .Cout(fa1bit_231_cout), .S(fa1bit_231_s));
  and and_244 (and_244_out, A[2], B[2]);
  FA1Bit fa1bit_232 (
    .Cin(fa1bit_236_cout), .A(and_244_out), .B(fa1bit_231_s), .Cout(fa1bit_232_cout), .S(fa1bit_232_s));
  and and_245 (and_245_out, A[1], B[3]);
  FA1Bit fa1bit_233 (
    .Cin(fa1bit_237_cout), .A(and_245_out), .B(fa1bit_232_s), .Cout(fa1bit_233_cout), .S(fa1bit_233_s));
  and and_246 (and_246_out, A[0], B[4]);
  FA1Bit fa1bit_234 (.Cin(1'b0), .A(and_246_out), .B(fa1bit_233_s), .Cout(fa1bit_234_cout), .S(Product[4]));
  and and_247 (and_247_out, A[3], B[0]);
  and and_248 (and_248_out, A[2], B[1]);
  FA1Bit fa1bit_235 (.Cin(fa1bit_238_cout), .A(and_247_out), .B(and_248_out), .Cout(fa1bit_235_cout), .S(fa1bit_235_s));
  and and_249 (and_249_out, A[1], B[2]);
  FA1Bit fa1bit_236 (
    .Cin(fa1bit_239_cout), .A(and_249_out), .B(fa1bit_235_s), .Cout(fa1bit_236_cout), .S(fa1bit_236_s));
  and and_250 (and_250_out, A[0], B[3]);
  FA1Bit fa1bit_237 (.Cin(1'b0), .A(and_250_out), .B(fa1bit_236_s), .Cout(fa1bit_237_cout), .S(Product[3]));
  and and_251 (and_251_out, A[2], B[0]);
  and and_252 (and_252_out, A[1], B[1]);
  FA1Bit fa1bit_238 (.Cin(fa1bit_240_cout), .A(and_251_out), .B(and_252_out), .Cout(fa1bit_238_cout), .S(fa1bit_238_s));
  and and_253 (and_253_out, A[0], B[2]);
  FA1Bit fa1bit_239 (.Cin(1'b0), .A(and_253_out), .B(fa1bit_238_s), .Cout(fa1bit_239_cout), .S(Product[2]));
  and and_254 (and_254_out, A[1], B[0]);
  and and_255 (and_255_out, A[0], B[1]);
  FA1Bit fa1bit_240 (.Cin(1'b0), .A(and_254_out), .B(and_255_out), .Cout(fa1bit_240_cout), .S(Product[1]));
  and and_256 (Product[0], A[0], B[0]);

  // Notes on the sheet:
  //   x15
  //   x14
  //   x13
  //   x12
  //   x11
  //   x10
  //   x9
  //   x8
  //   x7
  //   x6
  //   x5
  //   x4
  //   x3
  //   x2
  //   x1
  //   x0
endmodule

module DivisionStep (
  input  [31:0] Divisor,
  input  DividendBit,
  input  [31:0] CurrentRest,
  output [31:0] NewRest,
  output QuotientBit
);

  wire [31:0] subtractor_2_out;

  Subtractor #(.width(32)) subtractor_1 (
    .a(Divisor), .b({CurrentRest[30:0], DividendBit}), .bin(1'b1), .bout(QuotientBit));  // open: out
  Subtractor #(.width(32)) subtractor_2 (
    .a({CurrentRest[30:0], DividendBit}), .b(Divisor), .out(subtractor_2_out));  // open: bin, bout
  Multiplexer #(.width(32)) multiplexer_1 (
    .in0({CurrentRest[30:0], DividendBit}), .in1(subtractor_2_out), .out(NewRest), .sel(QuotientBit));
endmodule

module Divider32Bit (
  input  [31:0] Divisor,
  input  [31:0] Dividend,
  output [31:0] Rest,
  output [31:0] Quotient
);

  wire or32to1_1_out_2;
  wire [31:0] divisionstep_2_newrest, divisionstep_3_newrest, divisionstep_4_newrest, divisionstep_5_newrest,
       divisionstep_6_newrest, divisionstep_7_newrest, divisionstep_8_newrest, divisionstep_9_newrest,
       divisionstep_10_newrest, divisionstep_11_newrest, divisionstep_12_newrest, divisionstep_13_newrest,
       divisionstep_14_newrest, divisionstep_15_newrest, divisionstep_16_newrest, divisionstep_17_newrest,
       divisionstep_18_newrest, divisionstep_19_newrest, divisionstep_20_newrest, divisionstep_21_newrest,
       divisionstep_22_newrest, divisionstep_23_newrest, divisionstep_24_newrest, divisionstep_25_newrest,
       divisionstep_26_newrest, divisionstep_27_newrest, divisionstep_28_newrest, divisionstep_29_newrest,
       divisionstep_30_newrest, divisionstep_31_newrest, divisionstep_32_newrest, multiplexer_1_out;

  OR32to1 or32to1_1 (.in_1(Divisor), .out_2(or32to1_1_out_2));
  Multiplexer #(.width(32)) multiplexer_1 (.in0(Divisor), .in1(32'h1), .out(multiplexer_1_out), .sel(or32to1_1_out_2));
  DivisionStep divisionstep_1 (
    .Divisor(multiplexer_1_out), .CurrentRest(divisionstep_2_newrest), .DividendBit(Dividend[0]),
    .NewRest(Rest), .QuotientBit(Quotient[0]));
  DivisionStep divisionstep_2 (
    .Divisor(multiplexer_1_out), .CurrentRest(divisionstep_3_newrest), .DividendBit(Dividend[1]),
    .NewRest(divisionstep_2_newrest), .QuotientBit(Quotient[1]));
  DivisionStep divisionstep_3 (
    .Divisor(multiplexer_1_out), .CurrentRest(divisionstep_4_newrest), .DividendBit(Dividend[2]),
    .NewRest(divisionstep_3_newrest), .QuotientBit(Quotient[2]));
  DivisionStep divisionstep_4 (
    .Divisor(multiplexer_1_out), .CurrentRest(divisionstep_5_newrest), .DividendBit(Dividend[3]),
    .NewRest(divisionstep_4_newrest), .QuotientBit(Quotient[3]));
  DivisionStep divisionstep_5 (
    .Divisor(multiplexer_1_out), .CurrentRest(divisionstep_6_newrest), .DividendBit(Dividend[4]),
    .NewRest(divisionstep_5_newrest), .QuotientBit(Quotient[4]));
  DivisionStep divisionstep_6 (
    .Divisor(multiplexer_1_out), .CurrentRest(divisionstep_7_newrest), .DividendBit(Dividend[5]),
    .NewRest(divisionstep_6_newrest), .QuotientBit(Quotient[5]));
  DivisionStep divisionstep_7 (
    .Divisor(multiplexer_1_out), .CurrentRest(divisionstep_8_newrest), .DividendBit(Dividend[6]),
    .NewRest(divisionstep_7_newrest), .QuotientBit(Quotient[6]));
  DivisionStep divisionstep_8 (
    .Divisor(multiplexer_1_out), .CurrentRest(divisionstep_9_newrest), .DividendBit(Dividend[7]),
    .NewRest(divisionstep_8_newrest), .QuotientBit(Quotient[7]));
  DivisionStep divisionstep_9 (
    .Divisor(multiplexer_1_out), .CurrentRest(divisionstep_10_newrest), .DividendBit(Dividend[8]),
    .NewRest(divisionstep_9_newrest), .QuotientBit(Quotient[8]));
  DivisionStep divisionstep_10 (
    .Divisor(multiplexer_1_out), .CurrentRest(divisionstep_11_newrest), .DividendBit(Dividend[9]),
    .NewRest(divisionstep_10_newrest), .QuotientBit(Quotient[9]));
  DivisionStep divisionstep_11 (
    .Divisor(multiplexer_1_out), .CurrentRest(divisionstep_12_newrest), .DividendBit(Dividend[10]),
    .NewRest(divisionstep_11_newrest), .QuotientBit(Quotient[10]));
  DivisionStep divisionstep_12 (
    .Divisor(multiplexer_1_out), .CurrentRest(divisionstep_13_newrest), .DividendBit(Dividend[11]),
    .NewRest(divisionstep_12_newrest), .QuotientBit(Quotient[11]));
  DivisionStep divisionstep_13 (
    .Divisor(multiplexer_1_out), .CurrentRest(divisionstep_14_newrest), .DividendBit(Dividend[12]),
    .NewRest(divisionstep_13_newrest), .QuotientBit(Quotient[12]));
  DivisionStep divisionstep_14 (
    .Divisor(multiplexer_1_out), .CurrentRest(divisionstep_15_newrest), .DividendBit(Dividend[13]),
    .NewRest(divisionstep_14_newrest), .QuotientBit(Quotient[13]));
  DivisionStep divisionstep_15 (
    .Divisor(multiplexer_1_out), .CurrentRest(divisionstep_16_newrest), .DividendBit(Dividend[14]),
    .NewRest(divisionstep_15_newrest), .QuotientBit(Quotient[14]));
  DivisionStep divisionstep_16 (
    .Divisor(multiplexer_1_out), .CurrentRest(divisionstep_17_newrest), .DividendBit(Dividend[15]),
    .NewRest(divisionstep_16_newrest), .QuotientBit(Quotient[15]));
  DivisionStep divisionstep_17 (
    .Divisor(multiplexer_1_out), .CurrentRest(divisionstep_18_newrest), .DividendBit(Dividend[16]),
    .NewRest(divisionstep_17_newrest), .QuotientBit(Quotient[16]));
  DivisionStep divisionstep_18 (
    .Divisor(multiplexer_1_out), .CurrentRest(divisionstep_19_newrest), .DividendBit(Dividend[17]),
    .NewRest(divisionstep_18_newrest), .QuotientBit(Quotient[17]));
  DivisionStep divisionstep_19 (
    .Divisor(multiplexer_1_out), .CurrentRest(divisionstep_20_newrest), .DividendBit(Dividend[18]),
    .NewRest(divisionstep_19_newrest), .QuotientBit(Quotient[18]));
  DivisionStep divisionstep_20 (
    .Divisor(multiplexer_1_out), .CurrentRest(divisionstep_21_newrest), .DividendBit(Dividend[19]),
    .NewRest(divisionstep_20_newrest), .QuotientBit(Quotient[19]));
  DivisionStep divisionstep_21 (
    .Divisor(multiplexer_1_out), .CurrentRest(divisionstep_22_newrest), .DividendBit(Dividend[20]),
    .NewRest(divisionstep_21_newrest), .QuotientBit(Quotient[20]));
  DivisionStep divisionstep_22 (
    .Divisor(multiplexer_1_out), .CurrentRest(divisionstep_23_newrest), .DividendBit(Dividend[21]),
    .NewRest(divisionstep_22_newrest), .QuotientBit(Quotient[21]));
  DivisionStep divisionstep_23 (
    .Divisor(multiplexer_1_out), .CurrentRest(divisionstep_24_newrest), .DividendBit(Dividend[22]),
    .NewRest(divisionstep_23_newrest), .QuotientBit(Quotient[22]));
  DivisionStep divisionstep_24 (
    .Divisor(multiplexer_1_out), .CurrentRest(divisionstep_25_newrest), .DividendBit(Dividend[23]),
    .NewRest(divisionstep_24_newrest), .QuotientBit(Quotient[23]));
  DivisionStep divisionstep_25 (
    .Divisor(multiplexer_1_out), .CurrentRest(divisionstep_26_newrest), .DividendBit(Dividend[24]),
    .NewRest(divisionstep_25_newrest), .QuotientBit(Quotient[24]));
  DivisionStep divisionstep_26 (
    .Divisor(multiplexer_1_out), .CurrentRest(divisionstep_27_newrest), .DividendBit(Dividend[25]),
    .NewRest(divisionstep_26_newrest), .QuotientBit(Quotient[25]));
  DivisionStep divisionstep_27 (
    .Divisor(multiplexer_1_out), .CurrentRest(divisionstep_28_newrest), .DividendBit(Dividend[26]),
    .NewRest(divisionstep_27_newrest), .QuotientBit(Quotient[26]));
  DivisionStep divisionstep_28 (
    .Divisor(multiplexer_1_out), .CurrentRest(divisionstep_29_newrest), .DividendBit(Dividend[27]),
    .NewRest(divisionstep_28_newrest), .QuotientBit(Quotient[27]));
  DivisionStep divisionstep_29 (
    .Divisor(multiplexer_1_out), .CurrentRest(divisionstep_30_newrest), .DividendBit(Dividend[28]),
    .NewRest(divisionstep_29_newrest), .QuotientBit(Quotient[28]));
  DivisionStep divisionstep_30 (
    .Divisor(multiplexer_1_out), .CurrentRest(divisionstep_31_newrest), .DividendBit(Dividend[29]),
    .NewRest(divisionstep_30_newrest), .QuotientBit(Quotient[29]));
  DivisionStep divisionstep_31 (
    .Divisor(multiplexer_1_out), .CurrentRest(divisionstep_32_newrest), .DividendBit(Dividend[30]),
    .NewRest(divisionstep_31_newrest), .QuotientBit(Quotient[30]));
  DivisionStep divisionstep_32 (
    .Divisor(multiplexer_1_out), .CurrentRest({32{1'b0}}), .DividendBit(Dividend[31]),
    .NewRest(divisionstep_32_newrest), .QuotientBit(Quotient[31]));
endmodule

module ArithmeticUnit (
  input  Cin,
  input  [31:0] A,
  input  [31:0] B,
  input  Sel,
  output [31:0] Q,
  output Cout,
  output CoutSUBLESS
);

  wire adder32bit_1_cout;
  wire [31:0] adder32bit_1_s, subtractor32bit_1_s;

  Adder32Bit adder32bit_1 (.A(A), .B(B), .Cin(Cin), .Cout(adder32bit_1_cout), .S(adder32bit_1_s));
  Subtractor32Bit subtractor32bit_1 (.A(A), .B(B), .Cout(CoutSUBLESS), .S(subtractor32bit_1_s));
  Multiplexer multiplexer_1 (.in0(adder32bit_1_cout), .in1(CoutSUBLESS), .out(Cout), .sel(Sel));
  Multiplexer #(.width(32)) multiplexer_2 (.in0(adder32bit_1_s), .in1(subtractor32bit_1_s), .out(Q), .sel(Sel));
endmodule

module LogicUnit (
  input  [31:0] A,
  input  [31:0] B,
  input  [2:0] Sel,
  output [31:0] Q
);

  wire [31:0] and_1_out, nand_1_out, nor_1_out, or_1_out, xnor_1_out, xor_1_out;

  assign and_1_out = A & B;  // AND_Gate and_1, 32 bits wide
  assign or_1_out = A | B;  // OR_Gate or_1, 32 bits wide
  Multiplexer #(.select(3), .width(32)) multiplexer_1 (
    .in1(and_1_out), .in3(or_1_out), .in4(xor_1_out), .in5(nand_1_out), .in6(nor_1_out), .in7(xnor_1_out),
    .out(Q), .sel(Sel));  // open: in0, in2
  assign xor_1_out = A ^ B;  // XOR_Gate xor_1, 32 bits wide
  assign nand_1_out = ~(A & B);  // NAND_Gate nand_1, 32 bits wide
  assign nor_1_out = ~(A | B);  // NOR_Gate nor_1, 32 bits wide
  assign xnor_1_out = ~(A ^ B);  // XNOR_Gate xnor_1, 32 bits wide
endmodule

module ComparatorUnit (
  input  [31:0] A,
  input  [31:0] B,
  input  CoutSUBLESS,
  input  [2:0] Sel,
  output TrueFalse
);

  wire and_1_out, equal_1_aequalb, less_1_alessb, not_1_out, not_2_out, not_3_out;

  Equal equal_1 (.A(A), .B(B), .AequalB(equal_1_aequalb));
  not not_1 (not_1_out, equal_1_aequalb);
  Less less_1 (.CoutSUBLESS(CoutSUBLESS), .AlessB(less_1_alessb));
  not not_2 (not_2_out, less_1_alessb);
  not not_3 (not_3_out, and_1_out);
  and and_1 (and_1_out, not_1_out, not_2_out);
  Multiplexer #(.select(3)) multiplexer_1 (
    .in0(equal_1_aequalb), .in1(not_1_out), .in2(less_1_alessb), .in3(and_1_out), .in4(not_3_out),
    .in5(not_2_out), .out(TrueFalse), .sel(Sel));  // open: in6, in7

  // Notes on the sheet:
  //   Input is 0 -> A<B
  //   !=
  //   >=
  //   <=
  //   >
endmodule

module ShifterUnit (
  input  [31:0] DataIn,
  input  FillSelect,
  input  Arithmetic,
  input  [4:0] ShiftAmount,
  input  Rotate,
  input  Direction,
  output [31:0] DataOut,
  output [31:0] Flip
);

  wire multiplexer_1_out, multiplexer_34_out, multiplexer_35_out, multiplexer_36_out, multiplexer_37_out,
       multiplexer_38_out, multiplexer_39_out, multiplexer_40_out, multiplexer_41_out, multiplexer_42_out,
       multiplexer_43_out, multiplexer_44_out, multiplexer_45_out, multiplexer_46_out, multiplexer_47_out,
       multiplexer_48_out, multiplexer_49_out, multiplexer_50_out, multiplexer_51_out, multiplexer_52_out,
       multiplexer_53_out, multiplexer_54_out, multiplexer_55_out, multiplexer_56_out, multiplexer_57_out,
       multiplexer_58_out, multiplexer_59_out, multiplexer_60_out, multiplexer_61_out, multiplexer_62_out,
       multiplexer_63_out, multiplexer_64_out, multiplexer_65_out, multiplexer_66_out, multiplexer_67_out,
       multiplexer_68_out, multiplexer_69_out, multiplexer_70_out, multiplexer_71_out, multiplexer_72_out,
       multiplexer_73_out, multiplexer_74_out, multiplexer_75_out, multiplexer_76_out, multiplexer_77_out,
       multiplexer_78_out, multiplexer_79_out, multiplexer_80_out, multiplexer_81_out, multiplexer_82_out,
       multiplexer_83_out, multiplexer_84_out, multiplexer_85_out, multiplexer_86_out, multiplexer_87_out,
       multiplexer_88_out, multiplexer_89_out, multiplexer_90_out, multiplexer_91_out, multiplexer_92_out,
       multiplexer_93_out, multiplexer_94_out, multiplexer_95_out, multiplexer_96_out, multiplexer_97_out,
       multiplexer_98_out, multiplexer_99_out, multiplexer_100_out, multiplexer_101_out, multiplexer_102_out,
       multiplexer_103_out, multiplexer_104_out, multiplexer_105_out, multiplexer_106_out,
       multiplexer_107_out, multiplexer_108_out, multiplexer_109_out, multiplexer_110_out,
       multiplexer_111_out, multiplexer_112_out, multiplexer_113_out, multiplexer_114_out,
       multiplexer_115_out, multiplexer_116_out, multiplexer_117_out, multiplexer_118_out,
       multiplexer_119_out, multiplexer_120_out, multiplexer_121_out, multiplexer_122_out,
       multiplexer_123_out, multiplexer_124_out, multiplexer_125_out, multiplexer_126_out,
       multiplexer_127_out, multiplexer_128_out, multiplexer_129_out, multiplexer_130_out,
       multiplexer_131_out, multiplexer_132_out, multiplexer_133_out, multiplexer_134_out,
       multiplexer_135_out, multiplexer_136_out, multiplexer_137_out, multiplexer_138_out,
       multiplexer_139_out, multiplexer_140_out, multiplexer_141_out, multiplexer_142_out,
       multiplexer_143_out, multiplexer_144_out, multiplexer_145_out, multiplexer_146_out,
       multiplexer_147_out, multiplexer_148_out, multiplexer_149_out, multiplexer_150_out,
       multiplexer_151_out, multiplexer_152_out, multiplexer_153_out, multiplexer_154_out,
       multiplexer_155_out, multiplexer_156_out, multiplexer_157_out, multiplexer_158_out,
       multiplexer_159_out, multiplexer_160_out, multiplexer_161_out, multiplexer_162_out,
       multiplexer_163_out, multiplexer_164_out, multiplexer_165_out, multiplexer_166_out,
       multiplexer_167_out, multiplexer_168_out, multiplexer_169_out, multiplexer_170_out,
       multiplexer_171_out, multiplexer_172_out, multiplexer_173_out, multiplexer_174_out,
       multiplexer_175_out, multiplexer_176_out, multiplexer_177_out, multiplexer_178_out,
       multiplexer_179_out, multiplexer_180_out, multiplexer_181_out, multiplexer_182_out,
       multiplexer_183_out, multiplexer_184_out, multiplexer_185_out, multiplexer_186_out,
       multiplexer_187_out, multiplexer_188_out, multiplexer_189_out, multiplexer_190_out,
       multiplexer_191_out, multiplexer_192_out, multiplexer_193_out, multiplexer_194_out,
       multiplexer_195_out, multiplexer_196_out, multiplexer_197_out, multiplexer_198_out,
       multiplexer_199_out, multiplexer_200_out, multiplexer_201_out, multiplexer_202_out,
       multiplexer_203_out, multiplexer_204_out, multiplexer_205_out, multiplexer_206_out,
       multiplexer_207_out, multiplexer_208_out, multiplexer_209_out, multiplexer_210_out,
       multiplexer_211_out, multiplexer_212_out, multiplexer_213_out, multiplexer_214_out,
       multiplexer_215_out, multiplexer_216_out, multiplexer_217_out, multiplexer_218_out,
       multiplexer_219_out, multiplexer_220_out, multiplexer_221_out, multiplexer_222_out,
       multiplexer_223_out, multiplexer_224_out;

  Multiplexer multiplexer_1 (.in0(FillSelect), .in1(DataIn[31]), .out(multiplexer_1_out), .sel(Arithmetic));
  Multiplexer multiplexer_2 (.in0(DataIn[0]), .in1(DataIn[31]), .out(Flip[0]), .sel(Direction));
  Multiplexer multiplexer_3 (.in0(DataIn[1]), .in1(DataIn[30]), .out(Flip[1]), .sel(Direction));
  Multiplexer multiplexer_4 (.in0(DataIn[2]), .in1(DataIn[29]), .out(Flip[2]), .sel(Direction));
  Multiplexer multiplexer_5 (.in0(DataIn[3]), .in1(DataIn[28]), .out(Flip[3]), .sel(Direction));
  Multiplexer multiplexer_6 (.in0(DataIn[4]), .in1(DataIn[27]), .out(Flip[4]), .sel(Direction));
  Multiplexer multiplexer_7 (.in0(DataIn[5]), .in1(DataIn[26]), .out(Flip[5]), .sel(Direction));
  Multiplexer multiplexer_8 (.in0(DataIn[6]), .in1(DataIn[25]), .out(Flip[6]), .sel(Direction));
  Multiplexer multiplexer_9 (.in0(DataIn[7]), .in1(DataIn[24]), .out(Flip[7]), .sel(Direction));
  Multiplexer multiplexer_10 (.in0(DataIn[8]), .in1(DataIn[23]), .out(Flip[8]), .sel(Direction));
  Multiplexer multiplexer_11 (.in0(DataIn[9]), .in1(DataIn[22]), .out(Flip[9]), .sel(Direction));
  Multiplexer multiplexer_12 (.in0(DataIn[10]), .in1(DataIn[21]), .out(Flip[10]), .sel(Direction));
  Multiplexer multiplexer_13 (.in0(DataIn[11]), .in1(DataIn[20]), .out(Flip[11]), .sel(Direction));
  Multiplexer multiplexer_14 (.in0(DataIn[12]), .in1(DataIn[19]), .out(Flip[12]), .sel(Direction));
  Multiplexer multiplexer_15 (.in0(DataIn[13]), .in1(DataIn[18]), .out(Flip[13]), .sel(Direction));
  Multiplexer multiplexer_16 (.in0(DataIn[14]), .in1(DataIn[17]), .out(Flip[14]), .sel(Direction));
  Multiplexer multiplexer_17 (.in0(DataIn[15]), .in1(DataIn[16]), .out(Flip[15]), .sel(Direction));
  Multiplexer multiplexer_18 (.in0(DataIn[16]), .in1(DataIn[15]), .out(Flip[16]), .sel(Direction));
  Multiplexer multiplexer_19 (.in0(DataIn[17]), .in1(DataIn[14]), .out(Flip[17]), .sel(Direction));
  Multiplexer multiplexer_20 (.in0(DataIn[18]), .in1(DataIn[13]), .out(Flip[18]), .sel(Direction));
  Multiplexer multiplexer_21 (.in0(DataIn[19]), .in1(DataIn[12]), .out(Flip[19]), .sel(Direction));
  Multiplexer multiplexer_22 (.in0(DataIn[20]), .in1(DataIn[11]), .out(Flip[20]), .sel(Direction));
  Multiplexer multiplexer_23 (.in0(DataIn[21]), .in1(DataIn[10]), .out(Flip[21]), .sel(Direction));
  Multiplexer multiplexer_24 (.in0(DataIn[22]), .in1(DataIn[9]), .out(Flip[22]), .sel(Direction));
  Multiplexer multiplexer_25 (.in0(DataIn[23]), .in1(DataIn[8]), .out(Flip[23]), .sel(Direction));
  Multiplexer multiplexer_26 (.in0(DataIn[24]), .in1(DataIn[7]), .out(Flip[24]), .sel(Direction));
  Multiplexer multiplexer_27 (.in0(DataIn[25]), .in1(DataIn[6]), .out(Flip[25]), .sel(Direction));
  Multiplexer multiplexer_28 (.in0(DataIn[26]), .in1(DataIn[5]), .out(Flip[26]), .sel(Direction));
  Multiplexer multiplexer_29 (.in0(DataIn[27]), .in1(DataIn[4]), .out(Flip[27]), .sel(Direction));
  Multiplexer multiplexer_30 (.in0(DataIn[28]), .in1(DataIn[3]), .out(Flip[28]), .sel(Direction));
  Multiplexer multiplexer_31 (.in0(DataIn[29]), .in1(DataIn[2]), .out(Flip[29]), .sel(Direction));
  Multiplexer multiplexer_32 (.in0(DataIn[30]), .in1(DataIn[1]), .out(Flip[30]), .sel(Direction));
  Multiplexer multiplexer_33 (.in0(DataIn[31]), .in1(DataIn[0]), .out(Flip[31]), .sel(Direction));
  Multiplexer multiplexer_34 (.in0(multiplexer_1_out), .in1(Flip[0]), .out(multiplexer_34_out), .sel(Rotate));
  Multiplexer multiplexer_35 (.in0(multiplexer_1_out), .in1(Flip[1]), .out(multiplexer_35_out), .sel(Rotate));
  Multiplexer multiplexer_36 (.in0(multiplexer_1_out), .in1(Flip[2]), .out(multiplexer_36_out), .sel(Rotate));
  Multiplexer multiplexer_37 (.in0(multiplexer_1_out), .in1(Flip[3]), .out(multiplexer_37_out), .sel(Rotate));
  Multiplexer multiplexer_38 (.in0(multiplexer_1_out), .in1(Flip[4]), .out(multiplexer_38_out), .sel(Rotate));
  Multiplexer multiplexer_39 (.in0(multiplexer_1_out), .in1(Flip[5]), .out(multiplexer_39_out), .sel(Rotate));
  Multiplexer multiplexer_40 (.in0(multiplexer_1_out), .in1(Flip[6]), .out(multiplexer_40_out), .sel(Rotate));
  Multiplexer multiplexer_41 (.in0(multiplexer_1_out), .in1(Flip[7]), .out(multiplexer_41_out), .sel(Rotate));
  Multiplexer multiplexer_42 (.in0(multiplexer_1_out), .in1(Flip[8]), .out(multiplexer_42_out), .sel(Rotate));
  Multiplexer multiplexer_43 (.in0(multiplexer_1_out), .in1(Flip[9]), .out(multiplexer_43_out), .sel(Rotate));
  Multiplexer multiplexer_44 (.in0(multiplexer_1_out), .in1(Flip[10]), .out(multiplexer_44_out), .sel(Rotate));
  Multiplexer multiplexer_45 (.in0(multiplexer_1_out), .in1(Flip[11]), .out(multiplexer_45_out), .sel(Rotate));
  Multiplexer multiplexer_46 (.in0(multiplexer_1_out), .in1(Flip[12]), .out(multiplexer_46_out), .sel(Rotate));
  Multiplexer multiplexer_47 (.in0(multiplexer_1_out), .in1(Flip[13]), .out(multiplexer_47_out), .sel(Rotate));
  Multiplexer multiplexer_48 (.in0(multiplexer_1_out), .in1(Flip[14]), .out(multiplexer_48_out), .sel(Rotate));
  Multiplexer multiplexer_49 (.in0(multiplexer_1_out), .in1(Flip[15]), .out(multiplexer_49_out), .sel(Rotate));
  Multiplexer multiplexer_50 (.in0(Flip[0]), .in1(Flip[16]), .out(multiplexer_50_out), .sel(ShiftAmount[4]));
  Multiplexer multiplexer_51 (.in0(Flip[1]), .in1(Flip[17]), .out(multiplexer_51_out), .sel(ShiftAmount[4]));
  Multiplexer multiplexer_52 (.in0(Flip[2]), .in1(Flip[18]), .out(multiplexer_52_out), .sel(ShiftAmount[4]));
  Multiplexer multiplexer_53 (.in0(Flip[3]), .in1(Flip[19]), .out(multiplexer_53_out), .sel(ShiftAmount[4]));
  Multiplexer multiplexer_54 (.in0(Flip[4]), .in1(Flip[20]), .out(multiplexer_54_out), .sel(ShiftAmount[4]));
  Multiplexer multiplexer_55 (.in0(Flip[5]), .in1(Flip[21]), .out(multiplexer_55_out), .sel(ShiftAmount[4]));
  Multiplexer multiplexer_56 (.in0(Flip[6]), .in1(Flip[22]), .out(multiplexer_56_out), .sel(ShiftAmount[4]));
  Multiplexer multiplexer_57 (.in0(Flip[7]), .in1(Flip[23]), .out(multiplexer_57_out), .sel(ShiftAmount[4]));
  Multiplexer multiplexer_58 (.in0(Flip[8]), .in1(Flip[24]), .out(multiplexer_58_out), .sel(ShiftAmount[4]));
  Multiplexer multiplexer_59 (.in0(Flip[9]), .in1(Flip[25]), .out(multiplexer_59_out), .sel(ShiftAmount[4]));
  Multiplexer multiplexer_60 (.in0(Flip[10]), .in1(Flip[26]), .out(multiplexer_60_out), .sel(ShiftAmount[4]));
  Multiplexer multiplexer_61 (.in0(Flip[11]), .in1(Flip[27]), .out(multiplexer_61_out), .sel(ShiftAmount[4]));
  Multiplexer multiplexer_62 (.in0(Flip[12]), .in1(Flip[28]), .out(multiplexer_62_out), .sel(ShiftAmount[4]));
  Multiplexer multiplexer_63 (.in0(Flip[13]), .in1(Flip[29]), .out(multiplexer_63_out), .sel(ShiftAmount[4]));
  Multiplexer multiplexer_64 (.in0(Flip[14]), .in1(Flip[30]), .out(multiplexer_64_out), .sel(ShiftAmount[4]));
  Multiplexer multiplexer_65 (.in0(Flip[15]), .in1(Flip[31]), .out(multiplexer_65_out), .sel(ShiftAmount[4]));
  Multiplexer multiplexer_66 (.in0(Flip[16]), .in1(multiplexer_34_out), .out(multiplexer_66_out), .sel(ShiftAmount[4]));
  Multiplexer multiplexer_67 (.in0(Flip[17]), .in1(multiplexer_35_out), .out(multiplexer_67_out), .sel(ShiftAmount[4]));
  Multiplexer multiplexer_68 (.in0(Flip[18]), .in1(multiplexer_36_out), .out(multiplexer_68_out), .sel(ShiftAmount[4]));
  Multiplexer multiplexer_69 (.in0(Flip[19]), .in1(multiplexer_37_out), .out(multiplexer_69_out), .sel(ShiftAmount[4]));
  Multiplexer multiplexer_70 (.in0(Flip[20]), .in1(multiplexer_38_out), .out(multiplexer_70_out), .sel(ShiftAmount[4]));
  Multiplexer multiplexer_71 (.in0(Flip[21]), .in1(multiplexer_39_out), .out(multiplexer_71_out), .sel(ShiftAmount[4]));
  Multiplexer multiplexer_72 (.in0(Flip[22]), .in1(multiplexer_40_out), .out(multiplexer_72_out), .sel(ShiftAmount[4]));
  Multiplexer multiplexer_73 (.in0(Flip[23]), .in1(multiplexer_41_out), .out(multiplexer_73_out), .sel(ShiftAmount[4]));
  Multiplexer multiplexer_74 (.in0(Flip[24]), .in1(multiplexer_42_out), .out(multiplexer_74_out), .sel(ShiftAmount[4]));
  Multiplexer multiplexer_75 (.in0(Flip[25]), .in1(multiplexer_43_out), .out(multiplexer_75_out), .sel(ShiftAmount[4]));
  Multiplexer multiplexer_76 (.in0(Flip[26]), .in1(multiplexer_44_out), .out(multiplexer_76_out), .sel(ShiftAmount[4]));
  Multiplexer multiplexer_77 (.in0(Flip[27]), .in1(multiplexer_45_out), .out(multiplexer_77_out), .sel(ShiftAmount[4]));
  Multiplexer multiplexer_78 (.in0(Flip[28]), .in1(multiplexer_46_out), .out(multiplexer_78_out), .sel(ShiftAmount[4]));
  Multiplexer multiplexer_79 (.in0(Flip[29]), .in1(multiplexer_47_out), .out(multiplexer_79_out), .sel(ShiftAmount[4]));
  Multiplexer multiplexer_80 (.in0(Flip[30]), .in1(multiplexer_48_out), .out(multiplexer_80_out), .sel(ShiftAmount[4]));
  Multiplexer multiplexer_81 (.in0(Flip[31]), .in1(multiplexer_49_out), .out(multiplexer_81_out), .sel(ShiftAmount[4]));
  Multiplexer multiplexer_82 (
    .in0(multiplexer_1_out), .in1(multiplexer_50_out), .out(multiplexer_82_out), .sel(Rotate));
  Multiplexer multiplexer_83 (
    .in0(multiplexer_1_out), .in1(multiplexer_51_out), .out(multiplexer_83_out), .sel(Rotate));
  Multiplexer multiplexer_84 (
    .in0(multiplexer_1_out), .in1(multiplexer_52_out), .out(multiplexer_84_out), .sel(Rotate));
  Multiplexer multiplexer_85 (
    .in0(multiplexer_1_out), .in1(multiplexer_53_out), .out(multiplexer_85_out), .sel(Rotate));
  Multiplexer multiplexer_86 (
    .in0(multiplexer_1_out), .in1(multiplexer_54_out), .out(multiplexer_86_out), .sel(Rotate));
  Multiplexer multiplexer_87 (
    .in0(multiplexer_1_out), .in1(multiplexer_55_out), .out(multiplexer_87_out), .sel(Rotate));
  Multiplexer multiplexer_88 (
    .in0(multiplexer_1_out), .in1(multiplexer_56_out), .out(multiplexer_88_out), .sel(Rotate));
  Multiplexer multiplexer_89 (
    .in0(multiplexer_1_out), .in1(multiplexer_57_out), .out(multiplexer_89_out), .sel(Rotate));
  Multiplexer multiplexer_90 (
    .in0(multiplexer_50_out), .in1(multiplexer_58_out), .out(multiplexer_90_out), .sel(ShiftAmount[3]));
  Multiplexer multiplexer_91 (
    .in0(multiplexer_51_out), .in1(multiplexer_59_out), .out(multiplexer_91_out), .sel(ShiftAmount[3]));
  Multiplexer multiplexer_92 (
    .in0(multiplexer_52_out), .in1(multiplexer_60_out), .out(multiplexer_92_out), .sel(ShiftAmount[3]));
  Multiplexer multiplexer_93 (
    .in0(multiplexer_53_out), .in1(multiplexer_61_out), .out(multiplexer_93_out), .sel(ShiftAmount[3]));
  Multiplexer multiplexer_94 (
    .in0(multiplexer_54_out), .in1(multiplexer_62_out), .out(multiplexer_94_out), .sel(ShiftAmount[3]));
  Multiplexer multiplexer_95 (
    .in0(multiplexer_55_out), .in1(multiplexer_63_out), .out(multiplexer_95_out), .sel(ShiftAmount[3]));
  Multiplexer multiplexer_96 (
    .in0(multiplexer_56_out), .in1(multiplexer_64_out), .out(multiplexer_96_out), .sel(ShiftAmount[3]));
  Multiplexer multiplexer_97 (
    .in0(multiplexer_57_out), .in1(multiplexer_65_out), .out(multiplexer_97_out), .sel(ShiftAmount[3]));
  Multiplexer multiplexer_98 (
    .in0(multiplexer_58_out), .in1(multiplexer_66_out), .out(multiplexer_98_out), .sel(ShiftAmount[3]));
  Multiplexer multiplexer_99 (
    .in0(multiplexer_59_out), .in1(multiplexer_67_out), .out(multiplexer_99_out), .sel(ShiftAmount[3]));
  Multiplexer multiplexer_100 (
    .in0(multiplexer_60_out), .in1(multiplexer_68_out), .out(multiplexer_100_out), .sel(ShiftAmount[3]));
  Multiplexer multiplexer_101 (
    .in0(multiplexer_61_out), .in1(multiplexer_69_out), .out(multiplexer_101_out), .sel(ShiftAmount[3]));
  Multiplexer multiplexer_102 (
    .in0(multiplexer_62_out), .in1(multiplexer_70_out), .out(multiplexer_102_out), .sel(ShiftAmount[3]));
  Multiplexer multiplexer_103 (
    .in0(multiplexer_63_out), .in1(multiplexer_71_out), .out(multiplexer_103_out), .sel(ShiftAmount[3]));
  Multiplexer multiplexer_104 (
    .in0(multiplexer_64_out), .in1(multiplexer_72_out), .out(multiplexer_104_out), .sel(ShiftAmount[3]));
  Multiplexer multiplexer_105 (
    .in0(multiplexer_65_out), .in1(multiplexer_73_out), .out(multiplexer_105_out), .sel(ShiftAmount[3]));
  Multiplexer multiplexer_106 (
    .in0(multiplexer_66_out), .in1(multiplexer_74_out), .out(multiplexer_106_out), .sel(ShiftAmount[3]));
  Multiplexer multiplexer_107 (
    .in0(multiplexer_67_out), .in1(multiplexer_75_out), .out(multiplexer_107_out), .sel(ShiftAmount[3]));
  Multiplexer multiplexer_108 (
    .in0(multiplexer_68_out), .in1(multiplexer_76_out), .out(multiplexer_108_out), .sel(ShiftAmount[3]));
  Multiplexer multiplexer_109 (
    .in0(multiplexer_69_out), .in1(multiplexer_77_out), .out(multiplexer_109_out), .sel(ShiftAmount[3]));
  Multiplexer multiplexer_110 (
    .in0(multiplexer_70_out), .in1(multiplexer_78_out), .out(multiplexer_110_out), .sel(ShiftAmount[3]));
  Multiplexer multiplexer_111 (
    .in0(multiplexer_71_out), .in1(multiplexer_79_out), .out(multiplexer_111_out), .sel(ShiftAmount[3]));
  Multiplexer multiplexer_112 (
    .in0(multiplexer_72_out), .in1(multiplexer_80_out), .out(multiplexer_112_out), .sel(ShiftAmount[3]));
  Multiplexer multiplexer_113 (
    .in0(multiplexer_73_out), .in1(multiplexer_81_out), .out(multiplexer_113_out), .sel(ShiftAmount[3]));
  Multiplexer multiplexer_114 (
    .in0(multiplexer_74_out), .in1(multiplexer_82_out), .out(multiplexer_114_out), .sel(ShiftAmount[3]));
  Multiplexer multiplexer_115 (
    .in0(multiplexer_75_out), .in1(multiplexer_83_out), .out(multiplexer_115_out), .sel(ShiftAmount[3]));
  Multiplexer multiplexer_116 (
    .in0(multiplexer_76_out), .in1(multiplexer_84_out), .out(multiplexer_116_out), .sel(ShiftAmount[3]));
  Multiplexer multiplexer_117 (
    .in0(multiplexer_77_out), .in1(multiplexer_85_out), .out(multiplexer_117_out), .sel(ShiftAmount[3]));
  Multiplexer multiplexer_118 (
    .in0(multiplexer_78_out), .in1(multiplexer_86_out), .out(multiplexer_118_out), .sel(ShiftAmount[3]));
  Multiplexer multiplexer_119 (
    .in0(multiplexer_79_out), .in1(multiplexer_87_out), .out(multiplexer_119_out), .sel(ShiftAmount[3]));
  Multiplexer multiplexer_120 (
    .in0(multiplexer_80_out), .in1(multiplexer_88_out), .out(multiplexer_120_out), .sel(ShiftAmount[3]));
  Multiplexer multiplexer_121 (
    .in0(multiplexer_81_out), .in1(multiplexer_89_out), .out(multiplexer_121_out), .sel(ShiftAmount[3]));
  Multiplexer multiplexer_122 (
    .in0(multiplexer_1_out), .in1(multiplexer_90_out), .out(multiplexer_122_out), .sel(Rotate));
  Multiplexer multiplexer_123 (
    .in0(multiplexer_1_out), .in1(multiplexer_91_out), .out(multiplexer_123_out), .sel(Rotate));
  Multiplexer multiplexer_124 (
    .in0(multiplexer_1_out), .in1(multiplexer_92_out), .out(multiplexer_124_out), .sel(Rotate));
  Multiplexer multiplexer_125 (
    .in0(multiplexer_1_out), .in1(multiplexer_93_out), .out(multiplexer_125_out), .sel(Rotate));
  Multiplexer multiplexer_126 (
    .in0(multiplexer_90_out), .in1(multiplexer_94_out), .out(multiplexer_126_out), .sel(ShiftAmount[2]));
  Multiplexer multiplexer_127 (
    .in0(multiplexer_91_out), .in1(multiplexer_95_out), .out(multiplexer_127_out), .sel(ShiftAmount[2]));
  Multiplexer multiplexer_128 (
    .in0(multiplexer_92_out), .in1(multiplexer_96_out), .out(multiplexer_128_out), .sel(ShiftAmount[2]));
  Multiplexer multiplexer_129 (
    .in0(multiplexer_93_out), .in1(multiplexer_97_out), .out(multiplexer_129_out), .sel(ShiftAmount[2]));
  Multiplexer multiplexer_130 (
    .in0(multiplexer_94_out), .in1(multiplexer_98_out), .out(multiplexer_130_out), .sel(ShiftAmount[2]));
  Multiplexer multiplexer_131 (
    .in0(multiplexer_95_out), .in1(multiplexer_99_out), .out(multiplexer_131_out), .sel(ShiftAmount[2]));
  Multiplexer multiplexer_132 (
    .in0(multiplexer_96_out), .in1(multiplexer_100_out), .out(multiplexer_132_out), .sel(ShiftAmount[2]));
  Multiplexer multiplexer_133 (
    .in0(multiplexer_97_out), .in1(multiplexer_101_out), .out(multiplexer_133_out), .sel(ShiftAmount[2]));
  Multiplexer multiplexer_134 (
    .in0(multiplexer_98_out), .in1(multiplexer_102_out), .out(multiplexer_134_out), .sel(ShiftAmount[2]));
  Multiplexer multiplexer_135 (
    .in0(multiplexer_99_out), .in1(multiplexer_103_out), .out(multiplexer_135_out), .sel(ShiftAmount[2]));
  Multiplexer multiplexer_136 (
    .in0(multiplexer_100_out), .in1(multiplexer_104_out), .out(multiplexer_136_out), .sel(ShiftAmount[2]));
  Multiplexer multiplexer_137 (
    .in0(multiplexer_101_out), .in1(multiplexer_105_out), .out(multiplexer_137_out), .sel(ShiftAmount[2]));
  Multiplexer multiplexer_138 (
    .in0(multiplexer_102_out), .in1(multiplexer_106_out), .out(multiplexer_138_out), .sel(ShiftAmount[2]));
  Multiplexer multiplexer_139 (
    .in0(multiplexer_103_out), .in1(multiplexer_107_out), .out(multiplexer_139_out), .sel(ShiftAmount[2]));
  Multiplexer multiplexer_140 (
    .in0(multiplexer_104_out), .in1(multiplexer_108_out), .out(multiplexer_140_out), .sel(ShiftAmount[2]));
  Multiplexer multiplexer_141 (
    .in0(multiplexer_105_out), .in1(multiplexer_109_out), .out(multiplexer_141_out), .sel(ShiftAmount[2]));
  Multiplexer multiplexer_142 (
    .in0(multiplexer_106_out), .in1(multiplexer_110_out), .out(multiplexer_142_out), .sel(ShiftAmount[2]));
  Multiplexer multiplexer_143 (
    .in0(multiplexer_107_out), .in1(multiplexer_111_out), .out(multiplexer_143_out), .sel(ShiftAmount[2]));
  Multiplexer multiplexer_144 (
    .in0(multiplexer_108_out), .in1(multiplexer_112_out), .out(multiplexer_144_out), .sel(ShiftAmount[2]));
  Multiplexer multiplexer_145 (
    .in0(multiplexer_109_out), .in1(multiplexer_113_out), .out(multiplexer_145_out), .sel(ShiftAmount[2]));
  Multiplexer multiplexer_146 (
    .in0(multiplexer_110_out), .in1(multiplexer_114_out), .out(multiplexer_146_out), .sel(ShiftAmount[2]));
  Multiplexer multiplexer_147 (
    .in0(multiplexer_111_out), .in1(multiplexer_115_out), .out(multiplexer_147_out), .sel(ShiftAmount[2]));
  Multiplexer multiplexer_148 (
    .in0(multiplexer_112_out), .in1(multiplexer_116_out), .out(multiplexer_148_out), .sel(ShiftAmount[2]));
  Multiplexer multiplexer_149 (
    .in0(multiplexer_113_out), .in1(multiplexer_117_out), .out(multiplexer_149_out), .sel(ShiftAmount[2]));
  Multiplexer multiplexer_150 (
    .in0(multiplexer_114_out), .in1(multiplexer_118_out), .out(multiplexer_150_out), .sel(ShiftAmount[2]));
  Multiplexer multiplexer_151 (
    .in0(multiplexer_115_out), .in1(multiplexer_119_out), .out(multiplexer_151_out), .sel(ShiftAmount[2]));
  Multiplexer multiplexer_152 (
    .in0(multiplexer_116_out), .in1(multiplexer_120_out), .out(multiplexer_152_out), .sel(ShiftAmount[2]));
  Multiplexer multiplexer_153 (
    .in0(multiplexer_117_out), .in1(multiplexer_121_out), .out(multiplexer_153_out), .sel(ShiftAmount[2]));
  Multiplexer multiplexer_154 (
    .in0(multiplexer_118_out), .in1(multiplexer_122_out), .out(multiplexer_154_out), .sel(ShiftAmount[2]));
  Multiplexer multiplexer_155 (
    .in0(multiplexer_119_out), .in1(multiplexer_123_out), .out(multiplexer_155_out), .sel(ShiftAmount[2]));
  Multiplexer multiplexer_156 (
    .in0(multiplexer_120_out), .in1(multiplexer_124_out), .out(multiplexer_156_out), .sel(ShiftAmount[2]));
  Multiplexer multiplexer_157 (
    .in0(multiplexer_121_out), .in1(multiplexer_125_out), .out(multiplexer_157_out), .sel(ShiftAmount[2]));
  Multiplexer multiplexer_158 (
    .in0(multiplexer_1_out), .in1(multiplexer_126_out), .out(multiplexer_158_out), .sel(Rotate));
  Multiplexer multiplexer_159 (
    .in0(multiplexer_1_out), .in1(multiplexer_127_out), .out(multiplexer_159_out), .sel(Rotate));
  Multiplexer multiplexer_160 (
    .in0(multiplexer_126_out), .in1(multiplexer_128_out), .out(multiplexer_160_out), .sel(ShiftAmount[1]));
  Multiplexer multiplexer_161 (
    .in0(multiplexer_127_out), .in1(multiplexer_129_out), .out(multiplexer_161_out), .sel(ShiftAmount[1]));
  Multiplexer multiplexer_162 (
    .in0(multiplexer_128_out), .in1(multiplexer_130_out), .out(multiplexer_162_out), .sel(ShiftAmount[1]));
  Multiplexer multiplexer_163 (
    .in0(multiplexer_129_out), .in1(multiplexer_131_out), .out(multiplexer_163_out), .sel(ShiftAmount[1]));
  Multiplexer multiplexer_164 (
    .in0(multiplexer_130_out), .in1(multiplexer_132_out), .out(multiplexer_164_out), .sel(ShiftAmount[1]));
  Multiplexer multiplexer_165 (
    .in0(multiplexer_131_out), .in1(multiplexer_133_out), .out(multiplexer_165_out), .sel(ShiftAmount[1]));
  Multiplexer multiplexer_166 (
    .in0(multiplexer_132_out), .in1(multiplexer_134_out), .out(multiplexer_166_out), .sel(ShiftAmount[1]));
  Multiplexer multiplexer_167 (
    .in0(multiplexer_133_out), .in1(multiplexer_135_out), .out(multiplexer_167_out), .sel(ShiftAmount[1]));
  Multiplexer multiplexer_168 (
    .in0(multiplexer_134_out), .in1(multiplexer_136_out), .out(multiplexer_168_out), .sel(ShiftAmount[1]));
  Multiplexer multiplexer_169 (
    .in0(multiplexer_135_out), .in1(multiplexer_137_out), .out(multiplexer_169_out), .sel(ShiftAmount[1]));
  Multiplexer multiplexer_170 (
    .in0(multiplexer_136_out), .in1(multiplexer_138_out), .out(multiplexer_170_out), .sel(ShiftAmount[1]));
  Multiplexer multiplexer_171 (
    .in0(multiplexer_137_out), .in1(multiplexer_139_out), .out(multiplexer_171_out), .sel(ShiftAmount[1]));
  Multiplexer multiplexer_172 (
    .in0(multiplexer_138_out), .in1(multiplexer_140_out), .out(multiplexer_172_out), .sel(ShiftAmount[1]));
  Multiplexer multiplexer_173 (
    .in0(multiplexer_139_out), .in1(multiplexer_141_out), .out(multiplexer_173_out), .sel(ShiftAmount[1]));
  Multiplexer multiplexer_174 (
    .in0(multiplexer_140_out), .in1(multiplexer_142_out), .out(multiplexer_174_out), .sel(ShiftAmount[1]));
  Multiplexer multiplexer_175 (
    .in0(multiplexer_141_out), .in1(multiplexer_143_out), .out(multiplexer_175_out), .sel(ShiftAmount[1]));
  Multiplexer multiplexer_176 (
    .in0(multiplexer_142_out), .in1(multiplexer_144_out), .out(multiplexer_176_out), .sel(ShiftAmount[1]));
  Multiplexer multiplexer_177 (
    .in0(multiplexer_143_out), .in1(multiplexer_145_out), .out(multiplexer_177_out), .sel(ShiftAmount[1]));
  Multiplexer multiplexer_178 (
    .in0(multiplexer_144_out), .in1(multiplexer_146_out), .out(multiplexer_178_out), .sel(ShiftAmount[1]));
  Multiplexer multiplexer_179 (
    .in0(multiplexer_145_out), .in1(multiplexer_147_out), .out(multiplexer_179_out), .sel(ShiftAmount[1]));
  Multiplexer multiplexer_180 (
    .in0(multiplexer_146_out), .in1(multiplexer_148_out), .out(multiplexer_180_out), .sel(ShiftAmount[1]));
  Multiplexer multiplexer_181 (
    .in0(multiplexer_147_out), .in1(multiplexer_149_out), .out(multiplexer_181_out), .sel(ShiftAmount[1]));
  Multiplexer multiplexer_182 (
    .in0(multiplexer_148_out), .in1(multiplexer_150_out), .out(multiplexer_182_out), .sel(ShiftAmount[1]));
  Multiplexer multiplexer_183 (
    .in0(multiplexer_149_out), .in1(multiplexer_151_out), .out(multiplexer_183_out), .sel(ShiftAmount[1]));
  Multiplexer multiplexer_184 (
    .in0(multiplexer_150_out), .in1(multiplexer_152_out), .out(multiplexer_184_out), .sel(ShiftAmount[1]));
  Multiplexer multiplexer_185 (
    .in0(multiplexer_151_out), .in1(multiplexer_153_out), .out(multiplexer_185_out), .sel(ShiftAmount[1]));
  Multiplexer multiplexer_186 (
    .in0(multiplexer_152_out), .in1(multiplexer_154_out), .out(multiplexer_186_out), .sel(ShiftAmount[1]));
  Multiplexer multiplexer_187 (
    .in0(multiplexer_153_out), .in1(multiplexer_155_out), .out(multiplexer_187_out), .sel(ShiftAmount[1]));
  Multiplexer multiplexer_188 (
    .in0(multiplexer_154_out), .in1(multiplexer_156_out), .out(multiplexer_188_out), .sel(ShiftAmount[1]));
  Multiplexer multiplexer_189 (
    .in0(multiplexer_155_out), .in1(multiplexer_157_out), .out(multiplexer_189_out), .sel(ShiftAmount[1]));
  Multiplexer multiplexer_190 (
    .in0(multiplexer_156_out), .in1(multiplexer_158_out), .out(multiplexer_190_out), .sel(ShiftAmount[1]));
  Multiplexer multiplexer_191 (
    .in0(multiplexer_157_out), .in1(multiplexer_159_out), .out(multiplexer_191_out), .sel(ShiftAmount[1]));
  Multiplexer multiplexer_192 (
    .in0(multiplexer_160_out), .in1(multiplexer_161_out), .out(multiplexer_192_out), .sel(ShiftAmount[0]));
  Multiplexer multiplexer_193 (
    .in0(multiplexer_161_out), .in1(multiplexer_162_out), .out(multiplexer_193_out), .sel(ShiftAmount[0]));
  Multiplexer multiplexer_194 (
    .in0(multiplexer_162_out), .in1(multiplexer_163_out), .out(multiplexer_194_out), .sel(ShiftAmount[0]));
  Multiplexer multiplexer_195 (
    .in0(multiplexer_163_out), .in1(multiplexer_164_out), .out(multiplexer_195_out), .sel(ShiftAmount[0]));
  Multiplexer multiplexer_196 (
    .in0(multiplexer_164_out), .in1(multiplexer_165_out), .out(multiplexer_196_out), .sel(ShiftAmount[0]));
  Multiplexer multiplexer_197 (
    .in0(multiplexer_165_out), .in1(multiplexer_166_out), .out(multiplexer_197_out), .sel(ShiftAmount[0]));
  Multiplexer multiplexer_198 (
    .in0(multiplexer_166_out), .in1(multiplexer_167_out), .out(multiplexer_198_out), .sel(ShiftAmount[0]));
  Multiplexer multiplexer_199 (
    .in0(multiplexer_167_out), .in1(multiplexer_168_out), .out(multiplexer_199_out), .sel(ShiftAmount[0]));
  Multiplexer multiplexer_200 (
    .in0(multiplexer_168_out), .in1(multiplexer_169_out), .out(multiplexer_200_out), .sel(ShiftAmount[0]));
  Multiplexer multiplexer_201 (
    .in0(multiplexer_169_out), .in1(multiplexer_170_out), .out(multiplexer_201_out), .sel(ShiftAmount[0]));
  Multiplexer multiplexer_202 (
    .in0(multiplexer_170_out), .in1(multiplexer_171_out), .out(multiplexer_202_out), .sel(ShiftAmount[0]));
  Multiplexer multiplexer_203 (
    .in0(multiplexer_171_out), .in1(multiplexer_172_out), .out(multiplexer_203_out), .sel(ShiftAmount[0]));
  Multiplexer multiplexer_204 (
    .in0(multiplexer_172_out), .in1(multiplexer_173_out), .out(multiplexer_204_out), .sel(ShiftAmount[0]));
  Multiplexer multiplexer_205 (
    .in0(multiplexer_173_out), .in1(multiplexer_174_out), .out(multiplexer_205_out), .sel(ShiftAmount[0]));
  Multiplexer multiplexer_206 (
    .in0(multiplexer_174_out), .in1(multiplexer_175_out), .out(multiplexer_206_out), .sel(ShiftAmount[0]));
  Multiplexer multiplexer_207 (
    .in0(multiplexer_175_out), .in1(multiplexer_176_out), .out(multiplexer_207_out), .sel(ShiftAmount[0]));
  Multiplexer multiplexer_208 (
    .in0(multiplexer_176_out), .in1(multiplexer_177_out), .out(multiplexer_208_out), .sel(ShiftAmount[0]));
  Multiplexer multiplexer_209 (
    .in0(multiplexer_177_out), .in1(multiplexer_178_out), .out(multiplexer_209_out), .sel(ShiftAmount[0]));
  Multiplexer multiplexer_210 (
    .in0(multiplexer_178_out), .in1(multiplexer_179_out), .out(multiplexer_210_out), .sel(ShiftAmount[0]));
  Multiplexer multiplexer_211 (
    .in0(multiplexer_179_out), .in1(multiplexer_180_out), .out(multiplexer_211_out), .sel(ShiftAmount[0]));
  Multiplexer multiplexer_212 (
    .in0(multiplexer_180_out), .in1(multiplexer_181_out), .out(multiplexer_212_out), .sel(ShiftAmount[0]));
  Multiplexer multiplexer_213 (
    .in0(multiplexer_181_out), .in1(multiplexer_182_out), .out(multiplexer_213_out), .sel(ShiftAmount[0]));
  Multiplexer multiplexer_214 (
    .in0(multiplexer_182_out), .in1(multiplexer_183_out), .out(multiplexer_214_out), .sel(ShiftAmount[0]));
  Multiplexer multiplexer_215 (
    .in0(multiplexer_183_out), .in1(multiplexer_184_out), .out(multiplexer_215_out), .sel(ShiftAmount[0]));
  Multiplexer multiplexer_216 (
    .in0(multiplexer_184_out), .in1(multiplexer_185_out), .out(multiplexer_216_out), .sel(ShiftAmount[0]));
  Multiplexer multiplexer_217 (
    .in0(multiplexer_185_out), .in1(multiplexer_186_out), .out(multiplexer_217_out), .sel(ShiftAmount[0]));
  Multiplexer multiplexer_218 (
    .in0(multiplexer_186_out), .in1(multiplexer_187_out), .out(multiplexer_218_out), .sel(ShiftAmount[0]));
  Multiplexer multiplexer_219 (
    .in0(multiplexer_187_out), .in1(multiplexer_188_out), .out(multiplexer_219_out), .sel(ShiftAmount[0]));
  Multiplexer multiplexer_220 (
    .in0(multiplexer_188_out), .in1(multiplexer_189_out), .out(multiplexer_220_out), .sel(ShiftAmount[0]));
  Multiplexer multiplexer_221 (
    .in0(multiplexer_189_out), .in1(multiplexer_190_out), .out(multiplexer_221_out), .sel(ShiftAmount[0]));
  Multiplexer multiplexer_222 (
    .in0(multiplexer_190_out), .in1(multiplexer_191_out), .out(multiplexer_222_out), .sel(ShiftAmount[0]));
  Multiplexer multiplexer_223 (
    .in0(multiplexer_191_out), .in1(multiplexer_224_out), .out(multiplexer_223_out), .sel(ShiftAmount[0]));
  Multiplexer multiplexer_224 (
    .in0(multiplexer_1_out), .in1(multiplexer_160_out), .out(multiplexer_224_out), .sel(Rotate));
  Multiplexer multiplexer_225 (.in0(multiplexer_192_out), .in1(multiplexer_223_out), .out(DataOut[0]), .sel(Direction));
  Multiplexer multiplexer_226 (.in0(multiplexer_193_out), .in1(multiplexer_222_out), .out(DataOut[1]), .sel(Direction));
  Multiplexer multiplexer_227 (.in0(multiplexer_194_out), .in1(multiplexer_221_out), .out(DataOut[2]), .sel(Direction));
  Multiplexer multiplexer_228 (.in0(multiplexer_195_out), .in1(multiplexer_220_out), .out(DataOut[3]), .sel(Direction));
  Multiplexer multiplexer_229 (.in0(multiplexer_196_out), .in1(multiplexer_219_out), .out(DataOut[4]), .sel(Direction));
  Multiplexer multiplexer_230 (.in0(multiplexer_197_out), .in1(multiplexer_218_out), .out(DataOut[5]), .sel(Direction));
  Multiplexer multiplexer_231 (.in0(multiplexer_198_out), .in1(multiplexer_217_out), .out(DataOut[6]), .sel(Direction));
  Multiplexer multiplexer_232 (.in0(multiplexer_199_out), .in1(multiplexer_216_out), .out(DataOut[7]), .sel(Direction));
  Multiplexer multiplexer_233 (.in0(multiplexer_200_out), .in1(multiplexer_215_out), .out(DataOut[8]), .sel(Direction));
  Multiplexer multiplexer_234 (.in0(multiplexer_201_out), .in1(multiplexer_214_out), .out(DataOut[9]), .sel(Direction));
  Multiplexer multiplexer_235 (
    .in0(multiplexer_202_out), .in1(multiplexer_213_out), .out(DataOut[10]), .sel(Direction));
  Multiplexer multiplexer_236 (
    .in0(multiplexer_203_out), .in1(multiplexer_212_out), .out(DataOut[11]), .sel(Direction));
  Multiplexer multiplexer_237 (
    .in0(multiplexer_204_out), .in1(multiplexer_211_out), .out(DataOut[12]), .sel(Direction));
  Multiplexer multiplexer_238 (
    .in0(multiplexer_205_out), .in1(multiplexer_210_out), .out(DataOut[13]), .sel(Direction));
  Multiplexer multiplexer_239 (
    .in0(multiplexer_206_out), .in1(multiplexer_209_out), .out(DataOut[14]), .sel(Direction));
  Multiplexer multiplexer_240 (
    .in0(multiplexer_207_out), .in1(multiplexer_208_out), .out(DataOut[15]), .sel(Direction));
  Multiplexer multiplexer_241 (
    .in0(multiplexer_208_out), .in1(multiplexer_207_out), .out(DataOut[16]), .sel(Direction));
  Multiplexer multiplexer_242 (
    .in0(multiplexer_209_out), .in1(multiplexer_206_out), .out(DataOut[17]), .sel(Direction));
  Multiplexer multiplexer_243 (
    .in0(multiplexer_210_out), .in1(multiplexer_205_out), .out(DataOut[18]), .sel(Direction));
  Multiplexer multiplexer_244 (
    .in0(multiplexer_211_out), .in1(multiplexer_204_out), .out(DataOut[19]), .sel(Direction));
  Multiplexer multiplexer_245 (
    .in0(multiplexer_212_out), .in1(multiplexer_203_out), .out(DataOut[20]), .sel(Direction));
  Multiplexer multiplexer_246 (
    .in0(multiplexer_213_out), .in1(multiplexer_202_out), .out(DataOut[21]), .sel(Direction));
  Multiplexer multiplexer_247 (
    .in0(multiplexer_214_out), .in1(multiplexer_201_out), .out(DataOut[22]), .sel(Direction));
  Multiplexer multiplexer_248 (
    .in0(multiplexer_215_out), .in1(multiplexer_200_out), .out(DataOut[23]), .sel(Direction));
  Multiplexer multiplexer_249 (
    .in0(multiplexer_216_out), .in1(multiplexer_199_out), .out(DataOut[24]), .sel(Direction));
  Multiplexer multiplexer_250 (
    .in0(multiplexer_217_out), .in1(multiplexer_198_out), .out(DataOut[25]), .sel(Direction));
  Multiplexer multiplexer_251 (
    .in0(multiplexer_218_out), .in1(multiplexer_197_out), .out(DataOut[26]), .sel(Direction));
  Multiplexer multiplexer_252 (
    .in0(multiplexer_219_out), .in1(multiplexer_196_out), .out(DataOut[27]), .sel(Direction));
  Multiplexer multiplexer_253 (
    .in0(multiplexer_220_out), .in1(multiplexer_195_out), .out(DataOut[28]), .sel(Direction));
  Multiplexer multiplexer_254 (
    .in0(multiplexer_221_out), .in1(multiplexer_194_out), .out(DataOut[29]), .sel(Direction));
  Multiplexer multiplexer_255 (
    .in0(multiplexer_222_out), .in1(multiplexer_193_out), .out(DataOut[30]), .sel(Direction));
  Multiplexer multiplexer_256 (
    .in0(multiplexer_223_out), .in1(multiplexer_192_out), .out(DataOut[31]), .sel(Direction));
endmodule
module ALU32Bit (
  input  [31:0] A,
  input  [31:0] B,
  input  [15:0] I,
  input  Cin,
  input  ImmediateSel,
  input  [4:0] ShiftAmount,
  input  [5:0] Sel,
  output Cout,
  output [31:0] DataOut,
  output CmpDataOut
);

  wire arithmeticunit_1_coutsubless;
  wire [4:0] multiplexer_2_out;
  wire [31:0] arithmeticunit_1_q, logicunit_1_q, multiplexer_1_out, shifterunit_1_dataout;

  Multiplexer #(.width(32)) multiplexer_1 (.in0(B), .in1({{16{1'b0}}, I}), .out(multiplexer_1_out), .sel(ImmediateSel));
  Multiplexer #(.width(5)) multiplexer_2 (.in0(B[4:0]), .in1(I[4:0]), .out(multiplexer_2_out), .sel(ImmediateSel));
  LogicUnit logicunit_1 (.A(A), .B(multiplexer_1_out), .Sel(Sel[2:0]), .Q(logicunit_1_q));
  ArithmeticUnit arithmeticunit_1 (
    .Sel(Sel[0]), .Cin(Cin), .A(A), .B(multiplexer_1_out), .Q(arithmeticunit_1_q), .Cout(Cout),
    .CoutSUBLESS(arithmeticunit_1_coutsubless));
  ComparatorUnit comparatorunit_1 (
    .Sel(Sel[2:0]), .A(A), .B(multiplexer_1_out), .CoutSUBLESS(arithmeticunit_1_coutsubless),
    .TrueFalse(CmpDataOut));
  ShifterUnit shifterunit_1 (
    .DataIn(A), .Arithmetic(Sel[2]), .Rotate(Sel[1]), .Direction(Sel[0]), .ShiftAmount(multiplexer_2_out),
    .DataOut(shifterunit_1_dataout));  // open: FillSelect, Flip
  Multiplexer #(.select(5), .width(32)) multiplexer_3 (
    .in1(logicunit_1_q), .in2(logicunit_1_q), .in3(logicunit_1_q), .in4(logicunit_1_q), .in5(logicunit_1_q),
    .in6(logicunit_1_q), .in7(logicunit_1_q), .in8(arithmeticunit_1_q), .in9(arithmeticunit_1_q),
    .in16({{31{1'b0}}, CmpDataOut}), .in17({{31{1'b0}}, CmpDataOut}), .in18({{31{1'b0}}, CmpDataOut}),
    .in19({{31{1'b0}}, CmpDataOut}), .in20({{31{1'b0}}, CmpDataOut}), .in21({{31{1'b0}}, CmpDataOut}),
    .in24(shifterunit_1_dataout), .in25(shifterunit_1_dataout), .in26(shifterunit_1_dataout),
    .in27(shifterunit_1_dataout), .in28(shifterunit_1_dataout), .in29(shifterunit_1_dataout), .out(DataOut),
    .sel(Sel[4:0]));  // open: in0, in10, in11, in12, in13, in14, in15, in22, in23, in30, in31
endmodule

module IntegerUnit (
  input  [31:0] A,
  input  [31:0] B,
  input  [15:0] I,
  input  [5:0] Sel,
  input  [4:0] SA,
  input  ISel,
  input  Clk,
  output CmpDataOut,
  output [31:0] IntegerResult
);

  wire and_1_out, and_2_out, and_3_out, multiplexer_1_out, not_1_out, not_2_out, not_3_out, not_4_out,
       not_5_out, not_6_out, not_7_out, or_1_out;
  wire [1:0] and_4_out;
  wire [31:0] alu32bit_1_dataout, multiplexer_2_out, multiplier32bit_1_product, reghi_1_ausgabe,
       reglo_1_ausgabe, undriven, undriven_2;

  not not_1 (not_1_out, Sel[0]);
  not not_2 (not_2_out, Sel[2]);
  not not_3 (not_3_out, Sel[4]);
  not not_4 (not_4_out, Sel[5]);
  Multiplier32Bit multiplier32bit_1 (.A(A), .B(B), .Product(multiplier32bit_1_product));
  ALU32Bit alu32bit_1 (
    .ImmediateSel(ISel), .I(I), .ShiftAmount(SA), .Sel(Sel), .A(A), .B(B), .CmpDataOut(CmpDataOut),
    .DataOut(alu32bit_1_dataout));  // open: Cin, Cout
  and and_1 (and_1_out, not_1_out, Sel[1], not_2_out, Sel[3], not_3_out, not_4_out);
  or or_1 (or_1_out, and_1_out, and_2_out);
  and and_2 (and_2_out, Sel[0], Sel[1], not_2_out, Sel[3], not_3_out, not_4_out);
  Multiplexer multiplexer_1 (.in0(1'b0), .in1(or_1_out), .out(multiplexer_1_out), .sel(Clk));
  RegLO reglo_1 (.Clk(multiplexer_1_out), .Eingabe(undriven), .Ausgabe(reglo_1_ausgabe));
  RegHI reghi_1 (.Clk(multiplexer_1_out), .Eingabe(undriven_2), .Ausgabe(reghi_1_ausgabe));
  not not_5 (not_5_out, Sel[0]);
  not not_6 (not_6_out, Sel[2]);
  not not_7 (not_7_out, Sel[5]);
  and and_3 (and_3_out, not_5_out, Sel[1], not_6_out, Sel[3], Sel[4], not_7_out);
  and and_4 (and_4_out[0], Sel[0], Sel[1], not_6_out, Sel[3], Sel[4], not_7_out);
  or or_2 (and_4_out[1], and_3_out, and_4_out[0]);
  Multiplexer #(.select(5), .width(32)) multiplexer_2 (
    .in1(alu32bit_1_dataout), .in3(alu32bit_1_dataout), .in4(alu32bit_1_dataout), .in5(alu32bit_1_dataout),
    .in6(alu32bit_1_dataout), .in7(alu32bit_1_dataout), .in8(alu32bit_1_dataout), .in9(alu32bit_1_dataout),
    .in10(multiplier32bit_1_product), .in16(alu32bit_1_dataout), .in17(alu32bit_1_dataout),
    .in18(alu32bit_1_dataout), .in19(alu32bit_1_dataout), .in20(alu32bit_1_dataout),
    .in21(alu32bit_1_dataout), .in23({I, {16{1'b0}}}), .in24(alu32bit_1_dataout), .in25(alu32bit_1_dataout),
    .in28(alu32bit_1_dataout), .in29(alu32bit_1_dataout), .out(multiplexer_2_out), .sel(Sel[4:0]));  // open: in0, in2, in11, in12, in13, in14, in15, in22, in26, in27, in30, in31
  Multiplexer #(.select(2), .width(32)) multiplexer_3 (
    .in0(multiplexer_2_out), .in2(reghi_1_ausgabe), .in3(reglo_1_ausgabe), .out(IntegerResult),
    .sel(and_4_out));  // open: in1
endmodule

module ControlUnit (
  input  [31:0] Instruction,
  output [4:0] rs,
  output [4:0] rt,
  output [4:0] rd,
  output [4:0] sa,
  output [15:0] branchto,
  output [15:0] i,
  output [25:0] jumpto,
  output [5:0] fct,
  output ISel,
  output jump,
  output Float,
  output IntWrite,
  output FloatWrite,
  output branch,
  output store,
  output load
);

  wire instructiontypes_1_msb, muldiv_1_mul_or_div;
  wire [2:0] instructiontypes_1_r;
  wire [25:0] demultiplexer_1_out1;
  wire [25:16] demultiplexer_1_out4;

  xor xor_1 (Float, instructiontypes_1_msb, demultiplexer_1_out1[5]);
  MulDiv muldiv_1 (.OpCode(demultiplexer_1_out1[5:0]), .Mul_or_Div(muldiv_1_mul_or_div));
  Branches branches_1 (.OpCode(Instruction[31:26]), .Branch(branch));
  LoadStore loadstore_1 (.OpCode(Instruction[31:26]), .store(store), .load(load));
  InstructionTypes instructiontypes_1 (
    .OpCode(Instruction[31:26]), .MSB(instructiontypes_1_msb), .R(instructiontypes_1_r[0]), .J(jump),
    .I(instructiontypes_1_r[2]));
  Demultiplexer #(.select(3), .width(26)) demultiplexer_1 (
    .out1({demultiplexer_1_out1[25:11], sa, demultiplexer_1_out1[5:0]}), .out2(jumpto),
    .out4({demultiplexer_1_out4, branchto}), .in(Instruction[25:0]),
    .sel({instructiontypes_1_r[2], jump, instructiontypes_1_r[0]}));  // open: out0, out3, out5, out6, out7
  WriteEnable writeenable_1 (
    .iType(instructiontypes_1_r[2]), .Funct(demultiplexer_1_out1[5:0]), .OpCode(Instruction[31:26]),
    .MulDiv(muldiv_1_mul_or_div), .Branch(branch), .Jump(jump), .Store(store), .Float(Float),
    .IntWrite(IntWrite), .FloatWrite(FloatWrite));
  Multiplexer multiplexer_1 (.in0(instructiontypes_1_r[2]), .in1(1'b0), .out(ISel), .sel(branch));
  assign rs = demultiplexer_1_out1[25:21] ^ demultiplexer_1_out4[25:21];  // XOR_Gate xor_2, 5 bits wide
  Multiplexer #(.width(5)) multiplexer_2 (
    .in0(demultiplexer_1_out1[20:16]), .in1(demultiplexer_1_out4[20:16]), .out(rt),
    .sel(instructiontypes_1_r[2]));
  Multiplexer #(.width(5)) multiplexer_3 (
    .in0(demultiplexer_1_out1[15:11]), .in1(demultiplexer_1_out4[20:16]), .out(rd),
    .sel(instructiontypes_1_r[2]));
  Multiplexer #(.select(2), .width(6)) multiplexer_4 (
    .in0(demultiplexer_1_out1[5:0]), .in1(Instruction[31:26]), .in3(6'b001000), .out(fct),
    .sel({store, instructiontypes_1_r[2]}));  // open: in2

  assign i = branchto;

  // Notes on the sheet:
  //   OpCode
  //   isfloat
  //   rs
  //   rs
  //   rt
  //   rt
  //   instruction index
  //   rd
  //   sa
  //   i
  //   opcode for addi
  //   when storing
  //   fct
endmodule

module ProgramCounter (
  input  jump,
  input  [25:0] jumpto,
  input  [15:0] branchto,
  input  branch,
  input  Clk,
  input  CmpDataOut,
  output [9:0] instructionadress
);

  wire and_1_out, counter_1_carry, multiplexer_2_out, xor_1_out;
  wire [9:0] multiplexer_1_out;

  and and_1 (and_1_out, branch, CmpDataOut);
  xor xor_1 (xor_1_out, jump, and_1_out);
  Multiplexer #(.width(10)) multiplexer_1 (
    .in0(jumpto[9:0]), .in1(branchto[9:0]), .out(multiplexer_1_out), .sel(and_1_out));
  Counter #(.max('h3ff), .width(10)) counter_1 (
    .load(xor_1_out), .D(multiplexer_1_out), .Q(instructionadress), .carry(counter_1_carry),
    .clk(multiplexer_2_out));  // open: count, up, clr
  Multiplexer multiplexer_2 (.in0(Clk), .in1(1'b0), .out(multiplexer_2_out), .sel(counter_1_carry));

  // Notes on the sheet:
  //   if the comparison outputs 1, then branch
endmodule

module DataRAM (
  input  [31:0] DataIn,
  input  Clk,
  input  [4:0] WriteSel,
  input  [4:0] ReadSel,
  output [31:0] DataOut
);

  wire decoder_1_out0, decoder_1_out1, decoder_1_out2, decoder_1_out3, decoder_1_out4, decoder_1_out5,
       decoder_1_out6, decoder_1_out7, decoder_1_out8, decoder_1_out9, decoder_1_out10, decoder_1_out11,
       decoder_1_out12, decoder_1_out13, decoder_1_out14, decoder_1_out15, decoder_1_out16, decoder_1_out17,
       decoder_1_out18, decoder_1_out19, decoder_1_out20, decoder_1_out21, decoder_1_out22, decoder_1_out23,
       decoder_1_out24, decoder_1_out25, decoder_1_out26, decoder_1_out27, decoder_1_out28, decoder_1_out29,
       decoder_1_out30, decoder_1_out31;
  wire [31:0] reg32bit_1_ausgabe, reg32bit_2_ausgabe, reg32bit_3_ausgabe, reg32bit_4_ausgabe,
       reg32bit_5_ausgabe, reg32bit_6_ausgabe, reg32bit_7_ausgabe, reg32bit_8_ausgabe, reg32bit_9_ausgabe,
       reg32bit_10_ausgabe, reg32bit_11_ausgabe, reg32bit_12_ausgabe, reg32bit_13_ausgabe,
       reg32bit_14_ausgabe, reg32bit_15_ausgabe, reg32bit_16_ausgabe, reg32bit_17_ausgabe,
       reg32bit_18_ausgabe, reg32bit_19_ausgabe, reg32bit_20_ausgabe, reg32bit_21_ausgabe,
       reg32bit_22_ausgabe, reg32bit_23_ausgabe, reg32bit_24_ausgabe, reg32bit_25_ausgabe,
       reg32bit_26_ausgabe, reg32bit_27_ausgabe, reg32bit_28_ausgabe, reg32bit_29_ausgabe,
       reg32bit_30_ausgabe, reg32bit_31_ausgabe, reg32bit_32_ausgabe;

  Decoder #(.select(5)) decoder_1 (
    .out0(decoder_1_out0), .out1(decoder_1_out1), .out2(decoder_1_out2), .out3(decoder_1_out3),
    .out4(decoder_1_out4), .out5(decoder_1_out5), .out6(decoder_1_out6), .out7(decoder_1_out7),
    .out8(decoder_1_out8), .out9(decoder_1_out9), .out10(decoder_1_out10), .out11(decoder_1_out11),
    .out12(decoder_1_out12), .out13(decoder_1_out13), .out14(decoder_1_out14), .out15(decoder_1_out15),
    .out16(decoder_1_out16), .out17(decoder_1_out17), .out18(decoder_1_out18), .out19(decoder_1_out19),
    .out20(decoder_1_out20), .out21(decoder_1_out21), .out22(decoder_1_out22), .out23(decoder_1_out23),
    .out24(decoder_1_out24), .out25(decoder_1_out25), .out26(decoder_1_out26), .out27(decoder_1_out27),
    .out28(decoder_1_out28), .out29(decoder_1_out29), .out30(decoder_1_out30), .out31(decoder_1_out31),
    .sel(WriteSel));  // open: en
  Reg32Bit reg32bit_1 (.Eingabe(DataIn), .Clk(Clk), .Enable(decoder_1_out0), .Ausgabe(reg32bit_1_ausgabe));
  Reg32Bit reg32bit_2 (.Eingabe(DataIn), .Clk(Clk), .Enable(decoder_1_out2), .Ausgabe(reg32bit_2_ausgabe));
  Reg32Bit reg32bit_3 (.Eingabe(DataIn), .Clk(Clk), .Enable(decoder_1_out4), .Ausgabe(reg32bit_3_ausgabe));
  Reg32Bit reg32bit_4 (.Eingabe(DataIn), .Clk(Clk), .Enable(decoder_1_out6), .Ausgabe(reg32bit_4_ausgabe));
  Reg32Bit reg32bit_5 (.Eingabe(DataIn), .Clk(Clk), .Enable(decoder_1_out8), .Ausgabe(reg32bit_5_ausgabe));
  Reg32Bit reg32bit_6 (.Eingabe(DataIn), .Clk(Clk), .Enable(decoder_1_out10), .Ausgabe(reg32bit_6_ausgabe));
  Reg32Bit reg32bit_7 (.Eingabe(DataIn), .Clk(Clk), .Enable(decoder_1_out12), .Ausgabe(reg32bit_7_ausgabe));
  Reg32Bit reg32bit_8 (.Eingabe(DataIn), .Clk(Clk), .Enable(decoder_1_out14), .Ausgabe(reg32bit_8_ausgabe));
  Reg32Bit reg32bit_9 (.Eingabe(DataIn), .Clk(Clk), .Enable(decoder_1_out16), .Ausgabe(reg32bit_9_ausgabe));
  Reg32Bit reg32bit_10 (.Eingabe(DataIn), .Clk(Clk), .Enable(decoder_1_out18), .Ausgabe(reg32bit_10_ausgabe));
  Reg32Bit reg32bit_11 (.Eingabe(DataIn), .Clk(Clk), .Enable(decoder_1_out20), .Ausgabe(reg32bit_11_ausgabe));
  Reg32Bit reg32bit_12 (.Eingabe(DataIn), .Clk(Clk), .Enable(decoder_1_out22), .Ausgabe(reg32bit_12_ausgabe));
  Reg32Bit reg32bit_13 (.Eingabe(DataIn), .Clk(Clk), .Enable(decoder_1_out24), .Ausgabe(reg32bit_13_ausgabe));
  Reg32Bit reg32bit_14 (.Eingabe(DataIn), .Clk(Clk), .Enable(decoder_1_out26), .Ausgabe(reg32bit_14_ausgabe));
  Reg32Bit reg32bit_15 (.Eingabe(DataIn), .Clk(Clk), .Enable(decoder_1_out28), .Ausgabe(reg32bit_15_ausgabe));
  Reg32Bit reg32bit_16 (.Eingabe(DataIn), .Clk(Clk), .Enable(decoder_1_out30), .Ausgabe(reg32bit_16_ausgabe));
  Reg32Bit reg32bit_17 (.Eingabe(DataIn), .Clk(Clk), .Enable(decoder_1_out1), .Ausgabe(reg32bit_17_ausgabe));
  Reg32Bit reg32bit_18 (.Eingabe(DataIn), .Clk(Clk), .Enable(decoder_1_out3), .Ausgabe(reg32bit_18_ausgabe));
  Reg32Bit reg32bit_19 (.Eingabe(DataIn), .Clk(Clk), .Enable(decoder_1_out5), .Ausgabe(reg32bit_19_ausgabe));
  Reg32Bit reg32bit_20 (.Eingabe(DataIn), .Clk(Clk), .Enable(decoder_1_out7), .Ausgabe(reg32bit_20_ausgabe));
  Reg32Bit reg32bit_21 (.Eingabe(DataIn), .Clk(Clk), .Enable(decoder_1_out9), .Ausgabe(reg32bit_21_ausgabe));
  Reg32Bit reg32bit_22 (.Eingabe(DataIn), .Clk(Clk), .Enable(decoder_1_out11), .Ausgabe(reg32bit_22_ausgabe));
  Reg32Bit reg32bit_23 (.Eingabe(DataIn), .Clk(Clk), .Enable(decoder_1_out13), .Ausgabe(reg32bit_23_ausgabe));
  Reg32Bit reg32bit_24 (.Eingabe(DataIn), .Clk(Clk), .Enable(decoder_1_out15), .Ausgabe(reg32bit_24_ausgabe));
  Reg32Bit reg32bit_25 (.Eingabe(DataIn), .Clk(Clk), .Enable(decoder_1_out17), .Ausgabe(reg32bit_25_ausgabe));
  Reg32Bit reg32bit_26 (.Eingabe(DataIn), .Clk(Clk), .Enable(decoder_1_out19), .Ausgabe(reg32bit_26_ausgabe));
  Reg32Bit reg32bit_27 (.Eingabe(DataIn), .Clk(Clk), .Enable(decoder_1_out21), .Ausgabe(reg32bit_27_ausgabe));
  Reg32Bit reg32bit_28 (.Eingabe(DataIn), .Clk(Clk), .Enable(decoder_1_out23), .Ausgabe(reg32bit_28_ausgabe));
  Reg32Bit reg32bit_29 (.Eingabe(DataIn), .Clk(Clk), .Enable(decoder_1_out25), .Ausgabe(reg32bit_29_ausgabe));
  Reg32Bit reg32bit_30 (.Eingabe(DataIn), .Clk(Clk), .Enable(decoder_1_out27), .Ausgabe(reg32bit_30_ausgabe));
  Reg32Bit reg32bit_31 (.Eingabe(DataIn), .Clk(Clk), .Enable(decoder_1_out29), .Ausgabe(reg32bit_31_ausgabe));
  Reg32Bit reg32bit_32 (.Eingabe(DataIn), .Clk(Clk), .Enable(decoder_1_out31), .Ausgabe(reg32bit_32_ausgabe));
  Multiplexer #(.select(5), .width(32)) multiplexer_1 (
    .in0(reg32bit_1_ausgabe), .in1(reg32bit_17_ausgabe), .in2(reg32bit_2_ausgabe), .in3(reg32bit_18_ausgabe),
    .in4(reg32bit_3_ausgabe), .in5(reg32bit_19_ausgabe), .in6(reg32bit_4_ausgabe), .in7(reg32bit_20_ausgabe),
    .in8(reg32bit_5_ausgabe), .in9(reg32bit_21_ausgabe), .in10(reg32bit_6_ausgabe),
    .in11(reg32bit_22_ausgabe), .in12(reg32bit_7_ausgabe), .in13(reg32bit_23_ausgabe),
    .in14(reg32bit_8_ausgabe), .in15(reg32bit_24_ausgabe), .in16(reg32bit_9_ausgabe),
    .in17(reg32bit_25_ausgabe), .in18(reg32bit_10_ausgabe), .in19(reg32bit_26_ausgabe),
    .in20(reg32bit_11_ausgabe), .in21(reg32bit_27_ausgabe), .in22(reg32bit_12_ausgabe),
    .in23(reg32bit_28_ausgabe), .in24(reg32bit_13_ausgabe), .in25(reg32bit_29_ausgabe),
    .in26(reg32bit_14_ausgabe), .in27(reg32bit_30_ausgabe), .in28(reg32bit_15_ausgabe),
    .in29(reg32bit_31_ausgabe), .in30(reg32bit_16_ausgabe), .in31(reg32bit_32_ausgabe), .out(DataOut),
    .sel(ReadSel));
endmodule

module SevenSegment (
  input  [3:0] Data,
  output Aout,
  output Bout,
  output Cout,
  output Dout,
  output Eout,
  output Fout,
  output Gout
);

  wire and_1_out, and_2_out, and_3_out, and_4_out, and_5_out, and_6_out, and_7_out, and_8_out, and_9_out,
       and_10_out, and_11_out, and_12_out, and_13_out, and_14_out, and_15_out, and_16_out, not_1_out,
       not_2_out, not_3_out;

  not not_1 (not_1_out, Data[2]);
  not not_2 (not_2_out, Data[1]);
  not not_3 (not_3_out, Data[0]);
  and and_1 (and_1_out, Data[0], Data[2]);
  and and_2 (and_2_out, not_1_out, not_3_out);
  and and_3 (and_3_out, not_2_out, not_3_out);
  and and_4 (and_4_out, Data[1], Data[0]);
  and and_5 (and_5_out, not_1_out, not_3_out);
  and and_6 (and_6_out, Data[1], not_3_out);
  and and_7 (and_7_out, not_1_out, Data[1]);
  and and_8 (and_8_out, Data[2], not_2_out, Data[0]);
  and and_9 (and_9_out, not_3_out, Data[1]);
  and and_10 (and_10_out, not_3_out, not_1_out);
  and and_11 (and_11_out, not_3_out, not_2_out);
  and and_12 (and_12_out, Data[2], not_2_out);
  and and_13 (and_13_out, Data[2], not_3_out);
  and and_14 (and_14_out, Data[1], not_3_out);
  and and_15 (and_15_out, not_1_out, Data[1]);
  and and_16 (and_16_out, Data[2], not_2_out);
  or a (Aout, Data[3], Data[1], and_1_out, and_2_out);
  or b (Bout, Data[3], not_1_out, and_3_out, and_4_out);
  or c (Cout, not_2_out, Data[0], Data[2]);
  or d (Dout, Data[3], and_5_out, and_6_out, and_7_out, and_8_out);
  or e (Eout, and_9_out, and_10_out);
  or f (Fout, Data[3], and_11_out, and_12_out, and_13_out);
  or g (Gout, Data[3], and_14_out, and_15_out, and_16_out);
endmodule

module SevenSegmentROM (
  input  [3:0] in_1,
  output dot,
  output g,
  output f,
  output e,
  output d,
  output c,
  output b,
  output a
);

  ROM #(.addrWidth(4)) rom_1 (.addr(in_1), .data({a, b, c, d, e, f, g, dot}));

  // Notes on the sheet:
  //   contents of rom_1 (hex, n*v repeats v):
  //   fc 60 da f2 66 b6 be e0 fe f6 9e 8e 1c ce a b
endmodule

module DoubleDabbleCmp (
  input  [3:0] DataIn,
  output [3:0] DataOut
);

  wire comparator_1_eq, comparator_1_gt, or_1_out;
  wire [3:0] adder_1_out;

  Comparator #(.mode("unsigned"), .width(4)) comparator_1 (
    .a(DataIn), .b(4'b0101), .gt(comparator_1_gt), .eq(comparator_1_eq));  // open: lt
  Multiplexer #(.width(4)) multiplexer_1 (.in0(DataIn), .in1(adder_1_out), .out(DataOut), .sel(or_1_out));
  or or_1 (or_1_out, comparator_1_gt, comparator_1_eq);
  Adder #(.width(4)) adder_1 (.a(DataIn), .b(4'b0011), .out(adder_1_out));  // open: cin, cout
endmodule

module DoubleDabble10digit (
  input  [31:0] in_1,
  output [3:0] Billion,
  output [3:0] HundredMill,
  output [3:0] TenMill,
  output [3:0] Million,
  output [3:0] HundredK,
  output [3:0] TenK,
  output [3:0] Tausend,
  output [3:0] Hundred,
  output [3:0] Ten,
  output [3:0] One
);

  wire ddshifter4bit_3_shiftedbit, ddshifter4bit_4_shiftedbit, ddshifter4bit_5_shiftedbit,
       ddshifter4bit_6_shiftedbit, ddshifter4bit_7_shiftedbit, ddshifter4bit_8_shiftedbit,
       ddshifter4bit_9_shiftedbit, ddshifter4bit_10_shiftedbit, ddshifter4bit_11_shiftedbit,
       ddshifter4bit_12_shiftedbit, ddshifter4bit_13_shiftedbit, ddshifter4bit_14_shiftedbit,
       ddshifter4bit_15_shiftedbit, ddshifter4bit_16_shiftedbit, ddshifter4bit_17_shiftedbit,
       ddshifter4bit_18_shiftedbit, ddshifter4bit_19_shiftedbit, ddshifter4bit_20_shiftedbit,
       ddshifter4bit_21_shiftedbit, ddshifter4bit_22_shiftedbit, ddshifter4bit_23_shiftedbit,
       ddshifter4bit_24_shiftedbit, ddshifter4bit_25_shiftedbit, ddshifter4bit_26_shiftedbit,
       ddshifter4bit_27_shiftedbit, ddshifter4bit_28_shiftedbit, ddshifter4bit_29_shiftedbit,
       ddshifter4bit_30_shiftedbit, ddshifter4bit_31_shiftedbit, ddshifter4bit_32_shiftedbit,
       ddshifter4bit_33_shiftedbit, ddshifter4bit_34_shiftedbit, ddshifter4bit_35_shiftedbit,
       ddshifter4bit_36_shiftedbit, ddshifter4bit_37_shiftedbit, ddshifter4bit_38_shiftedbit,
       ddshifter4bit_39_shiftedbit, ddshifter4bit_40_shiftedbit, ddshifter4bit_41_shiftedbit,
       ddshifter4bit_42_shiftedbit, ddshifter4bit_43_shiftedbit, ddshifter4bit_44_shiftedbit,
       ddshifter4bit_45_shiftedbit, ddshifter4bit_46_shiftedbit, ddshifter4bit_47_shiftedbit,
       ddshifter4bit_48_shiftedbit, ddshifter4bit_49_shiftedbit, ddshifter4bit_50_shiftedbit,
       ddshifter4bit_51_shiftedbit, ddshifter4bit_52_shiftedbit, ddshifter4bit_53_shiftedbit,
       ddshifter4bit_54_shiftedbit, ddshifter4bit_55_shiftedbit, ddshifter4bit_56_shiftedbit,
       ddshifter4bit_57_shiftedbit, ddshifter4bit_58_shiftedbit, ddshifter4bit_59_shiftedbit,
       ddshifter4bit_60_shiftedbit, ddshifter4bit_61_shiftedbit, ddshifter4bit_62_shiftedbit,
       ddshifter4bit_63_shiftedbit, ddshifter4bit_64_shiftedbit, ddshifter4bit_65_shiftedbit,
       ddshifter4bit_66_shiftedbit, ddshifter4bit_67_shiftedbit, ddshifter4bit_68_shiftedbit,
       ddshifter4bit_69_shiftedbit, ddshifter4bit_70_shiftedbit, ddshifter4bit_71_shiftedbit,
       ddshifter4bit_72_shiftedbit, ddshifter4bit_73_shiftedbit, ddshifter4bit_74_shiftedbit,
       ddshifter4bit_75_shiftedbit, ddshifter4bit_76_shiftedbit, ddshifter4bit_77_shiftedbit,
       ddshifter4bit_78_shiftedbit, ddshifter4bit_79_shiftedbit, ddshifter4bit_80_shiftedbit,
       ddshifter4bit_81_shiftedbit, ddshifter4bit_82_shiftedbit, ddshifter4bit_83_shiftedbit,
       ddshifter4bit_84_shiftedbit, ddshifter4bit_85_shiftedbit, ddshifter4bit_86_shiftedbit,
       ddshifter4bit_87_shiftedbit, ddshifter4bit_88_shiftedbit, ddshifter4bit_89_shiftedbit,
       ddshifter4bit_90_shiftedbit, ddshifter4bit_91_shiftedbit, ddshifter4bit_92_shiftedbit,
       ddshifter4bit_93_shiftedbit, ddshifter4bit_94_shiftedbit, ddshifter4bit_95_shiftedbit,
       ddshifter4bit_96_shiftedbit, ddshifter4bit_97_shiftedbit, ddshifter4bit_98_shiftedbit,
       ddshifter4bit_99_shiftedbit, ddshifter4bit_100_shiftedbit, ddshifter4bit_101_shiftedbit,
       ddshifter4bit_102_shiftedbit, ddshifter4bit_103_shiftedbit, ddshifter4bit_104_shiftedbit,
       ddshifter4bit_105_shiftedbit, ddshifter4bit_106_shiftedbit, ddshifter4bit_107_shiftedbit,
       ddshifter4bit_108_shiftedbit, ddshifter4bit_109_shiftedbit, ddshifter4bit_110_shiftedbit,
       ddshifter4bit_111_shiftedbit, ddshifter4bit_112_shiftedbit, ddshifter4bit_113_shiftedbit,
       ddshifter4bit_114_shiftedbit, ddshifter4bit_115_shiftedbit, ddshifter4bit_116_shiftedbit,
       ddshifter4bit_117_shiftedbit, ddshifter4bit_118_shiftedbit, ddshifter4bit_119_shiftedbit,
       ddshifter4bit_120_shiftedbit, ddshifter4bit_121_shiftedbit, ddshifter4bit_122_shiftedbit,
       ddshifter4bit_123_shiftedbit, ddshifter4bit_124_shiftedbit, ddshifter4bit_125_shiftedbit,
       ddshifter4bit_126_shiftedbit, ddshifter4bit_127_shiftedbit, ddshifter4bit_128_shiftedbit,
       ddshifter4bit_129_shiftedbit, ddshifter4bit_130_shiftedbit, ddshifter4bit_131_shiftedbit,
       ddshifter4bit_132_shiftedbit, ddshifter4bit_133_shiftedbit, ddshifter4bit_134_shiftedbit,
       ddshifter4bit_135_shiftedbit, ddshifter4bit_136_shiftedbit, ddshifter4bit_137_shiftedbit,
       ddshifter4bit_138_shiftedbit, ddshifter4bit_139_shiftedbit, ddshifter4bit_140_shiftedbit,
       ddshifter4bit_141_shiftedbit, ddshifter4bit_142_shiftedbit, ddshifter4bit_143_shiftedbit,
       ddshifter4bit_144_shiftedbit, ddshifter4bit_145_shiftedbit, ddshifter4bit_146_shiftedbit,
       ddshifter4bit_147_shiftedbit, ddshifter4bit_148_shiftedbit, ddshifter4bit_149_shiftedbit,
       ddshifter4bit_150_shiftedbit, ddshifter4bit_151_shiftedbit, ddshifter4bit_152_shiftedbit,
       ddshifter4bit_153_shiftedbit, ddshifter4bit_154_shiftedbit, ddshifter4bit_155_shiftedbit;
  wire [3:0] ddshifter1_3bit_1_dataout, ddshifter1_3bit_2_dataout, ddshifter1_3bit_3_dataout,
       ddshifter1_3bit_4_dataout, ddshifter1_3bit_5_dataout, ddshifter1_3bit_6_dataout,
       ddshifter1_3bit_7_dataout, ddshifter1_3bit_8_dataout, ddshifter1_3bit_9_dataout,
       ddshifter1_3bit_10_dataout, ddshifter4bit_2_dataout, ddshifter4bit_4_dataout, ddshifter4bit_5_dataout,
       ddshifter4bit_6_dataout, ddshifter4bit_7_dataout, ddshifter4bit_9_dataout, ddshifter4bit_10_dataout,
       ddshifter4bit_11_dataout, ddshifter4bit_12_dataout, ddshifter4bit_13_dataout,
       ddshifter4bit_14_dataout, ddshifter4bit_15_dataout, ddshifter4bit_17_dataout,
       ddshifter4bit_18_dataout, ddshifter4bit_19_dataout, ddshifter4bit_20_dataout,
       ddshifter4bit_21_dataout, ddshifter4bit_22_dataout, ddshifter4bit_23_dataout,
       ddshifter4bit_24_dataout, ddshifter4bit_25_dataout, ddshifter4bit_26_dataout,
       ddshifter4bit_28_dataout, ddshifter4bit_29_dataout, ddshifter4bit_30_dataout,
       ddshifter4bit_31_dataout, ddshifter4bit_32_dataout, ddshifter4bit_33_dataout,
       ddshifter4bit_34_dataout, ddshifter4bit_35_dataout, ddshifter4bit_36_dataout,
       ddshifter4bit_37_dataout, ddshifter4bit_38_dataout, ddshifter4bit_39_dataout,
       ddshifter4bit_40_dataout, ddshifter4bit_42_dataout, ddshifter4bit_43_dataout,
       ddshifter4bit_44_dataout, ddshifter4bit_45_dataout, ddshifter4bit_46_dataout,
       ddshifter4bit_47_dataout, ddshifter4bit_48_dataout, ddshifter4bit_49_dataout,
       ddshifter4bit_50_dataout, ddshifter4bit_51_dataout, ddshifter4bit_52_dataout,
       ddshifter4bit_53_dataout, ddshifter4bit_54_dataout, ddshifter4bit_55_dataout,
       ddshifter4bit_56_dataout, ddshifter4bit_57_dataout, ddshifter4bit_59_dataout,
       ddshifter4bit_60_dataout, ddshifter4bit_61_dataout, ddshifter4bit_62_dataout,
       ddshifter4bit_63_dataout, ddshifter4bit_64_dataout, ddshifter4bit_65_dataout,
       ddshifter4bit_66_dataout, ddshifter4bit_67_dataout, ddshifter4bit_68_dataout,
       ddshifter4bit_69_dataout, ddshifter4bit_70_dataout, ddshifter4bit_71_dataout,
       ddshifter4bit_72_dataout, ddshifter4bit_73_dataout, ddshifter4bit_74_dataout,
       ddshifter4bit_75_dataout, ddshifter4bit_76_dataout, ddshifter4bit_77_dataout,
       ddshifter4bit_79_dataout, ddshifter4bit_80_dataout, ddshifter4bit_81_dataout,
       ddshifter4bit_82_dataout, ddshifter4bit_83_dataout, ddshifter4bit_84_dataout,
       ddshifter4bit_85_dataout, ddshifter4bit_86_dataout, ddshifter4bit_87_dataout,
       ddshifter4bit_88_dataout, ddshifter4bit_89_dataout, ddshifter4bit_90_dataout,
       ddshifter4bit_91_dataout, ddshifter4bit_92_dataout, ddshifter4bit_93_dataout,
       ddshifter4bit_94_dataout, ddshifter4bit_95_dataout, ddshifter4bit_96_dataout,
       ddshifter4bit_97_dataout, ddshifter4bit_98_dataout, ddshifter4bit_99_dataout,
       ddshifter4bit_100_dataout, ddshifter4bit_102_dataout, ddshifter4bit_103_dataout,
       ddshifter4bit_104_dataout, ddshifter4bit_105_dataout, ddshifter4bit_106_dataout,
       ddshifter4bit_107_dataout, ddshifter4bit_108_dataout, ddshifter4bit_109_dataout,
       ddshifter4bit_110_dataout, ddshifter4bit_111_dataout, ddshifter4bit_112_dataout,
       ddshifter4bit_113_dataout, ddshifter4bit_114_dataout, ddshifter4bit_115_dataout,
       ddshifter4bit_116_dataout, ddshifter4bit_117_dataout, ddshifter4bit_118_dataout,
       ddshifter4bit_119_dataout, ddshifter4bit_120_dataout, ddshifter4bit_121_dataout,
       ddshifter4bit_122_dataout, ddshifter4bit_123_dataout, ddshifter4bit_124_dataout,
       ddshifter4bit_125_dataout, ddshifter4bit_126_dataout, ddshifter4bit_128_dataout,
       ddshifter4bit_129_dataout, ddshifter4bit_130_dataout, ddshifter4bit_131_dataout,
       ddshifter4bit_132_dataout, ddshifter4bit_133_dataout, ddshifter4bit_134_dataout,
       ddshifter4bit_135_dataout, ddshifter4bit_136_dataout, ddshifter4bit_137_dataout,
       ddshifter4bit_138_dataout, ddshifter4bit_139_dataout, ddshifter4bit_140_dataout,
       ddshifter4bit_141_dataout, ddshifter4bit_142_dataout, ddshifter4bit_143_dataout,
       ddshifter4bit_144_dataout, ddshifter4bit_145_dataout, ddshifter4bit_146_dataout,
       ddshifter4bit_147_dataout, ddshifter4bit_148_dataout, ddshifter4bit_149_dataout,
       ddshifter4bit_150_dataout, ddshifter4bit_151_dataout, ddshifter4bit_152_dataout,
       ddshifter4bit_153_dataout, ddshifter4bit_154_dataout, ddshifter4bit_155_dataout;

  DDShifter4Bit ddshifter4bit_1 (
    .DataIn(ddshifter4bit_2_dataout), .NextBit(ddshifter4bit_3_shiftedbit), .DisplayOut(Billion));  // open: ShiftedBit, DataOut
  DDShifter4Bit ddshifter4bit_2 (
    .DataIn(ddshifter1_3bit_1_dataout), .NextBit(ddshifter4bit_4_shiftedbit),
    .DataOut(ddshifter4bit_2_dataout));  // open: ShiftedBit, DisplayOut
  DDShifter1_3Bit ddshifter1_3bit_1 (
    .Bit1(ddshifter4bit_7_shiftedbit), .Bit2(ddshifter4bit_6_shiftedbit), .Bit3(ddshifter4bit_5_shiftedbit),
    .DataOut(ddshifter1_3bit_1_dataout));
  DDShifter4Bit ddshifter4bit_3 (
    .DataIn(ddshifter4bit_4_dataout), .NextBit(ddshifter4bit_8_shiftedbit),
    .ShiftedBit(ddshifter4bit_3_shiftedbit), .DisplayOut(HundredMill));  // open: DataOut
  DDShifter4Bit ddshifter4bit_4 (
    .DataIn(ddshifter4bit_5_dataout), .NextBit(ddshifter4bit_9_shiftedbit),
    .ShiftedBit(ddshifter4bit_4_shiftedbit), .DataOut(ddshifter4bit_4_dataout));  // open: DisplayOut
  DDShifter4Bit ddshifter4bit_5 (
    .DataIn(ddshifter4bit_6_dataout), .NextBit(ddshifter4bit_10_shiftedbit),
    .ShiftedBit(ddshifter4bit_5_shiftedbit), .DataOut(ddshifter4bit_5_dataout));  // open: DisplayOut
  DDShifter4Bit ddshifter4bit_6 (
    .DataIn(ddshifter4bit_7_dataout), .NextBit(ddshifter4bit_11_shiftedbit),
    .ShiftedBit(ddshifter4bit_6_shiftedbit), .DataOut(ddshifter4bit_6_dataout));  // open: DisplayOut
  DDShifter4Bit ddshifter4bit_7 (
    .DataIn(ddshifter1_3bit_2_dataout), .NextBit(ddshifter4bit_12_shiftedbit),
    .ShiftedBit(ddshifter4bit_7_shiftedbit), .DataOut(ddshifter4bit_7_dataout));  // open: DisplayOut
  DDShifter1_3Bit ddshifter1_3bit_2 (
    .Bit1(ddshifter4bit_15_shiftedbit), .Bit2(ddshifter4bit_14_shiftedbit),
    .Bit3(ddshifter4bit_13_shiftedbit), .DataOut(ddshifter1_3bit_2_dataout));
  DDShifter4Bit ddshifter4bit_8 (
    .DataIn(ddshifter4bit_9_dataout), .NextBit(ddshifter4bit_16_shiftedbit),
    .ShiftedBit(ddshifter4bit_8_shiftedbit), .DisplayOut(TenMill));  // open: DataOut
  DDShifter4Bit ddshifter4bit_9 (
    .DataIn(ddshifter4bit_10_dataout), .NextBit(ddshifter4bit_17_shiftedbit),
    .ShiftedBit(ddshifter4bit_9_shiftedbit), .DataOut(ddshifter4bit_9_dataout));  // open: DisplayOut
  DDShifter4Bit ddshifter4bit_10 (
    .DataIn(ddshifter4bit_11_dataout), .NextBit(ddshifter4bit_18_shiftedbit),
    .ShiftedBit(ddshifter4bit_10_shiftedbit), .DataOut(ddshifter4bit_10_dataout));  // open: DisplayOut
  DDShifter4Bit ddshifter4bit_11 (
    .DataIn(ddshifter4bit_12_dataout), .NextBit(ddshifter4bit_19_shiftedbit),
    .ShiftedBit(ddshifter4bit_11_shiftedbit), .DataOut(ddshifter4bit_11_dataout));  // open: DisplayOut
  DDShifter4Bit ddshifter4bit_12 (
    .DataIn(ddshifter4bit_13_dataout), .NextBit(ddshifter4bit_20_shiftedbit),
    .ShiftedBit(ddshifter4bit_12_shiftedbit), .DataOut(ddshifter4bit_12_dataout));  // open: DisplayOut
  DDShifter4Bit ddshifter4bit_13 (
    .DataIn(ddshifter4bit_14_dataout), .NextBit(ddshifter4bit_21_shiftedbit),
    .ShiftedBit(ddshifter4bit_13_shiftedbit), .DataOut(ddshifter4bit_13_dataout));  // open: DisplayOut
  DDShifter4Bit ddshifter4bit_14 (
    .DataIn(ddshifter4bit_15_dataout), .NextBit(ddshifter4bit_22_shiftedbit),
    .ShiftedBit(ddshifter4bit_14_shiftedbit), .DataOut(ddshifter4bit_14_dataout));  // open: DisplayOut
  DDShifter4Bit ddshifter4bit_15 (
    .DataIn(ddshifter1_3bit_3_dataout), .NextBit(ddshifter4bit_23_shiftedbit),
    .ShiftedBit(ddshifter4bit_15_shiftedbit), .DataOut(ddshifter4bit_15_dataout));  // open: DisplayOut
  DDShifter1_3Bit ddshifter1_3bit_3 (
    .Bit1(ddshifter4bit_26_shiftedbit), .Bit2(ddshifter4bit_25_shiftedbit),
    .Bit3(ddshifter4bit_24_shiftedbit), .DataOut(ddshifter1_3bit_3_dataout));
  DDShifter4Bit ddshifter4bit_16 (
    .DataIn(ddshifter4bit_17_dataout), .NextBit(ddshifter4bit_27_shiftedbit),
    .ShiftedBit(ddshifter4bit_16_shiftedbit), .DisplayOut(Million));  // open: DataOut
  DDShifter4Bit ddshifter4bit_17 (
    .DataIn(ddshifter4bit_18_dataout), .NextBit(ddshifter4bit_28_shiftedbit),
    .ShiftedBit(ddshifter4bit_17_shiftedbit), .DataOut(ddshifter4bit_17_dataout));  // open: DisplayOut
  DDShifter4Bit ddshifter4bit_18 (
    .DataIn(ddshifter4bit_19_dataout), .NextBit(ddshifter4bit_29_shiftedbit),
    .ShiftedBit(ddshifter4bit_18_shiftedbit), .DataOut(ddshifter4bit_18_dataout));  // open: DisplayOut
  DDShifter4Bit ddshifter4bit_19 (
    .DataIn(ddshifter4bit_20_dataout), .NextBit(ddshifter4bit_30_shiftedbit),
    .ShiftedBit(ddshifter4bit_19_shiftedbit), .DataOut(ddshifter4bit_19_dataout));  // open: DisplayOut
  DDShifter4Bit ddshifter4bit_20 (
    .DataIn(ddshifter4bit_21_dataout), .NextBit(ddshifter4bit_31_shiftedbit),
    .ShiftedBit(ddshifter4bit_20_shiftedbit), .DataOut(ddshifter4bit_20_dataout));  // open: DisplayOut
  DDShifter4Bit ddshifter4bit_21 (
    .DataIn(ddshifter4bit_22_dataout), .NextBit(ddshifter4bit_32_shiftedbit),
    .ShiftedBit(ddshifter4bit_21_shiftedbit), .DataOut(ddshifter4bit_21_dataout));  // open: DisplayOut
  DDShifter4Bit ddshifter4bit_22 (
    .DataIn(ddshifter4bit_23_dataout), .NextBit(ddshifter4bit_33_shiftedbit),
    .ShiftedBit(ddshifter4bit_22_shiftedbit), .DataOut(ddshifter4bit_22_dataout));  // open: DisplayOut
  DDShifter4Bit ddshifter4bit_23 (
    .DataIn(ddshifter4bit_24_dataout), .NextBit(ddshifter4bit_34_shiftedbit),
    .ShiftedBit(ddshifter4bit_23_shiftedbit), .DataOut(ddshifter4bit_23_dataout));  // open: DisplayOut
  DDShifter4Bit ddshifter4bit_24 (
    .DataIn(ddshifter4bit_25_dataout), .NextBit(ddshifter4bit_35_shiftedbit),
    .ShiftedBit(ddshifter4bit_24_shiftedbit), .DataOut(ddshifter4bit_24_dataout));  // open: DisplayOut
  DDShifter4Bit ddshifter4bit_25 (
    .DataIn(ddshifter4bit_26_dataout), .NextBit(ddshifter4bit_36_shiftedbit),
    .ShiftedBit(ddshifter4bit_25_shiftedbit), .DataOut(ddshifter4bit_25_dataout));  // open: DisplayOut
  DDShifter4Bit ddshifter4bit_26 (
    .DataIn(ddshifter1_3bit_4_dataout), .NextBit(ddshifter4bit_37_shiftedbit),
    .ShiftedBit(ddshifter4bit_26_shiftedbit), .DataOut(ddshifter4bit_26_dataout));  // open: DisplayOut
  DDShifter1_3Bit ddshifter1_3bit_4 (
    .Bit1(ddshifter4bit_40_shiftedbit), .Bit2(ddshifter4bit_39_shiftedbit),
    .Bit3(ddshifter4bit_38_shiftedbit), .DataOut(ddshifter1_3bit_4_dataout));
  DDShifter4Bit ddshifter4bit_27 (
    .DataIn(ddshifter4bit_28_dataout), .NextBit(ddshifter4bit_41_shiftedbit),
    .ShiftedBit(ddshifter4bit_27_shiftedbit), .DisplayOut(HundredK));  // open: DataOut
  DDShifter4Bit ddshifter4bit_28 (
    .DataIn(ddshifter4bit_29_dataout), .NextBit(ddshifter4bit_42_shiftedbit),
    .ShiftedBit(ddshifter4bit_28_shiftedbit), .DataOut(ddshifter4bit_28_dataout));  // open: DisplayOut
  DDShifter4Bit ddshifter4bit_29 (
    .DataIn(ddshifter4bit_30_dataout), .NextBit(ddshifter4bit_43_shiftedbit),
    .ShiftedBit(ddshifter4bit_29_shiftedbit), .DataOut(ddshifter4bit_29_dataout));  // open: DisplayOut
  DDShifter4Bit ddshifter4bit_30 (
    .DataIn(ddshifter4bit_31_dataout), .NextBit(ddshifter4bit_44_shiftedbit),
    .ShiftedBit(ddshifter4bit_30_shiftedbit), .DataOut(ddshifter4bit_30_dataout));  // open: DisplayOut
  DDShifter4Bit ddshifter4bit_31 (
    .DataIn(ddshifter4bit_32_dataout), .NextBit(ddshifter4bit_45_shiftedbit),
    .ShiftedBit(ddshifter4bit_31_shiftedbit), .DataOut(ddshifter4bit_31_dataout));  // open: DisplayOut
  DDShifter4Bit ddshifter4bit_32 (
    .DataIn(ddshifter4bit_33_dataout), .NextBit(ddshifter4bit_46_shiftedbit),
    .ShiftedBit(ddshifter4bit_32_shiftedbit), .DataOut(ddshifter4bit_32_dataout));  // open: DisplayOut
  DDShifter4Bit ddshifter4bit_33 (
    .DataIn(ddshifter4bit_34_dataout), .NextBit(ddshifter4bit_47_shiftedbit),
    .ShiftedBit(ddshifter4bit_33_shiftedbit), .DataOut(ddshifter4bit_33_dataout));  // open: DisplayOut
  DDShifter4Bit ddshifter4bit_34 (
    .DataIn(ddshifter4bit_35_dataout), .NextBit(ddshifter4bit_48_shiftedbit),
    .ShiftedBit(ddshifter4bit_34_shiftedbit), .DataOut(ddshifter4bit_34_dataout));  // open: DisplayOut
  DDShifter4Bit ddshifter4bit_35 (
    .DataIn(ddshifter4bit_36_dataout), .NextBit(ddshifter4bit_49_shiftedbit),
    .ShiftedBit(ddshifter4bit_35_shiftedbit), .DataOut(ddshifter4bit_35_dataout));  // open: DisplayOut
  DDShifter4Bit ddshifter4bit_36 (
    .DataIn(ddshifter4bit_37_dataout), .NextBit(ddshifter4bit_50_shiftedbit),
    .ShiftedBit(ddshifter4bit_36_shiftedbit), .DataOut(ddshifter4bit_36_dataout));  // open: DisplayOut
  DDShifter4Bit ddshifter4bit_37 (
    .DataIn(ddshifter4bit_38_dataout), .NextBit(ddshifter4bit_51_shiftedbit),
    .ShiftedBit(ddshifter4bit_37_shiftedbit), .DataOut(ddshifter4bit_37_dataout));  // open: DisplayOut
  DDShifter4Bit ddshifter4bit_38 (
    .DataIn(ddshifter4bit_39_dataout), .NextBit(ddshifter4bit_52_shiftedbit),
    .ShiftedBit(ddshifter4bit_38_shiftedbit), .DataOut(ddshifter4bit_38_dataout));  // open: DisplayOut
  DDShifter4Bit ddshifter4bit_39 (
    .DataIn(ddshifter4bit_40_dataout), .NextBit(ddshifter4bit_53_shiftedbit),
    .ShiftedBit(ddshifter4bit_39_shiftedbit), .DataOut(ddshifter4bit_39_dataout));  // open: DisplayOut
  DDShifter4Bit ddshifter4bit_40 (
    .DataIn(ddshifter1_3bit_5_dataout), .NextBit(ddshifter4bit_54_shiftedbit),
    .ShiftedBit(ddshifter4bit_40_shiftedbit), .DataOut(ddshifter4bit_40_dataout));  // open: DisplayOut
  DDShifter1_3Bit ddshifter1_3bit_5 (
    .Bit1(ddshifter4bit_57_shiftedbit), .Bit2(ddshifter4bit_56_shiftedbit),
    .Bit3(ddshifter4bit_55_shiftedbit), .DataOut(ddshifter1_3bit_5_dataout));
  DDShifter4Bit ddshifter4bit_41 (
    .DataIn(ddshifter4bit_42_dataout), .NextBit(ddshifter4bit_58_shiftedbit),
    .ShiftedBit(ddshifter4bit_41_shiftedbit), .DisplayOut(TenK));  // open: DataOut
  DDShifter4Bit ddshifter4bit_42 (
    .DataIn(ddshifter4bit_43_dataout), .NextBit(ddshifter4bit_59_shiftedbit),
    .ShiftedBit(ddshifter4bit_42_shiftedbit), .DataOut(ddshifter4bit_42_dataout));  // open: DisplayOut
  DDShifter4Bit ddshifter4bit_43 (
    .DataIn(ddshifter4bit_44_dataout), .NextBit(ddshifter4bit_60_shiftedbit),
    .ShiftedBit(ddshifter4bit_43_shiftedbit), .DataOut(ddshifter4bit_43_dataout));  // open: DisplayOut
  DDShifter4Bit ddshifter4bit_44 (
    .DataIn(ddshifter4bit_45_dataout), .NextBit(ddshifter4bit_61_shiftedbit),
    .ShiftedBit(ddshifter4bit_44_shiftedbit), .DataOut(ddshifter4bit_44_dataout));  // open: DisplayOut
  DDShifter4Bit ddshifter4bit_45 (
    .DataIn(ddshifter4bit_46_dataout), .NextBit(ddshifter4bit_62_shiftedbit),
    .ShiftedBit(ddshifter4bit_45_shiftedbit), .DataOut(ddshifter4bit_45_dataout));  // open: DisplayOut
  DDShifter4Bit ddshifter4bit_46 (
    .DataIn(ddshifter4bit_47_dataout), .NextBit(ddshifter4bit_63_shiftedbit),
    .ShiftedBit(ddshifter4bit_46_shiftedbit), .DataOut(ddshifter4bit_46_dataout));  // open: DisplayOut
  DDShifter4Bit ddshifter4bit_47 (
    .DataIn(ddshifter4bit_48_dataout), .NextBit(ddshifter4bit_64_shiftedbit),
    .ShiftedBit(ddshifter4bit_47_shiftedbit), .DataOut(ddshifter4bit_47_dataout));  // open: DisplayOut
  DDShifter4Bit ddshifter4bit_48 (
    .DataIn(ddshifter4bit_49_dataout), .NextBit(ddshifter4bit_65_shiftedbit),
    .ShiftedBit(ddshifter4bit_48_shiftedbit), .DataOut(ddshifter4bit_48_dataout));  // open: DisplayOut
  DDShifter4Bit ddshifter4bit_49 (
    .DataIn(ddshifter4bit_50_dataout), .NextBit(ddshifter4bit_66_shiftedbit),
    .ShiftedBit(ddshifter4bit_49_shiftedbit), .DataOut(ddshifter4bit_49_dataout));  // open: DisplayOut
  DDShifter4Bit ddshifter4bit_50 (
    .DataIn(ddshifter4bit_51_dataout), .NextBit(ddshifter4bit_67_shiftedbit),
    .ShiftedBit(ddshifter4bit_50_shiftedbit), .DataOut(ddshifter4bit_50_dataout));  // open: DisplayOut
  DDShifter4Bit ddshifter4bit_51 (
    .DataIn(ddshifter4bit_52_dataout), .NextBit(ddshifter4bit_68_shiftedbit),
    .ShiftedBit(ddshifter4bit_51_shiftedbit), .DataOut(ddshifter4bit_51_dataout));  // open: DisplayOut
  DDShifter4Bit ddshifter4bit_52 (
    .DataIn(ddshifter4bit_53_dataout), .NextBit(ddshifter4bit_69_shiftedbit),
    .ShiftedBit(ddshifter4bit_52_shiftedbit), .DataOut(ddshifter4bit_52_dataout));  // open: DisplayOut
  DDShifter4Bit ddshifter4bit_53 (
    .DataIn(ddshifter4bit_54_dataout), .NextBit(ddshifter4bit_70_shiftedbit),
    .ShiftedBit(ddshifter4bit_53_shiftedbit), .DataOut(ddshifter4bit_53_dataout));  // open: DisplayOut
  DDShifter4Bit ddshifter4bit_54 (
    .DataIn(ddshifter4bit_55_dataout), .NextBit(ddshifter4bit_71_shiftedbit),
    .ShiftedBit(ddshifter4bit_54_shiftedbit), .DataOut(ddshifter4bit_54_dataout));  // open: DisplayOut
  DDShifter4Bit ddshifter4bit_55 (
    .DataIn(ddshifter4bit_56_dataout), .NextBit(ddshifter4bit_72_shiftedbit),
    .ShiftedBit(ddshifter4bit_55_shiftedbit), .DataOut(ddshifter4bit_55_dataout));  // open: DisplayOut
  DDShifter4Bit ddshifter4bit_56 (
    .DataIn(ddshifter4bit_57_dataout), .NextBit(ddshifter4bit_73_shiftedbit),
    .ShiftedBit(ddshifter4bit_56_shiftedbit), .DataOut(ddshifter4bit_56_dataout));  // open: DisplayOut
  DDShifter4Bit ddshifter4bit_57 (
    .DataIn(ddshifter1_3bit_6_dataout), .NextBit(ddshifter4bit_74_shiftedbit),
    .ShiftedBit(ddshifter4bit_57_shiftedbit), .DataOut(ddshifter4bit_57_dataout));  // open: DisplayOut
  DDShifter1_3Bit ddshifter1_3bit_6 (
    .Bit1(ddshifter4bit_77_shiftedbit), .Bit2(ddshifter4bit_76_shiftedbit),
    .Bit3(ddshifter4bit_75_shiftedbit), .DataOut(ddshifter1_3bit_6_dataout));
  DDShifter4Bit ddshifter4bit_58 (
    .DataIn(ddshifter4bit_59_dataout), .NextBit(ddshifter4bit_78_shiftedbit),
    .ShiftedBit(ddshifter4bit_58_shiftedbit), .DisplayOut(Tausend));  // open: DataOut
  DDShifter4Bit ddshifter4bit_59 (
    .DataIn(ddshifter4bit_60_dataout), .NextBit(ddshifter4bit_79_shiftedbit),
    .ShiftedBit(ddshifter4bit_59_shiftedbit), .DataOut(ddshifter4bit_59_dataout));  // open: DisplayOut
  DDShifter4Bit ddshifter4bit_60 (
    .DataIn(ddshifter4bit_61_dataout), .NextBit(ddshifter4bit_80_shiftedbit),
    .ShiftedBit(ddshifter4bit_60_shiftedbit), .DataOut(ddshifter4bit_60_dataout));  // open: DisplayOut
  DDShifter4Bit ddshifter4bit_61 (
    .DataIn(ddshifter4bit_62_dataout), .NextBit(ddshifter4bit_81_shiftedbit),
    .ShiftedBit(ddshifter4bit_61_shiftedbit), .DataOut(ddshifter4bit_61_dataout));  // open: DisplayOut
  DDShifter4Bit ddshifter4bit_62 (
    .DataIn(ddshifter4bit_63_dataout), .NextBit(ddshifter4bit_82_shiftedbit),
    .ShiftedBit(ddshifter4bit_62_shiftedbit), .DataOut(ddshifter4bit_62_dataout));  // open: DisplayOut
  DDShifter4Bit ddshifter4bit_63 (
    .DataIn(ddshifter4bit_64_dataout), .NextBit(ddshifter4bit_83_shiftedbit),
    .ShiftedBit(ddshifter4bit_63_shiftedbit), .DataOut(ddshifter4bit_63_dataout));  // open: DisplayOut
  DDShifter4Bit ddshifter4bit_64 (
    .DataIn(ddshifter4bit_65_dataout), .NextBit(ddshifter4bit_84_shiftedbit),
    .ShiftedBit(ddshifter4bit_64_shiftedbit), .DataOut(ddshifter4bit_64_dataout));  // open: DisplayOut
  DDShifter4Bit ddshifter4bit_65 (
    .DataIn(ddshifter4bit_66_dataout), .NextBit(ddshifter4bit_85_shiftedbit),
    .ShiftedBit(ddshifter4bit_65_shiftedbit), .DataOut(ddshifter4bit_65_dataout));  // open: DisplayOut
  DDShifter4Bit ddshifter4bit_66 (
    .DataIn(ddshifter4bit_67_dataout), .NextBit(ddshifter4bit_86_shiftedbit),
    .ShiftedBit(ddshifter4bit_66_shiftedbit), .DataOut(ddshifter4bit_66_dataout));  // open: DisplayOut
  DDShifter4Bit ddshifter4bit_67 (
    .DataIn(ddshifter4bit_68_dataout), .NextBit(ddshifter4bit_87_shiftedbit),
    .ShiftedBit(ddshifter4bit_67_shiftedbit), .DataOut(ddshifter4bit_67_dataout));  // open: DisplayOut
  DDShifter4Bit ddshifter4bit_68 (
    .DataIn(ddshifter4bit_69_dataout), .NextBit(ddshifter4bit_88_shiftedbit),
    .ShiftedBit(ddshifter4bit_68_shiftedbit), .DataOut(ddshifter4bit_68_dataout));  // open: DisplayOut
  DDShifter4Bit ddshifter4bit_69 (
    .DataIn(ddshifter4bit_70_dataout), .NextBit(ddshifter4bit_89_shiftedbit),
    .ShiftedBit(ddshifter4bit_69_shiftedbit), .DataOut(ddshifter4bit_69_dataout));  // open: DisplayOut
  DDShifter4Bit ddshifter4bit_70 (
    .DataIn(ddshifter4bit_71_dataout), .NextBit(ddshifter4bit_90_shiftedbit),
    .ShiftedBit(ddshifter4bit_70_shiftedbit), .DataOut(ddshifter4bit_70_dataout));  // open: DisplayOut
  DDShifter4Bit ddshifter4bit_71 (
    .DataIn(ddshifter4bit_72_dataout), .NextBit(ddshifter4bit_91_shiftedbit),
    .ShiftedBit(ddshifter4bit_71_shiftedbit), .DataOut(ddshifter4bit_71_dataout));  // open: DisplayOut
  DDShifter4Bit ddshifter4bit_72 (
    .DataIn(ddshifter4bit_73_dataout), .NextBit(ddshifter4bit_92_shiftedbit),
    .ShiftedBit(ddshifter4bit_72_shiftedbit), .DataOut(ddshifter4bit_72_dataout));  // open: DisplayOut
  DDShifter4Bit ddshifter4bit_73 (
    .DataIn(ddshifter4bit_74_dataout), .NextBit(ddshifter4bit_93_shiftedbit),
    .ShiftedBit(ddshifter4bit_73_shiftedbit), .DataOut(ddshifter4bit_73_dataout));  // open: DisplayOut
  DDShifter4Bit ddshifter4bit_74 (
    .DataIn(ddshifter4bit_75_dataout), .NextBit(ddshifter4bit_94_shiftedbit),
    .ShiftedBit(ddshifter4bit_74_shiftedbit), .DataOut(ddshifter4bit_74_dataout));  // open: DisplayOut
  DDShifter4Bit ddshifter4bit_75 (
    .DataIn(ddshifter4bit_76_dataout), .NextBit(ddshifter4bit_95_shiftedbit),
    .ShiftedBit(ddshifter4bit_75_shiftedbit), .DataOut(ddshifter4bit_75_dataout));  // open: DisplayOut
  DDShifter4Bit ddshifter4bit_76 (
    .DataIn(ddshifter4bit_77_dataout), .NextBit(ddshifter4bit_96_shiftedbit),
    .ShiftedBit(ddshifter4bit_76_shiftedbit), .DataOut(ddshifter4bit_76_dataout));  // open: DisplayOut
  DDShifter4Bit ddshifter4bit_77 (
    .DataIn(ddshifter1_3bit_7_dataout), .NextBit(ddshifter4bit_97_shiftedbit),
    .ShiftedBit(ddshifter4bit_77_shiftedbit), .DataOut(ddshifter4bit_77_dataout));  // open: DisplayOut
  DDShifter1_3Bit ddshifter1_3bit_7 (
    .Bit1(ddshifter4bit_100_shiftedbit), .Bit2(ddshifter4bit_99_shiftedbit),
    .Bit3(ddshifter4bit_98_shiftedbit), .DataOut(ddshifter1_3bit_7_dataout));
  DDShifter4Bit ddshifter4bit_78 (
    .DataIn(ddshifter4bit_79_dataout), .NextBit(ddshifter4bit_101_shiftedbit),
    .ShiftedBit(ddshifter4bit_78_shiftedbit), .DisplayOut(Hundred));  // open: DataOut
  DDShifter4Bit ddshifter4bit_79 (
    .DataIn(ddshifter4bit_80_dataout), .NextBit(ddshifter4bit_102_shiftedbit),
    .ShiftedBit(ddshifter4bit_79_shiftedbit), .DataOut(ddshifter4bit_79_dataout));  // open: DisplayOut
  DDShifter4Bit ddshifter4bit_80 (
    .DataIn(ddshifter4bit_81_dataout), .NextBit(ddshifter4bit_103_shiftedbit),
    .ShiftedBit(ddshifter4bit_80_shiftedbit), .DataOut(ddshifter4bit_80_dataout));  // open: DisplayOut
  DDShifter4Bit ddshifter4bit_81 (
    .DataIn(ddshifter4bit_82_dataout), .NextBit(ddshifter4bit_104_shiftedbit),
    .ShiftedBit(ddshifter4bit_81_shiftedbit), .DataOut(ddshifter4bit_81_dataout));  // open: DisplayOut
  DDShifter4Bit ddshifter4bit_82 (
    .DataIn(ddshifter4bit_83_dataout), .NextBit(ddshifter4bit_105_shiftedbit),
    .ShiftedBit(ddshifter4bit_82_shiftedbit), .DataOut(ddshifter4bit_82_dataout));  // open: DisplayOut
  DDShifter4Bit ddshifter4bit_83 (
    .DataIn(ddshifter4bit_84_dataout), .NextBit(ddshifter4bit_106_shiftedbit),
    .ShiftedBit(ddshifter4bit_83_shiftedbit), .DataOut(ddshifter4bit_83_dataout));  // open: DisplayOut
  DDShifter4Bit ddshifter4bit_84 (
    .DataIn(ddshifter4bit_85_dataout), .NextBit(ddshifter4bit_107_shiftedbit),
    .ShiftedBit(ddshifter4bit_84_shiftedbit), .DataOut(ddshifter4bit_84_dataout));  // open: DisplayOut
  DDShifter4Bit ddshifter4bit_85 (
    .DataIn(ddshifter4bit_86_dataout), .NextBit(ddshifter4bit_108_shiftedbit),
    .ShiftedBit(ddshifter4bit_85_shiftedbit), .DataOut(ddshifter4bit_85_dataout));  // open: DisplayOut
  DDShifter4Bit ddshifter4bit_86 (
    .DataIn(ddshifter4bit_87_dataout), .NextBit(ddshifter4bit_109_shiftedbit),
    .ShiftedBit(ddshifter4bit_86_shiftedbit), .DataOut(ddshifter4bit_86_dataout));  // open: DisplayOut
  DDShifter4Bit ddshifter4bit_87 (
    .DataIn(ddshifter4bit_88_dataout), .NextBit(ddshifter4bit_110_shiftedbit),
    .ShiftedBit(ddshifter4bit_87_shiftedbit), .DataOut(ddshifter4bit_87_dataout));  // open: DisplayOut
  DDShifter4Bit ddshifter4bit_88 (
    .DataIn(ddshifter4bit_89_dataout), .NextBit(ddshifter4bit_111_shiftedbit),
    .ShiftedBit(ddshifter4bit_88_shiftedbit), .DataOut(ddshifter4bit_88_dataout));  // open: DisplayOut
  DDShifter4Bit ddshifter4bit_89 (
    .DataIn(ddshifter4bit_90_dataout), .NextBit(ddshifter4bit_112_shiftedbit),
    .ShiftedBit(ddshifter4bit_89_shiftedbit), .DataOut(ddshifter4bit_89_dataout));  // open: DisplayOut
  DDShifter4Bit ddshifter4bit_90 (
    .DataIn(ddshifter4bit_91_dataout), .NextBit(ddshifter4bit_113_shiftedbit),
    .ShiftedBit(ddshifter4bit_90_shiftedbit), .DataOut(ddshifter4bit_90_dataout));  // open: DisplayOut
  DDShifter4Bit ddshifter4bit_91 (
    .DataIn(ddshifter4bit_92_dataout), .NextBit(ddshifter4bit_114_shiftedbit),
    .ShiftedBit(ddshifter4bit_91_shiftedbit), .DataOut(ddshifter4bit_91_dataout));  // open: DisplayOut
  DDShifter4Bit ddshifter4bit_92 (
    .DataIn(ddshifter4bit_93_dataout), .NextBit(ddshifter4bit_115_shiftedbit),
    .ShiftedBit(ddshifter4bit_92_shiftedbit), .DataOut(ddshifter4bit_92_dataout));  // open: DisplayOut
  DDShifter4Bit ddshifter4bit_93 (
    .DataIn(ddshifter4bit_94_dataout), .NextBit(ddshifter4bit_116_shiftedbit),
    .ShiftedBit(ddshifter4bit_93_shiftedbit), .DataOut(ddshifter4bit_93_dataout));  // open: DisplayOut
  DDShifter4Bit ddshifter4bit_94 (
    .DataIn(ddshifter4bit_95_dataout), .NextBit(ddshifter4bit_117_shiftedbit),
    .ShiftedBit(ddshifter4bit_94_shiftedbit), .DataOut(ddshifter4bit_94_dataout));  // open: DisplayOut
  DDShifter4Bit ddshifter4bit_95 (
    .DataIn(ddshifter4bit_96_dataout), .NextBit(ddshifter4bit_118_shiftedbit),
    .ShiftedBit(ddshifter4bit_95_shiftedbit), .DataOut(ddshifter4bit_95_dataout));  // open: DisplayOut
  DDShifter4Bit ddshifter4bit_96 (
    .DataIn(ddshifter4bit_97_dataout), .NextBit(ddshifter4bit_119_shiftedbit),
    .ShiftedBit(ddshifter4bit_96_shiftedbit), .DataOut(ddshifter4bit_96_dataout));  // open: DisplayOut
  DDShifter4Bit ddshifter4bit_97 (
    .DataIn(ddshifter4bit_98_dataout), .NextBit(ddshifter4bit_120_shiftedbit),
    .ShiftedBit(ddshifter4bit_97_shiftedbit), .DataOut(ddshifter4bit_97_dataout));  // open: DisplayOut
  DDShifter4Bit ddshifter4bit_98 (
    .DataIn(ddshifter4bit_99_dataout), .NextBit(ddshifter4bit_121_shiftedbit),
    .ShiftedBit(ddshifter4bit_98_shiftedbit), .DataOut(ddshifter4bit_98_dataout));  // open: DisplayOut
  DDShifter4Bit ddshifter4bit_99 (
    .DataIn(ddshifter4bit_100_dataout), .NextBit(ddshifter4bit_122_shiftedbit),
    .ShiftedBit(ddshifter4bit_99_shiftedbit), .DataOut(ddshifter4bit_99_dataout));  // open: DisplayOut
  DDShifter4Bit ddshifter4bit_100 (
    .DataIn(ddshifter1_3bit_8_dataout), .NextBit(ddshifter4bit_123_shiftedbit),
    .ShiftedBit(ddshifter4bit_100_shiftedbit), .DataOut(ddshifter4bit_100_dataout));  // open: DisplayOut
  DDShifter1_3Bit ddshifter1_3bit_8 (
    .Bit1(ddshifter4bit_126_shiftedbit), .Bit2(ddshifter4bit_125_shiftedbit),
    .Bit3(ddshifter4bit_124_shiftedbit), .DataOut(ddshifter1_3bit_8_dataout));
  DDShifter4Bit ddshifter4bit_101 (
    .DataIn(ddshifter4bit_102_dataout), .NextBit(ddshifter4bit_127_shiftedbit),
    .ShiftedBit(ddshifter4bit_101_shiftedbit), .DisplayOut(Ten));  // open: DataOut
  DDShifter4Bit ddshifter4bit_102 (
    .DataIn(ddshifter4bit_103_dataout), .NextBit(ddshifter4bit_128_shiftedbit),
    .ShiftedBit(ddshifter4bit_102_shiftedbit), .DataOut(ddshifter4bit_102_dataout));  // open: DisplayOut
  DDShifter4Bit ddshifter4bit_103 (
    .DataIn(ddshifter4bit_104_dataout), .NextBit(ddshifter4bit_129_shiftedbit),
    .ShiftedBit(ddshifter4bit_103_shiftedbit), .DataOut(ddshifter4bit_103_dataout));  // open: DisplayOut
  DDShifter4Bit ddshifter4bit_104 (
    .DataIn(ddshifter4bit_105_dataout), .NextBit(ddshifter4bit_130_shiftedbit),
    .ShiftedBit(ddshifter4bit_104_shiftedbit), .DataOut(ddshifter4bit_104_dataout));  // open: DisplayOut
  DDShifter4Bit ddshifter4bit_105 (
    .DataIn(ddshifter4bit_106_dataout), .NextBit(ddshifter4bit_131_shiftedbit),
    .ShiftedBit(ddshifter4bit_105_shiftedbit), .DataOut(ddshifter4bit_105_dataout));  // open: DisplayOut
  DDShifter4Bit ddshifter4bit_106 (
    .DataIn(ddshifter4bit_107_dataout), .NextBit(ddshifter4bit_132_shiftedbit),
    .ShiftedBit(ddshifter4bit_106_shiftedbit), .DataOut(ddshifter4bit_106_dataout));  // open: DisplayOut
  DDShifter4Bit ddshifter4bit_107 (
    .DataIn(ddshifter4bit_108_dataout), .NextBit(ddshifter4bit_133_shiftedbit),
    .ShiftedBit(ddshifter4bit_107_shiftedbit), .DataOut(ddshifter4bit_107_dataout));  // open: DisplayOut
  DDShifter4Bit ddshifter4bit_108 (
    .DataIn(ddshifter4bit_109_dataout), .NextBit(ddshifter4bit_134_shiftedbit),
    .ShiftedBit(ddshifter4bit_108_shiftedbit), .DataOut(ddshifter4bit_108_dataout));  // open: DisplayOut
  DDShifter4Bit ddshifter4bit_109 (
    .DataIn(ddshifter4bit_110_dataout), .NextBit(ddshifter4bit_135_shiftedbit),
    .ShiftedBit(ddshifter4bit_109_shiftedbit), .DataOut(ddshifter4bit_109_dataout));  // open: DisplayOut
  DDShifter4Bit ddshifter4bit_110 (
    .DataIn(ddshifter4bit_111_dataout), .NextBit(ddshifter4bit_136_shiftedbit),
    .ShiftedBit(ddshifter4bit_110_shiftedbit), .DataOut(ddshifter4bit_110_dataout));  // open: DisplayOut
  DDShifter4Bit ddshifter4bit_111 (
    .DataIn(ddshifter4bit_112_dataout), .NextBit(ddshifter4bit_137_shiftedbit),
    .ShiftedBit(ddshifter4bit_111_shiftedbit), .DataOut(ddshifter4bit_111_dataout));  // open: DisplayOut
  DDShifter4Bit ddshifter4bit_112 (
    .DataIn(ddshifter4bit_113_dataout), .NextBit(ddshifter4bit_138_shiftedbit),
    .ShiftedBit(ddshifter4bit_112_shiftedbit), .DataOut(ddshifter4bit_112_dataout));  // open: DisplayOut
  DDShifter4Bit ddshifter4bit_113 (
    .DataIn(ddshifter4bit_114_dataout), .NextBit(ddshifter4bit_139_shiftedbit),
    .ShiftedBit(ddshifter4bit_113_shiftedbit), .DataOut(ddshifter4bit_113_dataout));  // open: DisplayOut
  DDShifter4Bit ddshifter4bit_114 (
    .DataIn(ddshifter4bit_115_dataout), .NextBit(ddshifter4bit_140_shiftedbit),
    .ShiftedBit(ddshifter4bit_114_shiftedbit), .DataOut(ddshifter4bit_114_dataout));  // open: DisplayOut
  DDShifter4Bit ddshifter4bit_115 (
    .DataIn(ddshifter4bit_116_dataout), .NextBit(ddshifter4bit_141_shiftedbit),
    .ShiftedBit(ddshifter4bit_115_shiftedbit), .DataOut(ddshifter4bit_115_dataout));  // open: DisplayOut
  DDShifter4Bit ddshifter4bit_116 (
    .DataIn(ddshifter4bit_117_dataout), .NextBit(ddshifter4bit_142_shiftedbit),
    .ShiftedBit(ddshifter4bit_116_shiftedbit), .DataOut(ddshifter4bit_116_dataout));  // open: DisplayOut
  DDShifter4Bit ddshifter4bit_117 (
    .DataIn(ddshifter4bit_118_dataout), .NextBit(ddshifter4bit_143_shiftedbit),
    .ShiftedBit(ddshifter4bit_117_shiftedbit), .DataOut(ddshifter4bit_117_dataout));  // open: DisplayOut
  DDShifter4Bit ddshifter4bit_118 (
    .DataIn(ddshifter4bit_119_dataout), .NextBit(ddshifter4bit_144_shiftedbit),
    .ShiftedBit(ddshifter4bit_118_shiftedbit), .DataOut(ddshifter4bit_118_dataout));  // open: DisplayOut
  DDShifter4Bit ddshifter4bit_119 (
    .DataIn(ddshifter4bit_120_dataout), .NextBit(ddshifter4bit_145_shiftedbit),
    .ShiftedBit(ddshifter4bit_119_shiftedbit), .DataOut(ddshifter4bit_119_dataout));  // open: DisplayOut
  DDShifter4Bit ddshifter4bit_120 (
    .DataIn(ddshifter4bit_121_dataout), .NextBit(ddshifter4bit_146_shiftedbit),
    .ShiftedBit(ddshifter4bit_120_shiftedbit), .DataOut(ddshifter4bit_120_dataout));  // open: DisplayOut
  DDShifter4Bit ddshifter4bit_121 (
    .DataIn(ddshifter4bit_122_dataout), .NextBit(ddshifter4bit_147_shiftedbit),
    .ShiftedBit(ddshifter4bit_121_shiftedbit), .DataOut(ddshifter4bit_121_dataout));  // open: DisplayOut
  DDShifter4Bit ddshifter4bit_122 (
    .DataIn(ddshifter4bit_123_dataout), .NextBit(ddshifter4bit_148_shiftedbit),
    .ShiftedBit(ddshifter4bit_122_shiftedbit), .DataOut(ddshifter4bit_122_dataout));  // open: DisplayOut
  DDShifter4Bit ddshifter4bit_123 (
    .DataIn(ddshifter4bit_124_dataout), .NextBit(ddshifter4bit_149_shiftedbit),
    .ShiftedBit(ddshifter4bit_123_shiftedbit), .DataOut(ddshifter4bit_123_dataout));  // open: DisplayOut
  DDShifter4Bit ddshifter4bit_124 (
    .DataIn(ddshifter4bit_125_dataout), .NextBit(ddshifter4bit_150_shiftedbit),
    .ShiftedBit(ddshifter4bit_124_shiftedbit), .DataOut(ddshifter4bit_124_dataout));  // open: DisplayOut
  DDShifter4Bit ddshifter4bit_125 (
    .DataIn(ddshifter4bit_126_dataout), .NextBit(ddshifter4bit_151_shiftedbit),
    .ShiftedBit(ddshifter4bit_125_shiftedbit), .DataOut(ddshifter4bit_125_dataout));  // open: DisplayOut
  DDShifter4Bit ddshifter4bit_126 (
    .DataIn(ddshifter1_3bit_9_dataout), .NextBit(ddshifter4bit_152_shiftedbit),
    .ShiftedBit(ddshifter4bit_126_shiftedbit), .DataOut(ddshifter4bit_126_dataout));  // open: DisplayOut
  DDShifter1_3Bit ddshifter1_3bit_9 (
    .Bit1(ddshifter4bit_155_shiftedbit), .Bit2(ddshifter4bit_154_shiftedbit),
    .Bit3(ddshifter4bit_153_shiftedbit), .DataOut(ddshifter1_3bit_9_dataout));
  DDShifter4Bit ddshifter4bit_127 (
    .DataIn(ddshifter4bit_128_dataout), .NextBit(in_1[0]), .ShiftedBit(ddshifter4bit_127_shiftedbit),
    .DisplayOut(One));  // open: DataOut
  DDShifter4Bit ddshifter4bit_128 (
    .DataIn(ddshifter4bit_129_dataout), .NextBit(in_1[1]), .ShiftedBit(ddshifter4bit_128_shiftedbit),
    .DataOut(ddshifter4bit_128_dataout));  // open: DisplayOut
  DDShifter4Bit ddshifter4bit_129 (
    .DataIn(ddshifter4bit_130_dataout), .NextBit(in_1[2]), .ShiftedBit(ddshifter4bit_129_shiftedbit),
    .DataOut(ddshifter4bit_129_dataout));  // open: DisplayOut
  DDShifter4Bit ddshifter4bit_130 (
    .DataIn(ddshifter4bit_131_dataout), .NextBit(in_1[3]), .ShiftedBit(ddshifter4bit_130_shiftedbit),
    .DataOut(ddshifter4bit_130_dataout));  // open: DisplayOut
  DDShifter4Bit ddshifter4bit_131 (
    .DataIn(ddshifter4bit_132_dataout), .NextBit(in_1[4]), .ShiftedBit(ddshifter4bit_131_shiftedbit),
    .DataOut(ddshifter4bit_131_dataout));  // open: DisplayOut
  DDShifter4Bit ddshifter4bit_132 (
    .DataIn(ddshifter4bit_133_dataout), .NextBit(in_1[5]), .ShiftedBit(ddshifter4bit_132_shiftedbit),
    .DataOut(ddshifter4bit_132_dataout));  // open: DisplayOut
  DDShifter4Bit ddshifter4bit_133 (
    .DataIn(ddshifter4bit_134_dataout), .NextBit(in_1[6]), .ShiftedBit(ddshifter4bit_133_shiftedbit),
    .DataOut(ddshifter4bit_133_dataout));  // open: DisplayOut
  DDShifter4Bit ddshifter4bit_134 (
    .DataIn(ddshifter4bit_135_dataout), .NextBit(in_1[7]), .ShiftedBit(ddshifter4bit_134_shiftedbit),
    .DataOut(ddshifter4bit_134_dataout));  // open: DisplayOut
  DDShifter4Bit ddshifter4bit_135 (
    .DataIn(ddshifter4bit_136_dataout), .NextBit(in_1[8]), .ShiftedBit(ddshifter4bit_135_shiftedbit),
    .DataOut(ddshifter4bit_135_dataout));  // open: DisplayOut
  DDShifter4Bit ddshifter4bit_136 (
    .DataIn(ddshifter4bit_137_dataout), .NextBit(in_1[9]), .ShiftedBit(ddshifter4bit_136_shiftedbit),
    .DataOut(ddshifter4bit_136_dataout));  // open: DisplayOut
  DDShifter4Bit ddshifter4bit_137 (
    .DataIn(ddshifter4bit_138_dataout), .NextBit(in_1[10]), .ShiftedBit(ddshifter4bit_137_shiftedbit),
    .DataOut(ddshifter4bit_137_dataout));  // open: DisplayOut
  DDShifter4Bit ddshifter4bit_138 (
    .DataIn(ddshifter4bit_139_dataout), .NextBit(in_1[11]), .ShiftedBit(ddshifter4bit_138_shiftedbit),
    .DataOut(ddshifter4bit_138_dataout));  // open: DisplayOut
  DDShifter4Bit ddshifter4bit_139 (
    .DataIn(ddshifter4bit_140_dataout), .NextBit(in_1[12]), .ShiftedBit(ddshifter4bit_139_shiftedbit),
    .DataOut(ddshifter4bit_139_dataout));  // open: DisplayOut
  DDShifter4Bit ddshifter4bit_140 (
    .DataIn(ddshifter4bit_141_dataout), .NextBit(in_1[13]), .ShiftedBit(ddshifter4bit_140_shiftedbit),
    .DataOut(ddshifter4bit_140_dataout));  // open: DisplayOut
  DDShifter4Bit ddshifter4bit_141 (
    .DataIn(ddshifter4bit_142_dataout), .NextBit(in_1[14]), .ShiftedBit(ddshifter4bit_141_shiftedbit),
    .DataOut(ddshifter4bit_141_dataout));  // open: DisplayOut
  DDShifter4Bit ddshifter4bit_142 (
    .DataIn(ddshifter4bit_143_dataout), .NextBit(in_1[15]), .ShiftedBit(ddshifter4bit_142_shiftedbit),
    .DataOut(ddshifter4bit_142_dataout));  // open: DisplayOut
  DDShifter4Bit ddshifter4bit_143 (
    .DataIn(ddshifter4bit_144_dataout), .NextBit(in_1[16]), .ShiftedBit(ddshifter4bit_143_shiftedbit),
    .DataOut(ddshifter4bit_143_dataout));  // open: DisplayOut
  DDShifter4Bit ddshifter4bit_144 (
    .DataIn(ddshifter4bit_145_dataout), .NextBit(in_1[17]), .ShiftedBit(ddshifter4bit_144_shiftedbit),
    .DataOut(ddshifter4bit_144_dataout));  // open: DisplayOut
  DDShifter4Bit ddshifter4bit_145 (
    .DataIn(ddshifter4bit_146_dataout), .NextBit(in_1[18]), .ShiftedBit(ddshifter4bit_145_shiftedbit),
    .DataOut(ddshifter4bit_145_dataout));  // open: DisplayOut
  DDShifter4Bit ddshifter4bit_146 (
    .DataIn(ddshifter4bit_147_dataout), .NextBit(in_1[19]), .ShiftedBit(ddshifter4bit_146_shiftedbit),
    .DataOut(ddshifter4bit_146_dataout));  // open: DisplayOut
  DDShifter4Bit ddshifter4bit_147 (
    .DataIn(ddshifter4bit_148_dataout), .NextBit(in_1[20]), .ShiftedBit(ddshifter4bit_147_shiftedbit),
    .DataOut(ddshifter4bit_147_dataout));  // open: DisplayOut
  DDShifter4Bit ddshifter4bit_148 (
    .DataIn(ddshifter4bit_149_dataout), .NextBit(in_1[21]), .ShiftedBit(ddshifter4bit_148_shiftedbit),
    .DataOut(ddshifter4bit_148_dataout));  // open: DisplayOut
  DDShifter4Bit ddshifter4bit_149 (
    .DataIn(ddshifter4bit_150_dataout), .NextBit(in_1[22]), .ShiftedBit(ddshifter4bit_149_shiftedbit),
    .DataOut(ddshifter4bit_149_dataout));  // open: DisplayOut
  DDShifter4Bit ddshifter4bit_150 (
    .DataIn(ddshifter4bit_151_dataout), .NextBit(in_1[23]), .ShiftedBit(ddshifter4bit_150_shiftedbit),
    .DataOut(ddshifter4bit_150_dataout));  // open: DisplayOut
  DDShifter4Bit ddshifter4bit_151 (
    .DataIn(ddshifter4bit_152_dataout), .NextBit(in_1[24]), .ShiftedBit(ddshifter4bit_151_shiftedbit),
    .DataOut(ddshifter4bit_151_dataout));  // open: DisplayOut
  DDShifter4Bit ddshifter4bit_152 (
    .DataIn(ddshifter4bit_153_dataout), .NextBit(in_1[25]), .ShiftedBit(ddshifter4bit_152_shiftedbit),
    .DataOut(ddshifter4bit_152_dataout));  // open: DisplayOut
  DDShifter4Bit ddshifter4bit_153 (
    .DataIn(ddshifter4bit_154_dataout), .NextBit(in_1[26]), .ShiftedBit(ddshifter4bit_153_shiftedbit),
    .DataOut(ddshifter4bit_153_dataout));  // open: DisplayOut
  DDShifter4Bit ddshifter4bit_154 (
    .DataIn(ddshifter4bit_155_dataout), .NextBit(in_1[27]), .ShiftedBit(ddshifter4bit_154_shiftedbit),
    .DataOut(ddshifter4bit_154_dataout));  // open: DisplayOut
  DDShifter4Bit ddshifter4bit_155 (
    .DataIn(ddshifter1_3bit_10_dataout), .NextBit(in_1[28]), .ShiftedBit(ddshifter4bit_155_shiftedbit),
    .DataOut(ddshifter4bit_155_dataout));  // open: DisplayOut
  DDShifter1_3Bit ddshifter1_3bit_10 (
    .Bit1(in_1[31]), .Bit2(in_1[30]), .Bit3(in_1[29]), .DataOut(ddshifter1_3bit_10_dataout));
endmodule

module DDShifter4Bit (
  input  NextBit,
  input  [3:0] DataIn,
  output [3:0] DisplayOut,
  output [3:0] DataOut,
  output ShiftedBit
);

  Multiplexer multiplexer_1 (.in0(DataIn[3]), .in1(DataIn[2]), .out(DisplayOut[3]), .sel(1'b1));
  Multiplexer multiplexer_2 (.in0(DataIn[2]), .in1(DataIn[1]), .out(DisplayOut[2]), .sel(1'b1));
  DoubleDabbleCmp doubledabblecmp_1 (.DataIn(DisplayOut), .DataOut(DataOut));
  Multiplexer multiplexer_3 (.in0(DataIn[1]), .in1(DataIn[0]), .out(DisplayOut[1]), .sel(1'b1));
  Multiplexer multiplexer_4 (.in0(DataIn[0]), .in1(NextBit), .out(DisplayOut[0]), .sel(1'b1));

  assign ShiftedBit = DataIn[3];
endmodule

module DDShifter1_3Bit (
  input  Bit3,
  input  Bit2,
  input  Bit1,
  output [3:0] DataOut
);

  wire multiplexer_3_out, multiplexer_5_out, multiplexer_6_out;
  wire [2:0] multiplexer_4_out;

  Multiplexer multiplexer_1 (.in0(1'b0), .in1(multiplexer_3_out), .out(multiplexer_4_out[2]), .sel(1'b1));
  DoubleDabbleCmp doubledabblecmp_1 (.DataIn({1'b0, multiplexer_4_out}), .DataOut(DataOut));
  Multiplexer multiplexer_2 (.in0(multiplexer_3_out), .in1(multiplexer_5_out), .out(multiplexer_4_out[1]), .sel(1'b1));
  Multiplexer multiplexer_3 (.in0(1'b0), .in1(multiplexer_6_out), .out(multiplexer_3_out), .sel(1'b1));
  Multiplexer multiplexer_4 (.in0(multiplexer_5_out), .in1(Bit3), .out(multiplexer_4_out[0]), .sel(1'b1));
  Multiplexer multiplexer_5 (.in0(multiplexer_6_out), .in1(Bit2), .out(multiplexer_5_out), .sel(1'b1));
  Multiplexer multiplexer_6 (.in0(1'b0), .in1(Bit1), .out(multiplexer_6_out), .sel(1'b1));
endmodule

module DoubleDabble3digit (
  input  [31:0] DataIn,
  output aH,
  output bH,
  output cH,
  output dH,
  output eH,
  output fH,
  output gH,
  output dotH,
  output aT,
  output bT,
  output cT,
  output dT,
  output eT,
  output fT,
  output gT,
  output dotT,
  output aO,
  output bO,
  output cO,
  output dO,
  output eO,
  output fO,
  output gO,
  output dotO
);

  wire comparator_1_gt, ddshifter4bit_2_shiftedbit, ddshifter4bit_3_shiftedbit, ddshifter4bit_4_shiftedbit,
       ddshifter4bit_5_shiftedbit, ddshifter4bit_6_shiftedbit, ddshifter4bit_7_shiftedbit,
       ddshifter4bit_8_shiftedbit, ddshifter4bit_9_shiftedbit, ddshifter4bit_10_shiftedbit,
       ddshifter4bit_11_shiftedbit, ddshifter4bit_12_shiftedbit;
  wire [3:0] ddshifter1_3bit_1_dataout, ddshifter1_3bit_2_dataout, ddshifter1_3bit_3_dataout,
       ddshifter4bit_1_displayout, ddshifter4bit_2_displayout, ddshifter4bit_3_dataout,
       ddshifter4bit_4_dataout, ddshifter4bit_5_dataout, ddshifter4bit_6_displayout, ddshifter4bit_7_dataout,
       ddshifter4bit_8_dataout, ddshifter4bit_9_dataout, ddshifter4bit_10_dataout, ddshifter4bit_11_dataout,
       ddshifter4bit_12_dataout, multiplexer_1_out, multiplexer_2_out, multiplexer_3_out;

  ROM #(.addrWidth(4)) rom_1 (.addr(multiplexer_1_out), .data({aH, bH, cH, dH, eH, fH, gH, dotH}));
  Multiplexer #(.width(4)) multiplexer_1 (
    .in0(ddshifter4bit_1_displayout), .in1(4'b1010), .out(multiplexer_1_out), .sel(comparator_1_gt));
  DDShifter4Bit ddshifter4bit_1 (
    .DataIn(ddshifter1_3bit_1_dataout), .NextBit(ddshifter4bit_2_shiftedbit),
    .DisplayOut(ddshifter4bit_1_displayout));  // open: ShiftedBit, DataOut
  DDShifter1_3Bit ddshifter1_3bit_1 (
    .Bit1(ddshifter4bit_5_shiftedbit), .Bit2(ddshifter4bit_4_shiftedbit), .Bit3(ddshifter4bit_3_shiftedbit),
    .DataOut(ddshifter1_3bit_1_dataout));
  Multiplexer #(.width(4)) multiplexer_2 (
    .in0(ddshifter4bit_2_displayout), .in1(4'b1110), .out(multiplexer_2_out), .sel(comparator_1_gt));
  DDShifter4Bit ddshifter4bit_2 (
    .DataIn(ddshifter4bit_3_dataout), .NextBit(ddshifter4bit_6_shiftedbit),
    .ShiftedBit(ddshifter4bit_2_shiftedbit), .DisplayOut(ddshifter4bit_2_displayout));  // open: DataOut
  DDShifter4Bit ddshifter4bit_3 (
    .DataIn(ddshifter4bit_4_dataout), .NextBit(ddshifter4bit_7_shiftedbit),
    .ShiftedBit(ddshifter4bit_3_shiftedbit), .DataOut(ddshifter4bit_3_dataout));  // open: DisplayOut
  DDShifter4Bit ddshifter4bit_4 (
    .DataIn(ddshifter4bit_5_dataout), .NextBit(ddshifter4bit_8_shiftedbit),
    .ShiftedBit(ddshifter4bit_4_shiftedbit), .DataOut(ddshifter4bit_4_dataout));  // open: DisplayOut
  DDShifter4Bit ddshifter4bit_5 (
    .DataIn(ddshifter1_3bit_2_dataout), .NextBit(ddshifter4bit_9_shiftedbit),
    .ShiftedBit(ddshifter4bit_5_shiftedbit), .DataOut(ddshifter4bit_5_dataout));  // open: DisplayOut
  DDShifter1_3Bit ddshifter1_3bit_2 (
    .Bit1(ddshifter4bit_12_shiftedbit), .Bit2(ddshifter4bit_11_shiftedbit),
    .Bit3(ddshifter4bit_10_shiftedbit), .DataOut(ddshifter1_3bit_2_dataout));
  Multiplexer #(.width(4)) multiplexer_3 (
    .in0(ddshifter4bit_6_displayout), .in1(4'b1111), .out(multiplexer_3_out), .sel(comparator_1_gt));
  DDShifter4Bit ddshifter4bit_6 (
    .DataIn(ddshifter4bit_7_dataout), .NextBit(DataIn[0]), .ShiftedBit(ddshifter4bit_6_shiftedbit),
    .DisplayOut(ddshifter4bit_6_displayout));  // open: DataOut
  DDShifter4Bit ddshifter4bit_7 (
    .DataIn(ddshifter4bit_8_dataout), .NextBit(DataIn[1]), .ShiftedBit(ddshifter4bit_7_shiftedbit),
    .DataOut(ddshifter4bit_7_dataout));  // open: DisplayOut
  DDShifter4Bit ddshifter4bit_8 (
    .DataIn(ddshifter4bit_9_dataout), .NextBit(DataIn[2]), .ShiftedBit(ddshifter4bit_8_shiftedbit),
    .DataOut(ddshifter4bit_8_dataout));  // open: DisplayOut
  DDShifter4Bit ddshifter4bit_9 (
    .DataIn(ddshifter4bit_10_dataout), .NextBit(DataIn[3]), .ShiftedBit(ddshifter4bit_9_shiftedbit),
    .DataOut(ddshifter4bit_9_dataout));  // open: DisplayOut
  DDShifter4Bit ddshifter4bit_10 (
    .DataIn(ddshifter4bit_11_dataout), .NextBit(DataIn[4]), .ShiftedBit(ddshifter4bit_10_shiftedbit),
    .DataOut(ddshifter4bit_10_dataout));  // open: DisplayOut
  DDShifter4Bit ddshifter4bit_11 (
    .DataIn(ddshifter4bit_12_dataout), .NextBit(DataIn[5]), .ShiftedBit(ddshifter4bit_11_shiftedbit),
    .DataOut(ddshifter4bit_11_dataout));  // open: DisplayOut
  DDShifter4Bit ddshifter4bit_12 (
    .DataIn(ddshifter1_3bit_3_dataout), .NextBit(DataIn[6]), .ShiftedBit(ddshifter4bit_12_shiftedbit),
    .DataOut(ddshifter4bit_12_dataout));  // open: DisplayOut
  DDShifter1_3Bit ddshifter1_3bit_3 (
    .Bit1(DataIn[9]), .Bit2(DataIn[8]), .Bit3(DataIn[7]), .DataOut(ddshifter1_3bit_3_dataout));
  ROM #(.addrWidth(4)) rom_2 (.addr(multiplexer_2_out), .data({aT, bT, cT, dT, eT, fT, gT, dotT}));
  Comparator #(.width(32)) comparator_1 (.a(DataIn), .b(32'h3e7), .gt(comparator_1_gt));  // open: eq, lt
  ROM #(.addrWidth(4)) rom_3 (.addr(multiplexer_3_out), .data({aO, bO, cO, dO, eO, fO, gO, dotO}));

  // Notes on the sheet:
  //   contents of rom_1 (hex, n*v repeats v):
  //   fc 60 da f2 66 b6 be e0 fe f6 9e 8e 1c ce a b
  //   contents of rom_2 (hex, n*v repeats v):
  //   fc 60 da f2 66 b6 be e0 fe f6 9e 8e 1c ce a b
  //   contents of rom_3 (hex, n*v repeats v):
  //   fc 60 da f2 66 b6 be e0 fe f6 9e 8e 1c ce a b
endmodule

module CPU_RAM_Interface (
  input  [31:0] IU_Output,
  input  [31:0] FPU_Output,
  input  [31:0] RAM_Output,
  input  [31:0] int_X_Bus,
  input  [5:0] OpCode,
  input  Load,
  input  Store,
  input  [31:0] int_Y_Bus,
  input  [31:0] float_Y_Bus,
  input  float,
  input  Clk,
  output [31:0] RegFile_Input,
  output [9:0] RAM_Adress,
  output Output_Enable,
  output Write_Enable,
  output [31:0] RAM_Input,
  output RAM_Clk
);

  wire FLW_out;
  wire [21:0] multiplexer_1_out;
  wire [31:0] multiplexer_2_out;

  and FLW (FLW_out, OpCode[0], OpCode[1], OpCode[2], OpCode[3], OpCode[4], OpCode[5]);
  Multiplexer #(.width(32)) multiplexer_1 (
    .in0(IU_Output), .in1(int_X_Bus), .out({multiplexer_1_out, RAM_Adress}), .sel(FLW_out));
  Multiplexer #(.width(32)) multiplexer_2 (.in0(IU_Output), .in1(FPU_Output), .out(multiplexer_2_out), .sel(float));
  Multiplexer #(.width(32)) multiplexer_3 (.in0(multiplexer_2_out), .in1(RAM_Output), .out(RegFile_Input), .sel(Load));
  Multiplexer #(.width(32)) multiplexer_4 (.in0(int_Y_Bus), .in1(float_Y_Bus), .out(RAM_Input), .sel(float));

  assign Output_Enable = Load;
  assign RAM_Clk = Clk;
  assign Write_Enable = Store;

  // Notes on the sheet:
  //   RAMtoCPU
endmodule

module RAM_10Adress_Output (
  input  [9:0] Adress,
  input  [31:0] RAM_Input,
  input  Write_enable,
  input  Clk,
  output [31:0] Adress0,
  output [31:0] Adress1,
  output [31:0] Adress2,
  output [31:0] Adress3,
  output [31:0] Adress4,
  output [31:0] Adress5,
  output [31:0] Adress6,
  output [31:0] Adress7,
  output [31:0] Adress8,
  output [31:0] Adress9
);

  wire and_1_out, and_2_out, and_3_out, and_4_out, and_5_out, and_6_out, and_7_out, and_8_out, and_9_out,
       and_10_out, decoder_1_out0, decoder_1_out1, decoder_1_out2, decoder_1_out3, decoder_1_out4,
       decoder_1_out5, decoder_1_out6, decoder_1_out7, decoder_1_out8, decoder_1_out9;
  wire [31:0] demultiplexer_1_out0, demultiplexer_1_out1, demultiplexer_1_out2, demultiplexer_1_out3,
       demultiplexer_1_out4, demultiplexer_1_out5, demultiplexer_1_out6, demultiplexer_1_out7,
       demultiplexer_1_out8, demultiplexer_1_out9;

  Decoder #(.select(4)) decoder_1 (
    .out0(decoder_1_out0), .out1(decoder_1_out1), .out2(decoder_1_out2), .out3(decoder_1_out3),
    .out4(decoder_1_out4), .out5(decoder_1_out5), .out6(decoder_1_out6), .out7(decoder_1_out7),
    .out8(decoder_1_out8), .out9(decoder_1_out9), .sel(Adress[3:0]));  // open: out10, out11, out12, out13, out14, out15, en
  and and_1 (and_1_out, Write_enable, decoder_1_out0);
  and and_2 (and_2_out, Write_enable, decoder_1_out1);
  Register #(.width(32)) register_1 (.D(demultiplexer_1_out0), .en(and_1_out), .Q(Adress0), .clk(Clk));  // open: clr
  and and_3 (and_3_out, Write_enable, decoder_1_out2);
  and and_4 (and_4_out, Write_enable, decoder_1_out3);
  Register #(.width(32)) register_2 (.D(demultiplexer_1_out1), .en(and_2_out), .Q(Adress1), .clk(Clk));  // open: clr
  Register #(.width(32)) register_3 (.D(demultiplexer_1_out2), .en(and_3_out), .Q(Adress2), .clk(Clk));  // open: clr
  and and_5 (and_5_out, Write_enable, decoder_1_out4);
  Register #(.width(32)) register_4 (.D(demultiplexer_1_out3), .en(and_4_out), .Q(Adress3), .clk(Clk));  // open: clr
  Register #(.width(32)) register_5 (.D(demultiplexer_1_out4), .en(and_5_out), .Q(Adress4), .clk(Clk));  // open: clr
  Demultiplexer #(.select(4), .width(32)) demultiplexer_1 (
    .out0(demultiplexer_1_out0), .out1(demultiplexer_1_out1), .out2(demultiplexer_1_out2),
    .out3(demultiplexer_1_out3), .out4(demultiplexer_1_out4), .out5(demultiplexer_1_out5),
    .out6(demultiplexer_1_out6), .out7(demultiplexer_1_out7), .out8(demultiplexer_1_out8),
    .out9(demultiplexer_1_out9), .in(RAM_Input), .sel(Adress[3:0]));  // open: out10, out11, out12, out13, out14, out15
  and and_6 (and_6_out, Write_enable, decoder_1_out5);
  and and_7 (and_7_out, Write_enable, decoder_1_out6);
  Register #(.width(32)) register_6 (.D(demultiplexer_1_out5), .en(and_6_out), .Q(Adress5), .clk(Clk));  // open: clr
  and and_8 (and_8_out, Write_enable, decoder_1_out7);
  and and_9 (and_9_out, Write_enable, decoder_1_out8);
  Register #(.width(32)) register_7 (.D(demultiplexer_1_out6), .en(and_7_out), .Q(Adress6), .clk(Clk));  // open: clr
  Register #(.width(32)) register_8 (.D(demultiplexer_1_out7), .en(and_8_out), .Q(Adress7), .clk(Clk));  // open: clr
  and and_10 (and_10_out, Write_enable, decoder_1_out9);
  Register #(.width(32)) register_9 (.D(demultiplexer_1_out8), .en(and_9_out), .Q(Adress8), .clk(Clk));  // open: clr
  Register #(.width(32)) register_10 (.D(demultiplexer_1_out9), .en(and_10_out), .Q(Adress9), .clk(Clk));  // open: clr
endmodule

module OR32to1 (
  input  [31:0] in_1,
  output out_2
);

  wire and_1_out, and_2_out, and_3_out, and_4_out, and_5_out, and_6_out, and_7_out, and_8_out, and_9_out,
       and_10_out, and_11_out, and_12_out, and_13_out, and_14_out, and_15_out, and_16_out, and_17_out,
       and_18_out, and_19_out, and_20_out, and_21_out, and_22_out, and_23_out, and_24_out, and_25_out,
       and_26_out, and_27_out, and_28_out, and_29_out, and_30_out, and_31_out, and_32_out, or_1_out;

  and and_1 (and_1_out, in_1[31], 1'b1);
  and and_2 (and_2_out, in_1[30], 1'b1);
  and and_3 (and_3_out, in_1[29], 1'b1);
  and and_4 (and_4_out, in_1[28], 1'b1);
  and and_5 (and_5_out, in_1[27], 1'b1);
  and and_6 (and_6_out, in_1[26], 1'b1);
  and and_7 (and_7_out, in_1[25], 1'b1);
  and and_8 (and_8_out, in_1[24], 1'b1);
  and and_9 (and_9_out, in_1[23], 1'b1);
  and and_10 (and_10_out, in_1[22], 1'b1);
  and and_11 (and_11_out, in_1[21], 1'b1);
  and and_12 (and_12_out, in_1[20], 1'b1);
  and and_13 (and_13_out, in_1[19], 1'b1);
  and and_14 (and_14_out, in_1[18], 1'b1);
  and and_15 (and_15_out, in_1[17], 1'b1);
  and and_16 (and_16_out, in_1[16], 1'b1);
  or or_1 (or_1_out, and_1_out, and_2_out, and_3_out, and_4_out, and_5_out, and_6_out, and_7_out, and_8_out, and_9_out, and_10_out, and_11_out, and_12_out, and_13_out, and_14_out, and_15_out, and_16_out, and_17_out, and_18_out, and_19_out, and_20_out, and_21_out, and_22_out, and_23_out, and_24_out, and_25_out, and_26_out, and_27_out, and_30_out, and_28_out, and_29_out, and_31_out, and_32_out);
  not not_1 (out_2, or_1_out);
  and and_17 (and_17_out, in_1[15], 1'b1);
  and and_18 (and_18_out, in_1[14], 1'b1);
  and and_19 (and_19_out, in_1[13], 1'b1);
  and and_20 (and_20_out, in_1[12], 1'b1);
  and and_21 (and_21_out, in_1[11], 1'b1);
  and and_22 (and_22_out, in_1[10], 1'b1);
  and and_23 (and_23_out, in_1[9], 1'b1);
  and and_24 (and_24_out, in_1[8], 1'b1);
  and and_25 (and_25_out, in_1[7], 1'b1);
  and and_26 (and_26_out, in_1[6], 1'b1);
  and and_27 (and_27_out, in_1[5], 1'b1);
  and and_28 (and_28_out, in_1[3], 1'b1);
  and and_29 (and_29_out, in_1[2], 1'b1);
  and and_30 (and_30_out, in_1[4], 1'b1);
  and and_31 (and_31_out, in_1[1], 1'b1);
  and and_32 (and_32_out, in_1[0], 1'b1);
endmodule

module RegFilesDataInSel (
  input  [5:0] in_1,
  output MTF,
  output MFF
);

  wire not_1_out, not_2_out;

  not not_1 (not_1_out, in_1[0]);
  not not_2 (not_2_out, in_1[2]);
  and and_1 (MTF, not_1_out, in_1[1], not_2_out, in_1[3], in_1[4], in_1[5]);
  and and_2 (MFF, in_1[0], in_1[1], not_2_out, in_1[3], in_1[4], in_1[5]);
endmodule

module LoadStore (
  input  [5:0] OpCode,
  output store,
  output load
);

  wire FLW_out, FSW_out, LW_out, not_1_out, not_2_out, not_3_out, not_4_out, SW_out;

  not not_1 (not_1_out, OpCode[0]);
  not not_2 (not_2_out, OpCode[5]);
  not not_3 (not_3_out, OpCode[0]);
  not not_4 (not_4_out, OpCode[5]);
  and SW (SW_out, not_1_out, OpCode[1], OpCode[2], OpCode[3], OpCode[4], not_2_out);
  or or_1 (store, SW_out, FSW_out);
  and FSW (FSW_out, not_3_out, OpCode[1], OpCode[2], OpCode[3], OpCode[4], OpCode[5]);
  and LW (LW_out, OpCode[0], OpCode[1], OpCode[2], OpCode[3], OpCode[4], not_4_out);
  or or_2 (load, LW_out, FLW_out);
  and FLW (FLW_out, OpCode[0], OpCode[1], OpCode[2], OpCode[3], OpCode[4], OpCode[5]);
endmodule

module Branches (
  input  [5:0] OpCode,
  output Branch
);

  wire beq_out, bge_out, bgt_out, ble_out, blt_out, bne_out, not_1_out, not_2_out, not_3_out, not_4_out,
       not_5_out, not_6_out, not_7_out, not_8_out, not_9_out, not_10_out, not_11_out, not_12_out;

  not not_1 (not_1_out, OpCode[5]);
  not not_2 (not_2_out, OpCode[3]);
  not not_3 (not_3_out, OpCode[2]);
  not not_4 (not_4_out, OpCode[1]);
  not not_5 (not_5_out, not_3_out);
  not not_6 (not_6_out, not_3_out);
  not not_7 (not_7_out, OpCode[0]);
  not not_8 (not_8_out, not_7_out);
  not not_9 (not_9_out, not_4_out);
  not not_10 (not_10_out, not_7_out);
  not not_11 (not_11_out, not_4_out);
  not not_12 (not_12_out, not_7_out);
  and beq (beq_out, not_7_out, not_4_out, not_3_out, not_2_out, OpCode[4], not_1_out);
  and bne (bne_out, not_8_out, not_4_out, not_3_out, not_2_out, OpCode[4], not_1_out);
  and blt (blt_out, not_7_out, not_9_out, not_3_out, not_2_out, OpCode[4], not_1_out);
  and bgt (bgt_out, not_10_out, not_11_out, not_3_out, not_2_out, OpCode[4], not_1_out);
  and ble (ble_out, not_7_out, not_4_out, not_5_out, not_2_out, OpCode[4], not_1_out);
  and bge (bge_out, not_12_out, not_4_out, not_6_out, not_2_out, OpCode[4], not_1_out);
  ExactlyOne xor_1 (
    .out(Branch), .in0(beq_out), .in1(bne_out), .in2(blt_out), .in3(bgt_out), .in4(ble_out), .in5(bge_out));
endmodule

module MulDiv (
  input  [5:0] OpCode,
  output Mul_or_Div
);

  wire div_out, mul_out, not_1_out, not_2_out, not_3_out, not_4_out;

  not not_1 (not_1_out, OpCode[0]);
  not not_2 (not_2_out, OpCode[2]);
  not not_3 (not_3_out, OpCode[4]);
  not not_4 (not_4_out, OpCode[5]);
  and mul (mul_out, not_1_out, OpCode[1], not_2_out, OpCode[3], not_3_out, not_4_out);
  or or_1 (Mul_or_Div, mul_out, div_out);
  and div (div_out, OpCode[0], OpCode[1], not_2_out, OpCode[3], not_3_out, not_4_out);
endmodule

module WriteEnable (
  input  [5:0] Funct,
  input  [5:0] OpCode,
  input  MulDiv,
  input  Branch,
  input  Jump,
  input  Store,
  input  Float,
  input  iType,
  output IntWrite,
  output FloatWrite
);

  wire and_1_out, and_2_out, demultiplexer_1_out0, demultiplexer_1_out1, multiplexer_3_out, not_1_out,
       not_2_out, xor_1_out;
  wire [5:0] multiplexer_1_out, multiplexer_2_out;

  Multiplexer #(.width(6)) multiplexer_1 (.in0(Funct), .in1(OpCode), .out(multiplexer_1_out), .sel(iType));
  Multiplexer #(.width(6)) multiplexer_2 (.in0(Funct), .in1(OpCode), .out(multiplexer_2_out), .sel(iType));
  ExactlyOne xor_1 (.out(xor_1_out), .in0(MulDiv), .in1(Branch), .in2(Jump), .in3(Store));
  Multiplexer multiplexer_3 (.in0(1'b1), .in1(1'b0), .out(multiplexer_3_out), .sel(xor_1_out));
  not not_1 (not_1_out, multiplexer_1_out[2]);
  and and_1 (and_1_out, multiplexer_1_out[0], multiplexer_1_out[1], not_1_out, multiplexer_1_out[3], multiplexer_1_out[4], multiplexer_1_out[5]);
  not not_2 (not_2_out, multiplexer_2_out[2]);
  and and_2 (and_2_out, multiplexer_2_out[0], multiplexer_2_out[1], not_2_out, multiplexer_2_out[3], multiplexer_2_out[4], multiplexer_2_out[5]);
  Multiplexer multiplexer_4 (.in0(demultiplexer_1_out0), .in1(1'b1), .out(IntWrite), .sel(and_1_out));
  Demultiplexer demultiplexer_1 (
    .out0(demultiplexer_1_out0), .out1(demultiplexer_1_out1), .in(multiplexer_3_out), .sel(Float));
  Multiplexer multiplexer_5 (.in0(demultiplexer_1_out1), .in1(1'b0), .out(FloatWrite), .sel(and_2_out));
endmodule

module InstructionTypes (
  input  [5:0] OpCode,
  output R,
  output J,
  output I,
  output MSB
);

  wire not_1_out;

  not not_1 (not_1_out, OpCode[1]);
  or or_1 (I, OpCode[0], OpCode[2], OpCode[3], OpCode[4], OpCode[5]);
  nor nor_1 (R, OpCode[0], OpCode[1], OpCode[2], OpCode[3], OpCode[4], OpCode[5]);
  nor nor_2 (J, OpCode[0], not_1_out, OpCode[2], OpCode[3], OpCode[4], OpCode[5]);

  assign MSB = OpCode[5];

  // Notes on the sheet:
  //   R
  //   J
  //   I
endmodule
